// Digital circuit ALU.dig as structural Verilog
module ALU (
  input  [7:0] RHS,
  input  [7:0] LHS,
  input  [3:0] Control,
  input  Assert_Main,
  input  Clock,
  output [7:0] MAIN,
  output [4:0] FLAGS
);

  wire _7402_1_pin2, _7408_1_pin8, _7408_1_pin9, _7408_1_pin10, _7408_1_pin12, _7408_1_pin13, _7425_1_pin6,
       _7425_1_pin8, _74253_14_pin7, _74283_1_pin9, _74574_2_pin16, _74574_2_pin18, _74574_2_pin19, Clock_t,
       LHS_Sign, Logical_Carry_Out, RHS_Sign;
  wire [1:0] Carry_select, LHS_Control;
  wire [3:0] _74283_1_pin4, _74574_1_pin12, _74574_1_pin16, RHS_Control;
  wire [6:0] LHSData, RHSData;
  wire [6:4] _7425_1_pin9;
  wire [7:0] _74574_3_pin12;

  _74253 _74253_1 (
    .pin1(1'b0), .pin2(RHS[0]), .pin3(RHS_Control[3]), .pin4(RHS_Control[2]), .pin5(RHS_Control[1]),
    .pin6(RHS_Control[0]), .pin7(RHSData[0]), .pin8(1'b0), .pin9(1'b0), .pin10(RHSData[1]),
    .pin11(RHS_Control[0]), .pin12(RHS_Control[1]), .pin13(RHS_Control[2]), .pin14(RHS_Control[3]),
    .pin15(RHS[1]), .pin16(1'b0));
  _74253 _74253_2 (
    .pin1(1'b0), .pin2(LHS_Control[0]), .pin3(1'b0), .pin4(FLAGS[4]), .pin5(LHS[1]), .pin6(LHS[0]),
    .pin7(LHSData[0]), .pin8(1'b0), .pin9(LHSData[1]), .pin10(LHS[1]), .pin11(LHS[2]), .pin12(LHS[0]),
    .pin13(1'b0), .pin14(LHS_Control[1]), .pin15(1'b0), .pin16(1'b1));
  _74253 _74253_3 (
    .pin1(1'b0), .pin2(RHS[1]), .pin3(RHS_Control[3]), .pin4(RHS_Control[2]), .pin5(RHS_Control[1]),
    .pin6(RHS_Control[0]), .pin7(RHSData[1]), .pin8(1'b0), .pin9(1'b0), .pin10(RHSData[2]),
    .pin11(RHS_Control[0]), .pin12(RHS_Control[1]), .pin13(RHS_Control[2]), .pin14(RHS_Control[3]),
    .pin15(RHS[2]), .pin16(1'b0));
  _74253 _74253_4 (
    .pin1(1'b0), .pin2(LHS_Control[0]), .pin3(1'b0), .pin4(LHS[1]), .pin5(LHS[3]), .pin6(LHS[2]),
    .pin7(LHSData[2]), .pin8(1'b0), .pin9(LHSData[3]), .pin10(LHS[3]), .pin11(LHS[4]), .pin12(LHS[2]),
    .pin13(1'b0), .pin14(LHS_Control[1]), .pin15(1'b0), .pin16(1'b1));
  _74253 _74253_5 (
    .pin1(1'b0), .pin2(RHS[2]), .pin3(RHS_Control[3]), .pin4(RHS_Control[2]), .pin5(RHS_Control[1]),
    .pin6(RHS_Control[0]), .pin7(RHSData[2]), .pin8(1'b0), .pin9(1'b0), .pin10(RHSData[3]),
    .pin11(RHS_Control[0]), .pin12(RHS_Control[1]), .pin13(RHS_Control[2]), .pin14(RHS_Control[3]),
    .pin15(RHS[3]), .pin16(1'b0));
  _74253 _74253_6 (
    .pin1(1'b0), .pin2(LHS_Control[0]), .pin3(1'b0), .pin4(LHS[3]), .pin5(LHS[5]), .pin6(LHS[4]),
    .pin7(LHSData[4]), .pin8(1'b0), .pin9(LHSData[5]), .pin10(LHS[5]), .pin11(LHS[6]), .pin12(LHS[4]),
    .pin13(1'b0), .pin14(LHS_Control[1]), .pin15(1'b0), .pin16(1'b1));
  _74253 _74253_7 (
    .pin1(1'b0), .pin2(RHS[3]), .pin3(RHS_Control[3]), .pin4(RHS_Control[2]), .pin5(RHS_Control[1]),
    .pin6(RHS_Control[0]), .pin7(RHSData[3]), .pin8(1'b0), .pin9(1'b0), .pin10(RHSData[4]),
    .pin11(RHS_Control[0]), .pin12(RHS_Control[1]), .pin13(RHS_Control[2]), .pin14(RHS_Control[3]),
    .pin15(RHS[4]), .pin16(1'b0));
  _74253 _74253_8 (
    .pin1(1'b0), .pin2(RHS[4]), .pin3(RHS_Control[3]), .pin4(RHS_Control[2]), .pin5(RHS_Control[1]),
    .pin6(RHS_Control[0]), .pin7(RHSData[4]), .pin8(1'b0), .pin9(1'b0), .pin10(RHSData[5]),
    .pin11(RHS_Control[0]), .pin12(RHS_Control[1]), .pin13(RHS_Control[2]), .pin14(RHS_Control[3]),
    .pin15(RHS[5]), .pin16(1'b0));
  _74253 _74253_9 (
    .pin1(1'b0), .pin2(LHS_Control[0]), .pin3(1'b0), .pin4(LHS[5]), .pin5(LHS[7]), .pin6(LHS[6]),
    .pin7(LHSData[6]), .pin8(1'b0), .pin9(LHS_Sign), .pin10(LHS[7]), .pin11(FLAGS[4]), .pin12(LHS[6]),
    .pin13(1'b0), .pin14(LHS_Control[1]), .pin15(1'b0), .pin16(1'b1));
  _74253 _74253_10 (
    .pin1(1'b0), .pin2(RHS[5]), .pin3(RHS_Control[3]), .pin4(RHS_Control[2]), .pin5(RHS_Control[1]),
    .pin6(RHS_Control[0]), .pin7(RHSData[5]), .pin8(1'b0), .pin9(1'b0), .pin10(RHSData[6]),
    .pin11(RHS_Control[0]), .pin12(RHS_Control[1]), .pin13(RHS_Control[2]), .pin14(RHS_Control[3]),
    .pin15(RHS[6]), .pin16(1'b0));
  _74253 _74253_11 (
    .pin1(1'b0), .pin2(LHS_Control[0]), .pin3(1'b0), .pin4(LHS[7]), .pin5(LHS[0]), .pin6(FLAGS[4]),
    .pin7(Logical_Carry_Out), .pin8(1'b0), .pin10(1'b0), .pin11(1'b0), .pin12(1'b0), .pin13(1'b0),
    .pin14(LHS_Control[1]), .pin15(1'b1), .pin16(1'b1));  // open: pin9
  _74253 _74253_12 (
    .pin1(1'b0), .pin2(RHS[6]), .pin3(RHS_Control[3]), .pin4(RHS_Control[2]), .pin5(RHS_Control[1]),
    .pin6(RHS_Control[0]), .pin7(RHSData[6]), .pin8(1'b0), .pin9(1'b0), .pin10(RHS_Sign),
    .pin11(RHS_Control[0]), .pin12(RHS_Control[1]), .pin13(RHS_Control[2]), .pin14(RHS_Control[3]),
    .pin15(RHS[7]), .pin16(1'b0));
  _74253 _74253_13 (
    .pin1(1'b0), .pin2(RHS[7]), .pin3(RHS_Control[3]), .pin4(RHS_Control[2]), .pin5(RHS_Control[1]),
    .pin6(RHS_Control[0]), .pin7(RHS_Sign), .pin8(1'b0), .pin10(1'b0), .pin11(1'b0), .pin12(1'b0),
    .pin13(1'b0), .pin14(LHS[7]), .pin15(1'b0), .pin16(1'b1));  // open: pin9
  _74574 _74574_1 (
    .pin1(1'b0), .pin2(LHSData[0]), .pin3(LHSData[1]), .pin4(LHSData[2]), .pin5(LHSData[3]),
    .pin6(LHSData[4]), .pin7(LHSData[5]), .pin8(LHSData[6]), .pin9(LHS_Sign), .pin10(1'b0), .pin11(Clock_t),
    .pin12(_74574_1_pin12[3]), .pin13(_74574_1_pin12[2]), .pin14(_74574_1_pin12[1]),
    .pin15(_74574_1_pin12[0]), .pin16(_74574_1_pin16[3]), .pin17(_74574_1_pin16[2]),
    .pin18(_74574_1_pin16[1]), .pin19(_74574_1_pin16[0]), .pin20(1'b1));
  _74574 _74574_2 (
    .pin1(1'b0), .pin2(Carry_select[0]), .pin3(Carry_select[1]), .pin4(Logical_Carry_Out), .pin5(FLAGS[3]),
    .pin6(1'b0), .pin7(1'b0), .pin8(1'b0), .pin9(1'b0), .pin10(1'b0), .pin11(Clock_t),
    .pin16(_74574_2_pin16), .pin17(FLAGS[4]), .pin18(_74574_2_pin18), .pin19(_74574_2_pin19), .pin20(1'b1));  // open: pin12, pin13, pin14, pin15
  _74574 _74574_3 (
    .pin1(1'b0), .pin2(RHSData[0]), .pin3(RHSData[1]), .pin4(RHSData[2]), .pin5(RHSData[3]),
    .pin6(RHSData[4]), .pin7(RHSData[5]), .pin8(RHSData[6]), .pin9(RHS_Sign), .pin10(1'b0), .pin11(Clock_t),
    .pin12(_74574_3_pin12[7]), .pin13(_74574_3_pin12[6]), .pin14(_74574_3_pin12[5]),
    .pin15(_74574_3_pin12[4]), .pin16(_74574_3_pin12[3]), .pin17(_74574_3_pin12[2]),
    .pin18(_74574_3_pin12[1]), .pin19(_74574_3_pin12[0]), .pin20(1'b1));
  _74253 _74253_14 (
    .pin1(1'b0), .pin2(_74574_2_pin18), .pin3(1'b0), .pin4(1'b1), .pin5(_74574_2_pin16), .pin6(1'b0),
    .pin7(_74253_14_pin7), .pin8(1'b0), .pin10(1'b0), .pin11(1'b0), .pin12(1'b0), .pin13(1'b0),
    .pin14(_74574_2_pin19), .pin15(1'b1), .pin16(1'b1));  // open: pin9
  _74283 _74283_1 (
    .pin1(_74283_1_pin4[1]), .pin2(_74574_3_pin12[1]), .pin3(_74574_1_pin16[1]), .pin4(_74283_1_pin4[0]),
    .pin5(_74574_1_pin16[0]), .pin6(_74574_3_pin12[0]), .pin7(_74253_14_pin7), .pin8(1'b0),
    .pin9(_74283_1_pin9), .pin10(_74283_1_pin4[3]), .pin11(_74574_3_pin12[3]), .pin12(_74574_1_pin16[3]),
    .pin13(_74283_1_pin4[2]), .pin14(_74574_1_pin16[2]), .pin15(_74574_3_pin12[2]), .pin16(1'b1));
  _7425 _7425_1 (
    .pin1(_74283_1_pin4[0]), .pin2(_74283_1_pin4[1]), .pin4(_74283_1_pin4[2]), .pin5(_74283_1_pin4[3]),
    .pin6(_7425_1_pin6), .pin7(1'b0), .pin8(_7425_1_pin8), .pin9(_7425_1_pin9[4]), .pin10(_7425_1_pin9[5]),
    .pin12(_7425_1_pin9[6]), .pin13(FLAGS[1]), .pin14(1'b1));  // open: pin3, pin11
  _74283 _74283_2 (
    .pin1(_7425_1_pin9[5]), .pin2(_74574_3_pin12[5]), .pin3(_74574_1_pin12[1]), .pin4(_7425_1_pin9[4]),
    .pin5(_74574_1_pin12[0]), .pin6(_74574_3_pin12[4]), .pin7(_74283_1_pin9), .pin8(1'b0), .pin9(FLAGS[3]),
    .pin10(FLAGS[1]), .pin11(_74574_3_pin12[7]), .pin12(_74574_1_pin12[3]), .pin13(_7425_1_pin9[6]),
    .pin14(_74574_1_pin12[2]), .pin15(_74574_3_pin12[6]), .pin16(1'b1));
  // Probe on {Carry_select, LHS_Control, RHS_Control}
  LookUpTable #(.Bits(8)) ALU_Control (
    .in0(Control[0]), .in1(Control[1]), .in2(Control[2]), .in3(Control[3]),
    .out({Carry_select, LHS_Control, RHS_Control}));
  _7408 _7408_1 (
    .pin1(_7425_1_pin6), .pin2(_7425_1_pin8), .pin3(FLAGS[2]), .pin4(1'b0), .pin5(1'b0), .pin7(1'b0),
    .pin8(_7408_1_pin8), .pin9(_7408_1_pin9), .pin10(_7408_1_pin10), .pin11(FLAGS[0]), .pin12(_7408_1_pin12),
    .pin13(_7408_1_pin13), .pin14(1'b1));  // open: pin6
  _7402 _7402_1 (
    .pin1(Clock_t), .pin2(_7402_1_pin2), .pin3(_7402_1_pin2), .pin4(_7408_1_pin10), .pin5(Control[3]),
    .pin6(Control[1]), .pin7(1'b0), .pin8(Control[0]), .pin9(Control[2]), .pin10(_7408_1_pin9),
    .pin11(Clock), .pin12(_7408_1_pin8), .pin13(_7402_1_pin2), .pin14(1'b1));
  _74541 _74541_1 (
    .pin1(Assert_Main), .pin2(_74283_1_pin4[0]), .pin3(_74283_1_pin4[1]), .pin4(_74283_1_pin4[2]),
    .pin5(_74283_1_pin4[3]), .pin6(_7425_1_pin9[4]), .pin7(_7425_1_pin9[5]), .pin8(_7425_1_pin9[6]),
    .pin9(FLAGS[1]), .pin10(1'b0), .pin11(MAIN[7]), .pin12(MAIN[6]), .pin13(MAIN[5]), .pin14(MAIN[4]),
    .pin15(MAIN[3]), .pin16(MAIN[2]), .pin17(MAIN[1]), .pin18(MAIN[0]), .pin19(1'b0), .pin20(1'b1));
  _7486 _7486_1 (
    .pin1(FLAGS[1]), .pin2(LHS_Sign), .pin3(_7408_1_pin12), .pin4(FLAGS[1]), .pin5(RHS_Sign),
    .pin6(_7408_1_pin13), .pin7(1'b0), .pin9(1'b0), .pin10(1'b0), .pin12(1'b0), .pin13(1'b0), .pin14(1'b1));  // open: pin8, pin11

  // Other names for the same wires on the sheet: Sign = FLAGS[1]; MainBus[7:0] = MAIN; RHSData[7] = RHS_Sign;
  //   LHSData[7] = LHS_Sign; Arithmetic_Carry_Out = FLAGS[3]; Enable = Assert_Main; LHSBus[7:0] = LHS;
  //   Logical_Carry_In = FLAGS[4]; Overflow = FLAGS[0]; RHSBus[7:0] = RHS; Zero = FLAGS[2]

  // Notes on the sheet:
  //   Control: 0-3: ALUOP0-3
  //   FLAGS: 0: Overflow
  //   1: Sign
  //   2: Zero
  //   3: Carry A
  //   4: Carry L
  //   Shifter
  //   Bitwise-logic
  //   Adder
  //   Flags & control
  //   contents of ALU_Control (hex, n*v repeats v):
  //   0,10,20,c,4c,80,40,3,43,f,38,3e,36,33,30
endmodule
