// Digital circuit Board.dig as structural Verilog
module Board (
);

  wire LD0_p1, LD1_p1, LD2_p1, LD3_p1;

  LED LD7 (.in(LD3_p1));
  // RGBLED LD3: pin names not known; wires that end beside it: LD3_p1
  LED LD6 (.in(LD2_p1));
  // RGBLED LD2: pin names not known; wires that end beside it: LD2_p1
  LED LD5 (.in(LD1_p1));
  LED LD6_2 (.in(LD0_p1));
  // RGBLED LD0: pin names not known; wires that end beside it: LD0_p1
  // RGBLED LD1: pin names not known; wires that end beside it: LD1_p1
  DipSwitch SW2 ();  // open: out
  DipSwitch SW3 ();  // open: out
  System system_1 ();  // open: Clock, Reset
  DipSwitch SW0 ();  // open: out
  DipSwitch SW1 ();  // open: out
  Button BTN3 ();  // open: out
  Button BTN2 ();  // open: out
  Button BTN1 ();  // open: out
  Button BTN0 ();  // open: out
endmodule
