// Digital circuit Bus Control.dig as structural Verilog
module Bus_Control (
  input  [7:0] Main,
  input  [6:0] Xfer,
  input  [3:0] Inc,
  input  [3:0] ALU_Assert,
  input  [2:0] Addr_Assert,
  input  Reset,
  input  Clock,
  output [6:0] PCRA0,
  output [6:0] PCRA1,
  output [6:0] SP,
  output [6:0] SI,
  output [6:0] DI,
  output [3:0] GPR_A,
  output [3:0] GPR_B,
  output [3:0] GPR_C,
  output [3:0] GPR_D,
  output [2:0] Const,
  output [7:0] XFER_2,
  output [3:0] Mem,
  output [6:0] Dev_Assert,
  output [5:0] Dev_Load
);

  wire _7404_1_pin2, _7404_1_pin3, Clock_t;

  _7404 _7404_1 (
    .pin1(Clock), .pin2(_7404_1_pin2), .pin3(_7404_1_pin3), .pin4(Clock_t), .pin5(Clock_t), .pin6(DI[0]),
    .pin7(1'b0), .pin8(DI[1]), .pin9(Reset), .pin11(1'b0), .pin12(_7404_1_pin3), .pin13(_7404_1_pin2),
    .pin14(1'b1));  // open: pin10
  _74138 _74138_1 (
    .pin1(Xfer[0]), .pin2(Xfer[1]), .pin3(Xfer[2]), .pin4(1'b0), .pin5(1'b0), .pin6(1'b1), .pin7(XFER_2[3]),
    .pin8(1'b0), .pin9(XFER_2[2]), .pin10(DI[6]), .pin11(SI[6]), .pin12(SP[6]), .pin13(PCRA1[6]),
    .pin14(PCRA0[6]), .pin16(1'b1));  // open: pin15
  _74138 _74138_2 (
    .pin1(Addr_Assert[0]), .pin2(Addr_Assert[1]), .pin3(Addr_Assert[2]), .pin4(1'b0), .pin5(1'b0),
    .pin6(1'b1), .pin8(1'b0), .pin9(XFER_2[1]), .pin10(DI[5]), .pin11(SI[5]), .pin12(SP[5]),
    .pin13(PCRA1[5]), .pin14(PCRA0[5]), .pin15(Mem[3]), .pin16(1'b1));  // open: pin7
  _74138 _74138_3 (
    .pin1(Xfer[3]), .pin2(Xfer[4]), .pin3(Xfer[5]), .pin4(1'b0), .pin5(Clock_t), .pin6(Xfer[6]), .pin8(1'b0),
    .pin9(XFER_2[0]), .pin10(DI[4]), .pin11(SI[4]), .pin12(SP[4]), .pin13(PCRA1[4]), .pin14(PCRA0[4]),
    .pin16(1'b1));  // open: pin7, pin15
  _74139 _74139_1 (
    .pin1(Clock_t), .pin2(Inc[0]), .pin3(Inc[1]), .pin4(PCRA0[3]), .pin5(PCRA1[3]), .pin8(1'b0),
    .pin9(DI[3]), .pin10(SI[3]), .pin11(SP[3]), .pin13(Inc[3]), .pin14(Inc[2]), .pin15(Clock_t), .pin16(1'b1));  // open: pin6, pin7, pin12
  _74138 _74138_4 (
    .pin1(Xfer[3]), .pin2(Xfer[4]), .pin3(Xfer[5]), .pin4(1'b0), .pin5(Clock_t), .pin6(Xfer[6]), .pin8(1'b0),
    .pin10(DI[2]), .pin11(SI[2]), .pin12(SP[2]), .pin13(PCRA1[2]), .pin14(PCRA0[2]), .pin15(Const[0]),
    .pin16(1'b1));  // open: pin7, pin9
  _74138 _74138_5 (
    .pin1(Main[0]), .pin2(Main[1]), .pin3(Main[2]), .pin4(Main[3]), .pin5(1'b0), .pin6(1'b1),
    .pin7(XFER_2[7]), .pin8(1'b0), .pin9(XFER_2[5]), .pin10(Const[2]), .pin11(GPR_D[1]), .pin12(GPR_C[1]),
    .pin13(GPR_B[1]), .pin14(GPR_A[1]), .pin16(1'b1));  // open: pin15
  _74139 _74139_2 (
    .pin1(1'b0), .pin2(ALU_Assert[2]), .pin3(ALU_Assert[3]), .pin4(GPR_A[3]), .pin5(GPR_B[3]),
    .pin6(GPR_C[3]), .pin7(GPR_D[3]), .pin8(1'b0), .pin9(GPR_D[2]), .pin10(GPR_C[2]), .pin11(GPR_B[2]),
    .pin12(GPR_A[2]), .pin13(ALU_Assert[1]), .pin14(ALU_Assert[0]), .pin15(1'b0), .pin16(1'b1));
  _74138 _74138_6 (
    .pin1(Main[4]), .pin2(Main[5]), .pin3(Main[6]), .pin4(Main[7]), .pin5(Clock_t), .pin6(1'b1),
    .pin7(XFER_2[6]), .pin8(1'b0), .pin9(XFER_2[4]), .pin10(Const[1]), .pin11(GPR_D[0]), .pin12(GPR_C[0]),
    .pin13(GPR_B[0]), .pin14(GPR_A[0]), .pin16(1'b1));  // open: pin15
  _74138 _74138_7 (
    .pin1(Main[0]), .pin2(Main[1]), .pin3(Main[2]), .pin4(1'b0), .pin5(1'b0), .pin6(Main[3]), .pin7(Mem[0]),
    .pin8(1'b0), .pin9(Dev_Assert[6]), .pin10(Dev_Assert[5]), .pin11(Dev_Assert[4]), .pin12(Dev_Assert[3]),
    .pin13(Dev_Assert[2]), .pin14(Dev_Assert[1]), .pin15(Dev_Assert[0]), .pin16(1'b1));
  _74138 _74138_8 (
    .pin1(Main[4]), .pin2(Main[5]), .pin3(Main[6]), .pin4(1'b0), .pin5(Clock_t), .pin6(Main[7]),
    .pin7(Mem[1]), .pin8(1'b0), .pin9(Dev_Load[5]), .pin10(Dev_Load[4]), .pin11(Dev_Load[3]),
    .pin12(Dev_Load[2]), .pin13(Dev_Load[1]), .pin14(Dev_Load[0]), .pin16(1'b1));  // open: pin15
  _7420 _7420_1 (
    .pin1(Main[4]), .pin2(Main[5]), .pin4(Main[6]), .pin5(Main[7]), .pin6(Mem[2]), .pin7(1'b0), .pin9(1'b0),
    .pin10(1'b0), .pin12(1'b0), .pin13(1'b0), .pin14(1'b1));  // open: pin3, pin8, pin11

  assign PCRA0[1:0] = DI[1:0];
  assign PCRA1[1:0] = DI[1:0];
  assign SI[1:0] = DI[1:0];
  assign SP[1:0] = DI[1:0];

  // Other names for the same wires on the sheet: Addr[2:0] = Addr_Assert; ALU[3:0] = ALU_Assert

  // Notes on the sheet:
  //   Main: 0-3: Assert A-D
  //   4-7: Load A-D
  //   Xfer: Assert:
  //   xxxx000: -
  //   xxxx001: PCRA0
  //   xxxx010: PCRA1
  //   xxxx011: SP
  //   xxxx100: SI
  //   xxxx101: DI
  //   xxxx110: TX
  //   xxxx111: TX mode
  //   Load:
  //   0000xxx: -
  //   0001xxx: PCRA0
  //   0010xxx: PCRA1
  //   0011xxx: SP
  //   0100xxx: SI
  //   0101xxx: DI
  //   0110xxx: TX
  //   0111xxx: -
  //   1000xxx: Const LoadMem
  //   Dec:
  //   1001xxx: PCRA0
  //   1010xxx: PCRA1
  //   1011xxx: SP
  //   1100xxx: SI
  //   1101xxx: DI
  //   1110xxx: -
  //   1111xxx: -
  //   Inc: xx00: Inc PCRA0
  //   xx01: Inc PCRA1
  //   xx10: -
  //   xx11: -
  //   00xx: -
  //   01xx: Inc SP
  //   10xx: Inc SI
  //   11xx: Inc DI
  //   ALU_Assert: xx00-xx11: LHS A-B
  //   00xx-11xx: RHS A-B
  //   Addr_Assert: 000 Memory Ack
  //   001 PCRA0
  //   010 PCRA1
  //   011 SP
  //   100 SI
  //   101 DI
  //   111 TX
  //   PCRA0: 0: Clock
  //   1: Clear
  //   2: Dec
  //   3: Inc
  //   4: Load
  //   5: Assert Addr
  //   6: Assert Bus
  //   PCRA1: 0: Clock
  //   1: Clear
  //   2: Dec
  //   3: Inc
  //   4: Load
  //   5: Assert Addr
  //   6: Assert Bus
  //   SP: 0: Clock
  //   1: Clear
  //   2: Dec
  //   3: Inc
  //   4: Load
  //   5: Assert Addr
  //   6: Assert Bus
  //   SI: 0: Clock
  //   1: Clear
  //   2: Dec
  //   3: Inc
  //   4: Load
  //   5: Assert Addr
  //   6: Assert Bus
  //   DI: 0: Clock
  //   1: Clear
  //   2: Dec
  //   3: Inc
  //   4: Load
  //   5: Assert Addr
  //   6: Assert Bus
  //   GPR_A: 0: Load
  //   1: Assert Main
  //   2: Assert LHS
  //   3: Assert RHS
  //   GPR_B: 0: Load
  //   1: Assert Main
  //   2: Assert LHS
  //   3: Assert RHS
  //   GPR_C: 0: Load
  //   1: Assert Main
  //   2: Assert LHS
  //   3: Assert RHS
  //   GPR_D: 0: Load
  //   1: Assert Main
  //   2: Assert LHS
  //   3: Assert RHS
  //   Const: 0: Load Bus
  //   1: Load Mem
  //   2: Assert Main
  //   XFER_2: 0: RegTX Load
  //   1: RegTX Assert Addr
  //   2: RegTX Assert Xfer
  //   3: RegTX Assert Mode
  //   4: RegTL Load
  //   5: RegTL Assert
  //   6: RegTH Load
  //   7: RegTH Assert
  //   Mem: 0: Assert
  //   1: Load
  //   2: Dir
  //   3: Ack
  //   Dev_Assert: 0: ALU
  //   1-6: Assert Dev 9-14
  //   Dev_Load: 0-5: Load Dev 9-14
endmodule
