// Digital circuit Address Register.dig as structural Verilog
module Address_Register (
  input  [6:0] Control,
  output [15:0] ADDR,
  output [15:0] XFER
);

  wire _74193_1_pin12, _74193_1_pin13, _74193_2_pin12, _74193_2_pin13, _74193_3_pin12, _74193_3_pin13;
  wire [7:0] Reg_H, Reg_L;

  _74574 _74574_1 (
    .pin1(Control[6]), .pin2(Reg_L[0]), .pin3(Reg_L[1]), .pin4(Reg_L[2]), .pin5(Reg_L[3]), .pin6(Reg_L[4]),
    .pin7(Reg_L[5]), .pin8(Reg_L[6]), .pin9(Reg_L[7]), .pin10(1'b0), .pin11(Control[0]), .pin12(XFER[7]),
    .pin13(XFER[6]), .pin14(XFER[5]), .pin15(XFER[4]), .pin16(XFER[3]), .pin17(XFER[2]), .pin18(XFER[1]),
    .pin19(XFER[0]), .pin20(1'b1));
  _74193 _74193_1 (
    .pin1(XFER[1]), .pin2(Reg_L[1]), .pin3(Reg_L[0]), .pin4(Control[2]), .pin5(Control[3]), .pin6(Reg_L[2]),
    .pin7(Reg_L[3]), .pin8(1'b0), .pin9(XFER[3]), .pin10(XFER[2]), .pin11(Control[4]),
    .pin12(_74193_1_pin12), .pin13(_74193_1_pin13), .pin14(Control[1]), .pin15(XFER[0]), .pin16(1'b1));
  _74574 _74574_2 (
    .pin1(Control[6]), .pin2(Reg_H[0]), .pin3(Reg_H[1]), .pin4(Reg_H[2]), .pin5(Reg_H[3]), .pin6(Reg_H[4]),
    .pin7(Reg_H[5]), .pin8(Reg_H[6]), .pin9(Reg_H[7]), .pin10(1'b0), .pin11(Control[0]), .pin12(XFER[15]),
    .pin13(XFER[14]), .pin14(XFER[13]), .pin15(XFER[12]), .pin16(XFER[11]), .pin17(XFER[10]),
    .pin18(XFER[9]), .pin19(XFER[8]), .pin20(1'b1));
  _74193 _74193_2 (
    .pin1(XFER[5]), .pin2(Reg_L[5]), .pin3(Reg_L[4]), .pin4(_74193_1_pin13), .pin5(_74193_1_pin12),
    .pin6(Reg_L[6]), .pin7(Reg_L[7]), .pin8(1'b0), .pin9(XFER[7]), .pin10(XFER[6]), .pin11(Control[4]),
    .pin12(_74193_2_pin12), .pin13(_74193_2_pin13), .pin14(Control[1]), .pin15(XFER[4]), .pin16(1'b1));
  _74574 _74574_3 (
    .pin1(Control[5]), .pin2(Reg_L[0]), .pin3(Reg_L[1]), .pin4(Reg_L[2]), .pin5(Reg_L[3]), .pin6(Reg_L[4]),
    .pin7(Reg_L[5]), .pin8(Reg_L[6]), .pin9(Reg_L[7]), .pin10(1'b0), .pin11(Control[0]), .pin12(ADDR[7]),
    .pin13(ADDR[6]), .pin14(ADDR[5]), .pin15(ADDR[4]), .pin16(ADDR[3]), .pin17(ADDR[2]), .pin18(ADDR[1]),
    .pin19(ADDR[0]), .pin20(1'b1));
  _74193 _74193_3 (
    .pin1(XFER[9]), .pin2(Reg_H[1]), .pin3(Reg_H[0]), .pin4(_74193_2_pin13), .pin5(_74193_2_pin12),
    .pin6(Reg_H[2]), .pin7(Reg_H[3]), .pin8(1'b0), .pin9(XFER[11]), .pin10(XFER[10]), .pin11(Control[4]),
    .pin12(_74193_3_pin12), .pin13(_74193_3_pin13), .pin14(Control[1]), .pin15(XFER[8]), .pin16(1'b1));
  _74574 _74574_4 (
    .pin1(Control[5]), .pin2(Reg_H[0]), .pin3(Reg_H[1]), .pin4(Reg_H[2]), .pin5(Reg_H[3]), .pin6(Reg_H[4]),
    .pin7(Reg_H[5]), .pin8(Reg_H[6]), .pin9(Reg_H[7]), .pin10(1'b0), .pin11(Control[0]), .pin12(ADDR[15]),
    .pin13(ADDR[14]), .pin14(ADDR[13]), .pin15(ADDR[12]), .pin16(ADDR[11]), .pin17(ADDR[10]),
    .pin18(ADDR[9]), .pin19(ADDR[8]), .pin20(1'b1));
  _74193 _74193_4 (
    .pin1(XFER[13]), .pin2(Reg_H[5]), .pin3(Reg_H[4]), .pin4(_74193_3_pin13), .pin5(_74193_3_pin12),
    .pin6(Reg_H[6]), .pin7(Reg_H[7]), .pin8(1'b0), .pin9(XFER[15]), .pin10(XFER[14]), .pin11(Control[4]),
    .pin14(Control[1]), .pin15(XFER[12]), .pin16(1'b1));  // open: pin12, pin13

  // Other names for the same wires on the sheet: Addr_H[7:0] = ADDR[15:8]; Addr_L[7:0] = ADDR[7:0];
  //   Xfer_H[7:0] = XFER[15:8]; Xfer_L[7:0] = XFER[7:0]; Clock = Control[0]; Clear = Control[1]; Dec = Control[2];
  //   Inc = Control[3]; Load = Control[4]; A_Addr = Control[5]; A_Bus = Control[6]

  // Notes on the sheet:
  //   ADDR: Addr Bus
  //   XFER: Xfer Bus
  //   Control: 0: Clock
  //   1: Clear
  //   2: Dec
  //   3: Inc
  //   4: Load
  //   5: Assert Addr
  //   6: Assert Bus
endmodule
