// Digital circuit IOBuffer.dig as structural Verilog
module IOBuffer (
  input  [7:0] D_IN,
  input  Clock,
  input  R_nW,
  input  Sel,
  input  [7:0] D_r,
  output [7:0] D_w,
  output [7:0] Out_en,
  output [7:0] D_out
);

  wire and_1_out;

  and and_1 (and_1_out, Sel, R_nW);
  and and_2 (Out_en[0], Sel, ~R_nW);  // And
  Register #(.Bits(8), .generic("this.Bits=int(args.bitWidth);")) register_1 (
    .D(D_IN), .C(Clock), .en(and_1_out), .Q(D_w));
  // Pins of 1 and 8 bits meet at Out_en

  assign D_out = D_r;
endmodule
