// Digital circuit Main - exploded.dig as structural Verilog
module Main___exploded (
  input  clk
);

  wire _7400_1_pin3, _7402_1_pin1, _7402_1_pin2, _7402_1_pin6, _7402_1_pin10, _7402_1_pin13, _7404_1_pin2,
       _7404_1_pin3, _7404_1_pin4, _7404_1_pin5, _7404_1_pin6, _7404_1_pin8, _7404_1_pin12, _7404_1_pin13,
       _7404_2_pin3, _7404_2_pin4, _7404_2_pin5, _7404_2_pin6, _7404_2_pin13, _7408_1_pin1, _7408_1_pin2,
       _7408_1_pin3, _7408_1_pin4, _7408_1_pin6, _7408_1_pin8, _7408_1_pin11, _7408_2_pin4, _7408_2_pin5,
       _7408_2_pin9, _7408_2_pin10, _7486_1_pin10, _7486_1_pin13, _74138_1_pin1, _74138_1_pin2,
       _74138_1_pin3, _74138_1_pin4, _74138_1_pin5, _74138_2_pin15, _74138_3_pin1, _74138_3_pin2,
       _74138_3_pin3, _74138_4_pin1, _74138_4_pin2, _74138_4_pin3, _74138_5_pin1, _74138_5_pin2,
       _74138_5_pin3, _74138_5_pin4, _74138_5_pin10, _74138_5_pin11, _74138_5_pin12, _74138_5_pin13,
       _74138_5_pin14, _74138_6_pin1, _74138_6_pin2, _74138_6_pin3, _74138_6_pin4, _74138_6_pin11,
       _74138_6_pin12, _74138_6_pin13, _74138_6_pin14, _74138_7_pin7, _74138_7_pin10, _74138_7_pin11,
       _74138_7_pin12, _74138_7_pin13, _74138_7_pin14, _74138_7_pin15, _74138_8_pin10, _74138_8_pin11,
       _74138_8_pin12, _74138_8_pin13, _74138_8_pin14, _74139_1_pin2, _74139_1_pin3, _74139_1_pin13,
       _74139_1_pin14, _74139_2_pin4, _74139_2_pin5, _74139_2_pin6, _74139_2_pin7, _74139_2_pin9,
       _74139_2_pin10, _74139_2_pin11, _74139_2_pin12, _74153_1_pin2, _74153_1_pin7, _74153_1_pin9,
       _74153_1_pin14, _74153_2_pin7, _74153_2_pin9, _74153_3_pin7, _74153_3_pin9, _74153_4_pin7,
       _74153_4_pin9, _74157_1_pin4, _74157_1_pin7, _74157_1_pin9, _74157_1_pin12, _74157_2_pin4,
       _74157_2_pin7, _74157_2_pin9, _74157_2_pin12, _74157_3_pin4, _74157_3_pin7, _74157_3_pin9,
       _74157_3_pin12, _74157_4_pin4, _74157_4_pin7, _74157_4_pin9, _74157_4_pin12, _74193_1_pin4,
       _74193_1_pin5, _74193_1_pin11, _74193_1_pin12, _74193_1_pin13, _74193_1_pin14, _74193_2_pin12,
       _74193_2_pin13, _74193_3_pin12, _74193_3_pin13, _74193_5_pin4, _74193_5_pin5, _74193_5_pin11,
       _74193_5_pin12, _74193_5_pin13, _74193_5_pin14, _74193_6_pin12, _74193_6_pin13, _74193_7_pin12,
       _74193_7_pin13, _74193_9_pin4, _74193_9_pin5, _74193_9_pin11, _74193_9_pin12, _74193_9_pin13,
       _74193_9_pin14, _74193_10_pin12, _74193_10_pin13, _74193_11_pin12, _74193_11_pin13, _74193_13_pin4,
       _74193_13_pin5, _74193_13_pin11, _74193_13_pin12, _74193_13_pin13, _74193_13_pin14, _74193_14_pin12,
       _74193_14_pin13, _74193_15_pin12, _74193_15_pin13, _74193_17_pin4, _74193_17_pin5, _74193_17_pin11,
       _74193_17_pin12, _74193_17_pin13, _74193_17_pin14, _74193_18_pin12, _74193_18_pin13, _74193_19_pin12,
       _74193_19_pin13, _74253_1_pin4, _74253_1_pin5, _74253_2_pin4, _74253_2_pin6, _74253_2_pin7,
       _74253_2_pin9, _74253_3_pin4, _74253_3_pin6, _74253_3_pin7, _74253_3_pin9, _74253_4_pin4,
       _74253_4_pin6, _74253_4_pin7, _74253_5_pin9, _74253_6_pin14, _74283_1_pin2, _74283_1_pin3,
       _74283_1_pin5, _74283_1_pin6, _74283_1_pin9, _74283_1_pin11, _74283_1_pin12, _74283_1_pin14,
       _74283_1_pin15, _74283_2_pin2, _74283_2_pin3, _74283_2_pin5, _74283_2_pin6, _74283_2_pin11,
       _74283_2_pin12, _74283_2_pin14, _74283_2_pin15, _74541_1_pin1, _74541_1_pin2, _74541_1_pin3,
       _74541_1_pin4, _74541_1_pin5, _74541_1_pin6, _74541_1_pin7, _74541_1_pin8, _74541_1_pin9,
       _74541_2_pin2, _74541_2_pin3, _74541_2_pin4, _74541_2_pin5, _74541_2_pin6, _74541_2_pin7,
       _74541_2_pin8, _74541_2_pin9, _74541_3_pin1, _74541_3_pin11, _74541_3_pin12, _74541_3_pin13,
       _74541_3_pin14, _74541_3_pin15, _74541_3_pin16, _74541_3_pin17, _74541_3_pin18, _74541_4_pin11,
       _74541_4_pin12, _74541_4_pin13, _74541_4_pin14, _74541_4_pin15, _74541_4_pin16, _74541_4_pin17,
       _74541_4_pin18, _74541_7_pin11, _74541_7_pin12, _74541_7_pin13, _74541_7_pin14, _74541_7_pin15,
       _74541_7_pin16, _74541_7_pin17, _74541_14_pin11, _74541_14_pin12, _74541_14_pin13, _74541_14_pin14,
       _74541_14_pin15, _74541_14_pin16, _74541_14_pin17, _74541_14_pin18, _74541_15_pin11, _74541_15_pin12,
       _74541_15_pin13, _74541_15_pin14, _74541_15_pin15, _74541_15_pin16, _74541_15_pin17, _74541_15_pin18,
       _74541_16_pin11, _74541_16_pin12, _74541_16_pin13, _74541_16_pin14, _74541_16_pin15, _74541_16_pin16,
       _74541_16_pin17, _74541_16_pin18, _74541_17_pin11, _74541_17_pin12, _74541_17_pin13, _74541_17_pin14,
       _74541_17_pin15, _74541_17_pin16, _74541_17_pin17, _74541_17_pin18, _74541_18_pin11, _74541_18_pin12,
       _74541_18_pin13, _74541_18_pin14, _74541_18_pin15, _74541_18_pin16, _74541_18_pin17, _74541_18_pin18,
       _74541_19_pin11, _74541_19_pin12, _74541_19_pin13, _74541_19_pin14, _74541_19_pin15, _74541_19_pin16,
       _74541_19_pin17, _74541_19_pin18, _74541_20_pin11, _74541_20_pin12, _74541_20_pin13, _74541_20_pin14,
       _74541_20_pin15, _74541_20_pin16, _74541_20_pin17, _74541_20_pin18, _74541_21_pin11, _74541_21_pin12,
       _74541_21_pin13, _74541_21_pin14, _74541_21_pin15, _74541_21_pin16, _74541_21_pin17, _74541_21_pin18,
       _74574_1_pin1, _74574_1_pin2, _74574_1_pin3, _74574_1_pin4, _74574_1_pin5, _74574_1_pin6,
       _74574_1_pin7, _74574_1_pin8, _74574_1_pin9, _74574_1_pin11, _74574_2_pin2, _74574_2_pin3,
       _74574_2_pin4, _74574_2_pin5, _74574_2_pin6, _74574_2_pin7, _74574_2_pin8, _74574_2_pin9,
       _74574_3_pin1, _74574_3_pin2, _74574_3_pin3, _74574_3_pin4, _74574_3_pin5, _74574_3_pin6,
       _74574_3_pin7, _74574_3_pin8, _74574_3_pin9, _74574_3_pin11, _74574_4_pin2, _74574_4_pin3,
       _74574_4_pin4, _74574_4_pin5, _74574_4_pin6, _74574_4_pin7, _74574_4_pin8, _74574_4_pin9,
       _74574_5_pin1, _74574_5_pin2, _74574_5_pin3, _74574_5_pin4, _74574_5_pin5, _74574_5_pin6,
       _74574_5_pin7, _74574_5_pin8, _74574_5_pin9, _74574_5_pin11, _74574_6_pin2, _74574_6_pin3,
       _74574_6_pin4, _74574_6_pin5, _74574_6_pin6, _74574_6_pin7, _74574_6_pin8, _74574_6_pin9,
       _74574_7_pin1, _74574_7_pin2, _74574_7_pin3, _74574_7_pin4, _74574_7_pin5, _74574_7_pin6,
       _74574_7_pin7, _74574_7_pin8, _74574_7_pin9, _74574_7_pin11, _74574_8_pin2, _74574_8_pin3,
       _74574_8_pin4, _74574_8_pin5, _74574_8_pin6, _74574_8_pin7, _74574_8_pin8, _74574_8_pin9,
       _74574_9_pin1, _74574_9_pin2, _74574_9_pin3, _74574_9_pin4, _74574_9_pin5, _74574_9_pin6,
       _74574_9_pin7, _74574_9_pin8, _74574_9_pin9, _74574_9_pin11, _74574_10_pin2, _74574_10_pin3,
       _74574_10_pin4, _74574_10_pin5, _74574_10_pin6, _74574_10_pin7, _74574_10_pin8, _74574_10_pin9,
       _74574_11_pin1, _74574_11_pin12, _74574_11_pin13, _74574_11_pin14, _74574_11_pin15, _74574_11_pin16,
       _74574_11_pin17, _74574_11_pin18, _74574_11_pin19, _74574_12_pin12, _74574_12_pin13, _74574_12_pin14,
       _74574_12_pin15, _74574_12_pin16, _74574_12_pin17, _74574_12_pin18, _74574_12_pin19, _74574_13_pin1,
       _74574_13_pin12, _74574_13_pin13, _74574_13_pin14, _74574_13_pin15, _74574_13_pin16, _74574_13_pin17,
       _74574_13_pin18, _74574_13_pin19, _74574_14_pin12, _74574_14_pin13, _74574_14_pin14, _74574_14_pin15,
       _74574_14_pin16, _74574_14_pin17, _74574_14_pin18, _74574_14_pin19, _74574_15_pin1, _74574_15_pin12,
       _74574_15_pin13, _74574_15_pin14, _74574_15_pin15, _74574_15_pin16, _74574_15_pin17, _74574_15_pin18,
       _74574_15_pin19, _74574_16_pin12, _74574_16_pin13, _74574_16_pin14, _74574_16_pin15, _74574_16_pin16,
       _74574_16_pin17, _74574_16_pin18, _74574_16_pin19, _74574_17_pin1, _74574_17_pin12, _74574_17_pin13,
       _74574_17_pin14, _74574_17_pin15, _74574_17_pin16, _74574_17_pin17, _74574_17_pin18, _74574_17_pin19,
       _74574_18_pin12, _74574_18_pin13, _74574_18_pin14, _74574_18_pin15, _74574_18_pin16, _74574_18_pin17,
       _74574_18_pin18, _74574_18_pin19, _74574_19_pin1, _74574_19_pin12, _74574_19_pin13, _74574_19_pin14,
       _74574_19_pin15, _74574_19_pin16, _74574_19_pin17, _74574_19_pin18, _74574_19_pin19, _74574_20_pin12,
       _74574_20_pin13, _74574_20_pin14, _74574_20_pin15, _74574_20_pin16, _74574_20_pin17, _74574_20_pin18,
       _74574_20_pin19, _74574_21_pin12, _74574_21_pin13, _74574_21_pin14, _74574_21_pin15, _74574_21_pin16,
       _74574_21_pin17, _74574_21_pin18, _74574_21_pin19, _74574_22_pin2, _74574_22_pin3, _74574_22_pin4,
       _74574_22_pin5, _74574_22_pin6, _74574_22_pin7, _74574_22_pin8, _74574_22_pin9, _74574_22_pin12,
       _74574_22_pin13, _74574_22_pin14, _74574_22_pin15, _74574_22_pin16, _74574_22_pin17, _74574_22_pin18,
       _74574_23_pin2, _74574_23_pin3, _74574_23_pin4, _74574_23_pin5, _74574_23_pin6, _74574_23_pin7,
       _74574_23_pin8, _74574_23_pin9, _74574_23_pin12, _74574_23_pin13, _74574_23_pin14, _74574_23_pin15,
       _74574_23_pin16, _74574_23_pin17, _74574_23_pin18, _74574_23_pin19, _74574_26_pin12, _74574_26_pin13,
       _74574_26_pin14, _74574_26_pin15, _74574_26_pin16, _74574_26_pin17, _74574_26_pin18, _74574_26_pin19,
       _74574_27_pin2, _74574_27_pin3, _74574_27_pin4, _74574_27_pin5, _74574_27_pin6, _74574_27_pin7,
       _74574_27_pin8, _74574_27_pin9, _74574_27_pin12, _74574_27_pin13, _74574_27_pin14, _74574_27_pin15,
       _74574_27_pin16, _74574_27_pin17, _74574_28_pin2, _74574_28_pin3, _74574_28_pin4, _74574_28_pin5,
       _74574_28_pin6, _74574_28_pin7, _74574_28_pin8, _74574_28_pin9, _74574_28_pin12, _74574_28_pin13,
       _74574_28_pin14, _74574_28_pin15, _74574_28_pin16, _74574_28_pin17, _74574_28_pin18, _74574_29_pin12,
       _74574_29_pin13, _74574_29_pin14, _74574_29_pin15, _74574_29_pin16, _74574_29_pin17, _74574_29_pin18,
       _74574_29_pin19, _74574_30_pin12, _74574_30_pin13, _74574_30_pin14, _74574_30_pin15, _74574_30_pin16,
       _74574_30_pin17, _74574_30_pin18, _74574_30_pin19, _74574_31_pin12, _74574_31_pin13, _74574_31_pin14,
       _74574_31_pin15, _74574_31_pin16, _74574_31_pin17, _74574_31_pin18, _74574_31_pin19, _74574_32_pin12,
       _74574_32_pin13, _74574_32_pin14, _74574_32_pin15, _74574_32_pin16, _74574_32_pin17, _74574_32_pin18,
       _74574_32_pin19, _74574_34_pin6, _74574_34_pin14, _74574_34_pin16, _74574_34_pin19, _74574_36_pin2,
       _74574_36_pin3, _74574_36_pin4, _74574_36_pin5, _74574_36_pin6, _74574_36_pin7, _74574_36_pin8,
       fuse_1_a, fuse_1_b, fuse_2_a, fuse_2_b, fuse_3_a, fuse_3_b, fuse_4_a, fuse_4_b, fuse_9_a, fuse_10_a,
       fuse_11_a, fuse_12_a, fuse_13_a, fuse_14_a, fuse_15_a, fuse_16_a, fuse_17_a, fuse_18_a, fuse_19_a,
       fuse_20_a, fuse_21_a, fuse_22_a, fuse_23_a, fuse_24_a, fuse_25_a, fuse_26_a, fuse_27_a, fuse_28_a,
       fuse_29_a, fuse_29_b, fuse_30_a, fuse_30_b, fuse_31_a, fuse_31_b, fuse_32_a, fuse_32_b, fuse_37_a,
       fuse_38_a, fuse_39_a, fuse_40_a, fuse_41_a, fuse_42_a, fuse_43_a, fuse_44_a, fuse_45_a, fuse_46_a,
       fuse_47_a, fuse_48_a, fuse_49_a, fuse_50_a, fuse_51_a, fuse_52_a, fuse_53_a, fuse_54_a, fuse_55_a,
       fuse_56_a, fuse_57_a, fuse_57_b, fuse_58_a, fuse_58_b, fuse_59_a, fuse_59_b, fuse_60_a, fuse_60_b,
       fuse_65_a, fuse_66_a, fuse_67_a, fuse_68_a, fuse_69_a, fuse_70_a, fuse_71_a, fuse_72_a, fuse_73_a,
       fuse_74_a, fuse_75_a, fuse_76_a, fuse_77_a, fuse_78_a, fuse_79_a, fuse_80_a, fuse_81_a, fuse_82_a,
       fuse_83_a, fuse_84_a, fuse_85_a, fuse_85_b, fuse_86_a, fuse_86_b, fuse_87_a, fuse_87_b, fuse_88_a,
       fuse_88_b, fuse_93_a, fuse_94_a, fuse_95_a, fuse_96_a, fuse_97_a, fuse_98_a, fuse_99_a, fuse_100_a,
       fuse_101_a, fuse_102_a, fuse_103_a, fuse_104_a, fuse_105_a, fuse_106_a, fuse_107_a, fuse_108_a,
       fuse_109_a, fuse_110_a, fuse_111_a, fuse_112_a, fuse_167_a, fuse_167_b, fuse_168_a, fuse_168_b,
       fuse_169_a, fuse_169_b, fuse_170_a, fuse_170_b, fuse_171_a, fuse_171_b, fuse_172_a, fuse_172_b,
       fuse_173_a, fuse_173_b, fuse_174_a, fuse_174_b, fuse_217_a, fuse_218_a, fuse_221_b, fuse_222_b,
       fuse_223_b, fuse_225_b, fuse_226_b, fuse_227_b, fuse_228_b, fuse_229_b, fuse_230_b, fuse_233_b,
       fuse_234_b, fuse_235_b, fuse_236_b, fuse_237_b, fuse_240_b, fuse_241_b, fuse_242_b, fuse_243_b,
       fuse_244_b, fuse_247_b, fuse_248_b, fuse_249_b, fuse_250_b, fuse_251_b, fuse_254_b, fuse_255_b,
       fuse_256_a, fuse_257_a, fuse_257_b, fuse_258_a, fuse_262_a, fuse_262_b, fuse_264_a, fuse_275_b,
       fuse_276_b, fuse_277_b, fuse_278_b, fuse_279_b, fuse_280_b, fuse_281_b, fuse_282_b, fuse_283_a,
       fuse_283_b, fuse_284_a, fuse_284_b, fuse_285_a, fuse_285_b, fuse_286_a, fuse_286_b, fuse_287_a,
       fuse_287_b, fuse_301_b, fuse_302_b, fuse_303_b, fuse_304_b, fuse_305_b, fuse_306_b, fuse_307_b,
       fuse_308_b, fuse_309_b, fuse_310_b, fuse_311_b, fuse_312_b, fuse_313_b, fuse_314_b, fuse_315_b,
       fuse_316_b, fuse_317_b, fuse_318_b, fuse_319_b, fuse_320_b, fuse_321_b, fuse_322_b, fuse_323_b,
       fuse_324_b, fuse_325_b, fuse_326_b, fuse_327_b, fuse_328_b, fuse_329_b, fuse_330_b, fuse_331_a,
       fuse_332_a, fuse_333_a, fuse_334_a, fuse_335_a, fuse_336_a, fuse_337_a, fuse_338_a, fuse_339_a,
       fuse_340_a, fuse_341_a, fuse_342_a, fuse_343_a, fuse_344_a, fuse_345_a, fuse_346_a, fuse_347_a,
       fuse_348_a, fuse_349_a, fuse_350_a, fuse_351_a, fuse_352_a, fuse_353_a, fuse_354_a, fuse_355_a,
       fuse_356_a, fuse_357_a, fuse_358_a, fuse_359_a, fuse_360_a, fuse_361_a, fuse_362_a, fuse_363_a,
       fuse_364_a, fuse_365_a, fuse_366_a, fuse_367_a, fuse_368_a, fuse_369_a, fuse_370_a, fuse_371_a,
       fuse_372_a, fuse_373_a, fuse_374_a, fuse_375_a, fuse_376_a, fuse_377_a, fuse_378_a, fuse_379_a,
       fuse_380_a, fuse_381_a, fuse_382_a, fuse_383_a, fuse_384_a, fuse_385_a, fuse_386_a, fuse_431_a,
       fuse_432_a, fuse_433_a, fuse_434_a, fuse_447_a, fuse_448_a, fuse_449_a, fuse_450_a, not_2_out;
  wire [7:0] _74157_3_pin14, _74253_1_pin14;

  Fuse fuse_1 (.A(fuse_1_a), .B(fuse_1_b));
  Fuse fuse_2 (.A(fuse_2_a), .B(fuse_2_b));
  Fuse fuse_3 (.A(fuse_3_a), .B(fuse_3_b));
  Fuse fuse_4 (.A(fuse_4_a), .B(fuse_4_b));
  Fuse fuse_5 (.A(fuse_1_a), .B(fuse_1_b));
  Fuse fuse_6 (.A(fuse_2_a), .B(fuse_2_b));
  Fuse fuse_7 (.A(fuse_3_a), .B(fuse_3_b));
  Fuse fuse_8 (.A(fuse_4_a), .B(fuse_4_b));
  Fuse fuse_9 (.A(fuse_9_a), .B(fuse_1_a));
  Fuse fuse_10 (.A(fuse_10_a), .B(fuse_2_a));
  Fuse fuse_11 (.A(fuse_11_a), .B(fuse_3_a));
  Fuse fuse_12 (.A(fuse_12_a), .B(fuse_4_a));
  Fuse fuse_13 (.A(fuse_13_a), .B(fuse_9_a));
  Fuse fuse_14 (.A(fuse_14_a), .B(fuse_10_a));
  Fuse fuse_15 (.A(fuse_15_a), .B(fuse_11_a));
  Fuse fuse_16 (.A(fuse_16_a), .B(fuse_12_a));
  Fuse fuse_17 (.A(fuse_17_a), .B(fuse_13_a));
  Fuse fuse_18 (.A(fuse_18_a), .B(fuse_14_a));
  Fuse fuse_19 (.A(fuse_19_a), .B(fuse_15_a));
  Fuse fuse_20 (.A(fuse_20_a), .B(fuse_16_a));
  Fuse fuse_21 (.A(fuse_21_a), .B(fuse_17_a));
  Fuse fuse_22 (.A(fuse_22_a), .B(fuse_18_a));
  Fuse fuse_23 (.A(fuse_23_a), .B(fuse_19_a));
  Fuse fuse_24 (.A(fuse_24_a), .B(fuse_20_a));
  Fuse fuse_25 (.A(fuse_25_a), .B(fuse_21_a));
  Fuse fuse_26 (.A(fuse_26_a), .B(fuse_22_a));
  Fuse fuse_27 (.A(fuse_27_a), .B(fuse_23_a));
  Fuse fuse_28 (.A(fuse_28_a), .B(fuse_24_a));
  Fuse fuse_29 (.A(fuse_29_a), .B(fuse_29_b));
  Fuse fuse_30 (.A(fuse_30_a), .B(fuse_30_b));
  Fuse fuse_31 (.A(fuse_31_a), .B(fuse_31_b));
  Fuse fuse_32 (.A(fuse_32_a), .B(fuse_32_b));
  Fuse fuse_33 (.A(fuse_29_a), .B(fuse_29_b));
  Fuse fuse_34 (.A(fuse_30_a), .B(fuse_30_b));
  Fuse fuse_35 (.A(fuse_31_a), .B(fuse_31_b));
  Fuse fuse_36 (.A(fuse_32_a), .B(fuse_32_b));
  Fuse fuse_37 (.A(fuse_37_a), .B(fuse_29_a));
  Fuse fuse_38 (.A(fuse_38_a), .B(fuse_30_a));
  Fuse fuse_39 (.A(fuse_39_a), .B(fuse_31_a));
  Fuse fuse_40 (.A(fuse_40_a), .B(fuse_32_a));
  Fuse fuse_41 (.A(fuse_41_a), .B(fuse_37_a));
  Fuse fuse_42 (.A(fuse_42_a), .B(fuse_38_a));
  Fuse fuse_43 (.A(fuse_43_a), .B(fuse_39_a));
  Fuse fuse_44 (.A(fuse_44_a), .B(fuse_40_a));
  Fuse fuse_45 (.A(fuse_45_a), .B(fuse_41_a));
  Fuse fuse_46 (.A(fuse_46_a), .B(fuse_42_a));
  Fuse fuse_47 (.A(fuse_47_a), .B(fuse_43_a));
  Fuse fuse_48 (.A(fuse_48_a), .B(fuse_44_a));
  Fuse fuse_49 (.A(fuse_49_a), .B(fuse_45_a));
  Fuse fuse_50 (.A(fuse_50_a), .B(fuse_46_a));
  Fuse fuse_51 (.A(fuse_51_a), .B(fuse_47_a));
  Fuse fuse_52 (.A(fuse_52_a), .B(fuse_48_a));
  Fuse fuse_53 (.A(fuse_53_a), .B(fuse_49_a));
  Fuse fuse_54 (.A(fuse_54_a), .B(fuse_50_a));
  Fuse fuse_55 (.A(fuse_55_a), .B(fuse_51_a));
  Fuse fuse_56 (.A(fuse_56_a), .B(fuse_52_a));
  Fuse fuse_57 (.A(fuse_57_a), .B(fuse_57_b));
  Fuse fuse_58 (.A(fuse_58_a), .B(fuse_58_b));
  Fuse fuse_59 (.A(fuse_59_a), .B(fuse_59_b));
  Fuse fuse_60 (.A(fuse_60_a), .B(fuse_60_b));
  Fuse fuse_61 (.A(fuse_57_a), .B(fuse_57_b));
  Fuse fuse_62 (.A(fuse_58_a), .B(fuse_58_b));
  Fuse fuse_63 (.A(fuse_59_a), .B(fuse_59_b));
  Fuse fuse_64 (.A(fuse_60_a), .B(fuse_60_b));
  Fuse fuse_65 (.A(fuse_65_a), .B(fuse_57_a));
  Fuse fuse_66 (.A(fuse_66_a), .B(fuse_58_a));
  Fuse fuse_67 (.A(fuse_67_a), .B(fuse_59_a));
  Fuse fuse_68 (.A(fuse_68_a), .B(fuse_60_a));
  Fuse fuse_69 (.A(fuse_69_a), .B(fuse_65_a));
  Fuse fuse_70 (.A(fuse_70_a), .B(fuse_66_a));
  Fuse fuse_71 (.A(fuse_71_a), .B(fuse_67_a));
  Fuse fuse_72 (.A(fuse_72_a), .B(fuse_68_a));
  Fuse fuse_73 (.A(fuse_73_a), .B(fuse_69_a));
  Fuse fuse_74 (.A(fuse_74_a), .B(fuse_70_a));
  Fuse fuse_75 (.A(fuse_75_a), .B(fuse_71_a));
  Fuse fuse_76 (.A(fuse_76_a), .B(fuse_72_a));
  Fuse fuse_77 (.A(fuse_77_a), .B(fuse_73_a));
  Fuse fuse_78 (.A(fuse_78_a), .B(fuse_74_a));
  Fuse fuse_79 (.A(fuse_79_a), .B(fuse_75_a));
  Fuse fuse_80 (.A(fuse_80_a), .B(fuse_76_a));
  Fuse fuse_81 (.A(fuse_81_a), .B(fuse_77_a));
  Fuse fuse_82 (.A(fuse_82_a), .B(fuse_78_a));
  Fuse fuse_83 (.A(fuse_83_a), .B(fuse_79_a));
  Fuse fuse_84 (.A(fuse_84_a), .B(fuse_80_a));
  Fuse fuse_85 (.A(fuse_85_a), .B(fuse_85_b));
  Fuse fuse_86 (.A(fuse_86_a), .B(fuse_86_b));
  Fuse fuse_87 (.A(fuse_87_a), .B(fuse_87_b));
  Fuse fuse_88 (.A(fuse_88_a), .B(fuse_88_b));
  Fuse fuse_89 (.A(fuse_85_a), .B(fuse_85_b));
  Fuse fuse_90 (.A(fuse_86_a), .B(fuse_86_b));
  Fuse fuse_91 (.A(fuse_87_a), .B(fuse_87_b));
  Fuse fuse_92 (.A(fuse_88_a), .B(fuse_88_b));
  Fuse fuse_93 (.A(fuse_93_a), .B(fuse_85_a));
  Fuse fuse_94 (.A(fuse_94_a), .B(fuse_86_a));
  Fuse fuse_95 (.A(fuse_95_a), .B(fuse_87_a));
  Fuse fuse_96 (.A(fuse_96_a), .B(fuse_88_a));
  Fuse fuse_97 (.A(fuse_97_a), .B(fuse_93_a));
  Fuse fuse_98 (.A(fuse_98_a), .B(fuse_94_a));
  Fuse fuse_99 (.A(fuse_99_a), .B(fuse_95_a));
  Fuse fuse_100 (.A(fuse_100_a), .B(fuse_96_a));
  Fuse fuse_101 (.A(fuse_101_a), .B(fuse_97_a));
  Fuse fuse_102 (.A(fuse_102_a), .B(fuse_98_a));
  Fuse fuse_103 (.A(fuse_103_a), .B(fuse_99_a));
  Fuse fuse_104 (.A(fuse_104_a), .B(fuse_100_a));
  Fuse fuse_105 (.A(fuse_105_a), .B(fuse_101_a));
  Fuse fuse_106 (.A(fuse_106_a), .B(fuse_102_a));
  Fuse fuse_107 (.A(fuse_107_a), .B(fuse_103_a));
  Fuse fuse_108 (.A(fuse_108_a), .B(fuse_104_a));
  Fuse fuse_109 (.A(fuse_109_a), .B(fuse_105_a));
  Fuse fuse_110 (.A(fuse_110_a), .B(fuse_106_a));
  Fuse fuse_111 (.A(fuse_111_a), .B(fuse_107_a));
  Fuse fuse_112 (.A(fuse_112_a), .B(fuse_108_a));
  _28c256_programmable ROM (
    .nCE(fuse_25_a), .nOE(_7404_1_pin12), .nWE(1'b1), .VCC(1'b1), .GND(1'b0), .I_O0(fuse_174_b),
    .I_O1(fuse_173_b), .I_O2(fuse_172_b), .I_O3(fuse_171_b), .I_O4(fuse_170_b), .I_O5(fuse_169_b),
    .I_O6(fuse_168_b), .I_O7(fuse_167_b), .A0(fuse_112_a), .A1(fuse_111_a), .A2(fuse_110_a), .A3(fuse_109_a),
    .A4(fuse_84_a), .A5(fuse_83_a), .A6(fuse_82_a), .A7(fuse_81_a), .A8(fuse_56_a), .A9(fuse_55_a),
    .A10(fuse_54_a), .A11(fuse_53_a), .A12(fuse_28_a), .A13(fuse_27_a), .A14(fuse_26_a));
  LY62256 RAM (
    .nCE(_7404_1_pin2), .nOE(_7404_1_pin12), .nWE(_7404_1_pin8), .VCC(1'b1), .GND(1'b0), .I_O0(fuse_174_b),
    .I_O1(fuse_173_b), .I_O2(fuse_172_b), .I_O3(fuse_171_b), .I_O4(fuse_170_b), .I_O5(fuse_169_b),
    .I_O6(fuse_168_b), .I_O7(fuse_167_b), .A0(fuse_112_a), .A1(fuse_111_a), .A2(fuse_110_a), .A3(fuse_109_a),
    .A4(fuse_84_a), .A5(fuse_83_a), .A6(fuse_82_a), .A7(fuse_81_a), .A8(fuse_56_a), .A9(fuse_55_a),
    .A10(fuse_54_a), .A11(fuse_53_a), .A12(fuse_28_a), .A13(fuse_27_a), .A14(fuse_26_a));
  _74541 _74541_1 (
    .pin1(_74541_1_pin1), .pin2(_74541_1_pin2), .pin3(_74541_1_pin3), .pin4(_74541_1_pin4),
    .pin5(_74541_1_pin5), .pin6(_74541_1_pin6), .pin7(_74541_1_pin7), .pin8(_74541_1_pin8),
    .pin9(_74541_1_pin9), .pin10(1'b0), .pin11(fuse_88_b), .pin12(fuse_87_b), .pin13(fuse_86_b),
    .pin14(fuse_85_b), .pin15(fuse_60_b), .pin16(fuse_59_b), .pin17(fuse_58_b), .pin18(fuse_57_b),
    .pin19(1'b0), .pin20(1'b1));
  _74541 _74541_2 (
    .pin1(_74541_1_pin1), .pin2(_74541_2_pin2), .pin3(_74541_2_pin3), .pin4(_74541_2_pin4),
    .pin5(_74541_2_pin5), .pin6(_74541_2_pin6), .pin7(_74541_2_pin7), .pin8(_74541_2_pin8),
    .pin9(_74541_2_pin9), .pin10(1'b0), .pin11(fuse_32_b), .pin12(fuse_31_b), .pin13(fuse_30_b),
    .pin14(fuse_29_b), .pin15(fuse_4_b), .pin16(fuse_3_b), .pin17(fuse_2_b), .pin18(fuse_1_b), .pin19(1'b0),
    .pin20(1'b1));
  _74574 _74574_1 (
    .pin1(_74574_1_pin1), .pin2(_74574_1_pin2), .pin3(_74574_1_pin3), .pin4(_74574_1_pin4),
    .pin5(_74574_1_pin5), .pin6(_74574_1_pin6), .pin7(_74574_1_pin7), .pin8(_74574_1_pin8),
    .pin9(_74574_1_pin9), .pin10(1'b0), .pin11(_74574_1_pin11), .pin12(fuse_88_a), .pin13(fuse_87_a),
    .pin14(fuse_86_a), .pin15(fuse_85_a), .pin16(fuse_60_a), .pin17(fuse_59_a), .pin18(fuse_58_a),
    .pin19(fuse_57_a), .pin20(1'b1));
  _74574 _74574_2 (
    .pin1(_74574_1_pin1), .pin2(_74574_2_pin2), .pin3(_74574_2_pin3), .pin4(_74574_2_pin4),
    .pin5(_74574_2_pin5), .pin6(_74574_2_pin6), .pin7(_74574_2_pin7), .pin8(_74574_2_pin8),
    .pin9(_74574_2_pin9), .pin10(1'b0), .pin11(_74574_1_pin11), .pin12(fuse_32_a), .pin13(fuse_31_a),
    .pin14(fuse_30_a), .pin15(fuse_29_a), .pin16(fuse_4_a), .pin17(fuse_3_a), .pin18(fuse_2_a),
    .pin19(fuse_1_a), .pin20(1'b1));
  _74574 _74574_3 (
    .pin1(_74574_3_pin1), .pin2(_74574_3_pin2), .pin3(_74574_3_pin3), .pin4(_74574_3_pin4),
    .pin5(_74574_3_pin5), .pin6(_74574_3_pin6), .pin7(_74574_3_pin7), .pin8(_74574_3_pin8),
    .pin9(_74574_3_pin9), .pin10(1'b0), .pin11(_74574_3_pin11), .pin12(fuse_96_a), .pin13(fuse_95_a),
    .pin14(fuse_94_a), .pin15(fuse_93_a), .pin16(fuse_68_a), .pin17(fuse_67_a), .pin18(fuse_66_a),
    .pin19(fuse_65_a), .pin20(1'b1));
  _74574 _74574_4 (
    .pin1(_74574_3_pin1), .pin2(_74574_4_pin2), .pin3(_74574_4_pin3), .pin4(_74574_4_pin4),
    .pin5(_74574_4_pin5), .pin6(_74574_4_pin6), .pin7(_74574_4_pin7), .pin8(_74574_4_pin8),
    .pin9(_74574_4_pin9), .pin10(1'b0), .pin11(_74574_3_pin11), .pin12(fuse_40_a), .pin13(fuse_39_a),
    .pin14(fuse_38_a), .pin15(fuse_37_a), .pin16(fuse_12_a), .pin17(fuse_11_a), .pin18(fuse_10_a),
    .pin19(fuse_9_a), .pin20(1'b1));
  _74574 _74574_5 (
    .pin1(_74574_5_pin1), .pin2(_74574_5_pin2), .pin3(_74574_5_pin3), .pin4(_74574_5_pin4),
    .pin5(_74574_5_pin5), .pin6(_74574_5_pin6), .pin7(_74574_5_pin7), .pin8(_74574_5_pin8),
    .pin9(_74574_5_pin9), .pin10(1'b0), .pin11(_74574_5_pin11), .pin12(fuse_100_a), .pin13(fuse_99_a),
    .pin14(fuse_98_a), .pin15(fuse_97_a), .pin16(fuse_72_a), .pin17(fuse_71_a), .pin18(fuse_70_a),
    .pin19(fuse_69_a), .pin20(1'b1));
  _74574 _74574_6 (
    .pin1(_74574_5_pin1), .pin2(_74574_6_pin2), .pin3(_74574_6_pin3), .pin4(_74574_6_pin4),
    .pin5(_74574_6_pin5), .pin6(_74574_6_pin6), .pin7(_74574_6_pin7), .pin8(_74574_6_pin8),
    .pin9(_74574_6_pin9), .pin10(1'b0), .pin11(_74574_5_pin11), .pin12(fuse_44_a), .pin13(fuse_43_a),
    .pin14(fuse_42_a), .pin15(fuse_41_a), .pin16(fuse_16_a), .pin17(fuse_15_a), .pin18(fuse_14_a),
    .pin19(fuse_13_a), .pin20(1'b1));
  _74574 _74574_7 (
    .pin1(_74574_7_pin1), .pin2(_74574_7_pin2), .pin3(_74574_7_pin3), .pin4(_74574_7_pin4),
    .pin5(_74574_7_pin5), .pin6(_74574_7_pin6), .pin7(_74574_7_pin7), .pin8(_74574_7_pin8),
    .pin9(_74574_7_pin9), .pin10(1'b0), .pin11(_74574_7_pin11), .pin12(fuse_104_a), .pin13(fuse_103_a),
    .pin14(fuse_102_a), .pin15(fuse_101_a), .pin16(fuse_76_a), .pin17(fuse_75_a), .pin18(fuse_74_a),
    .pin19(fuse_73_a), .pin20(1'b1));
  _74574 _74574_8 (
    .pin1(_74574_7_pin1), .pin2(_74574_8_pin2), .pin3(_74574_8_pin3), .pin4(_74574_8_pin4),
    .pin5(_74574_8_pin5), .pin6(_74574_8_pin6), .pin7(_74574_8_pin7), .pin8(_74574_8_pin8),
    .pin9(_74574_8_pin9), .pin10(1'b0), .pin11(_74574_7_pin11), .pin12(fuse_48_a), .pin13(fuse_47_a),
    .pin14(fuse_46_a), .pin15(fuse_45_a), .pin16(fuse_20_a), .pin17(fuse_19_a), .pin18(fuse_18_a),
    .pin19(fuse_17_a), .pin20(1'b1));
  _74574 _74574_9 (
    .pin1(_74574_9_pin1), .pin2(_74574_9_pin2), .pin3(_74574_9_pin3), .pin4(_74574_9_pin4),
    .pin5(_74574_9_pin5), .pin6(_74574_9_pin6), .pin7(_74574_9_pin7), .pin8(_74574_9_pin8),
    .pin9(_74574_9_pin9), .pin10(1'b0), .pin11(_74574_9_pin11), .pin12(fuse_108_a), .pin13(fuse_107_a),
    .pin14(fuse_106_a), .pin15(fuse_105_a), .pin16(fuse_80_a), .pin17(fuse_79_a), .pin18(fuse_78_a),
    .pin19(fuse_77_a), .pin20(1'b1));
  _74574 _74574_10 (
    .pin1(_74574_9_pin1), .pin2(_74574_10_pin2), .pin3(_74574_10_pin3), .pin4(_74574_10_pin4),
    .pin5(_74574_10_pin5), .pin6(_74574_10_pin6), .pin7(_74574_10_pin7), .pin8(_74574_10_pin8),
    .pin9(_74574_10_pin9), .pin10(1'b0), .pin11(_74574_9_pin11), .pin12(fuse_52_a), .pin13(fuse_51_a),
    .pin14(fuse_50_a), .pin15(fuse_49_a), .pin16(fuse_24_a), .pin17(fuse_23_a), .pin18(fuse_22_a),
    .pin19(fuse_21_a), .pin20(1'b1));
  _7408 _7408_1 (
    .pin1(_7408_1_pin1), .pin2(_7408_1_pin2), .pin3(_7408_1_pin3), .pin4(_7408_1_pin4), .pin5(_7408_1_pin2),
    .pin6(_7408_1_pin6), .pin7(1'b0), .pin8(_7408_1_pin8), .pin9(_7408_1_pin4), .pin10(_7408_1_pin4),
    .pin11(_7408_1_pin11), .pin12(_7408_1_pin1), .pin13(_7408_1_pin1), .pin14(1'b1));
  _74541 _74541_3 (
    .pin1(_74541_3_pin1), .pin2(_74541_1_pin9), .pin3(_74541_1_pin8), .pin4(_74541_1_pin7),
    .pin5(_74541_1_pin6), .pin6(_74541_1_pin5), .pin7(_74541_1_pin4), .pin8(_74541_1_pin3),
    .pin9(_74541_1_pin2), .pin10(1'b0), .pin11(_74541_3_pin11), .pin12(_74541_3_pin12),
    .pin13(_74541_3_pin13), .pin14(_74541_3_pin14), .pin15(_74541_3_pin15), .pin16(_74541_3_pin16),
    .pin17(_74541_3_pin17), .pin18(_74541_3_pin18), .pin19(1'b0), .pin20(1'b1));
  _74541 _74541_4 (
    .pin1(_74541_3_pin1), .pin2(_74541_2_pin9), .pin3(_74541_2_pin8), .pin4(_74541_2_pin7),
    .pin5(_74541_2_pin6), .pin6(_74541_2_pin5), .pin7(_74541_2_pin4), .pin8(_74541_2_pin3),
    .pin9(_74541_2_pin2), .pin10(1'b0), .pin11(_74541_4_pin11), .pin12(_74541_4_pin12),
    .pin13(_74541_4_pin13), .pin14(_74541_4_pin14), .pin15(_74541_4_pin15), .pin16(_74541_4_pin16),
    .pin17(_74541_4_pin17), .pin18(_74541_4_pin18), .pin19(1'b0), .pin20(1'b1));
  _74574 _74574_11 (
    .pin1(_74574_11_pin1), .pin2(_74574_1_pin9), .pin3(_74574_1_pin8), .pin4(_74574_1_pin7),
    .pin5(_74574_1_pin6), .pin6(_74574_1_pin5), .pin7(_74574_1_pin4), .pin8(_74574_1_pin3),
    .pin9(_74574_1_pin2), .pin10(1'b0), .pin11(_74574_1_pin11), .pin12(_74574_11_pin12),
    .pin13(_74574_11_pin13), .pin14(_74574_11_pin14), .pin15(_74574_11_pin15), .pin16(_74574_11_pin16),
    .pin17(_74574_11_pin17), .pin18(_74574_11_pin18), .pin19(_74574_11_pin19), .pin20(1'b1));
  _74193 _74193_1 (
    .pin1(_74574_11_pin18), .pin2(_74574_1_pin8), .pin3(_74574_1_pin9), .pin4(_74193_1_pin4),
    .pin5(_74193_1_pin5), .pin6(_74574_1_pin7), .pin7(_74574_1_pin6), .pin8(1'b0), .pin9(_74574_11_pin16),
    .pin10(_74574_11_pin17), .pin11(_74193_1_pin11), .pin12(_74193_1_pin12), .pin13(_74193_1_pin13),
    .pin14(_74193_1_pin14), .pin15(_74574_11_pin19), .pin16(1'b1));
  _74193 _74193_2 (
    .pin1(_74574_11_pin14), .pin2(_74574_1_pin4), .pin3(_74574_1_pin5), .pin4(_74193_1_pin13),
    .pin5(_74193_1_pin12), .pin6(_74574_1_pin3), .pin7(_74574_1_pin2), .pin8(1'b0), .pin9(_74574_11_pin12),
    .pin10(_74574_11_pin13), .pin11(_74193_1_pin11), .pin12(_74193_2_pin12), .pin13(_74193_2_pin13),
    .pin14(_74193_1_pin14), .pin15(_74574_11_pin15), .pin16(1'b1));
  _74574 _74574_12 (
    .pin1(_74574_11_pin1), .pin2(_74574_2_pin9), .pin3(_74574_2_pin8), .pin4(_74574_2_pin7),
    .pin5(_74574_2_pin6), .pin6(_74574_2_pin5), .pin7(_74574_2_pin4), .pin8(_74574_2_pin3),
    .pin9(_74574_2_pin2), .pin10(1'b0), .pin11(_74574_1_pin11), .pin12(_74574_12_pin12),
    .pin13(_74574_12_pin13), .pin14(_74574_12_pin14), .pin15(_74574_12_pin15), .pin16(_74574_12_pin16),
    .pin17(_74574_12_pin17), .pin18(_74574_12_pin18), .pin19(_74574_12_pin19), .pin20(1'b1));
  _74193 _74193_3 (
    .pin1(_74574_12_pin18), .pin2(_74574_2_pin8), .pin3(_74574_2_pin9), .pin4(_74193_2_pin13),
    .pin5(_74193_2_pin12), .pin6(_74574_2_pin7), .pin7(_74574_2_pin6), .pin8(1'b0), .pin9(_74574_12_pin16),
    .pin10(_74574_12_pin17), .pin11(_74193_1_pin11), .pin12(_74193_3_pin12), .pin13(_74193_3_pin13),
    .pin14(_74193_1_pin14), .pin15(_74574_12_pin19), .pin16(1'b1));
  _74193 _74193_4 (
    .pin1(_74574_12_pin14), .pin2(_74574_2_pin4), .pin3(_74574_2_pin5), .pin4(_74193_3_pin13),
    .pin5(_74193_3_pin12), .pin6(_74574_2_pin3), .pin7(_74574_2_pin2), .pin8(1'b0), .pin9(_74574_12_pin12),
    .pin10(_74574_12_pin13), .pin11(_74193_1_pin11), .pin14(_74193_1_pin14), .pin15(_74574_12_pin15),
    .pin16(1'b1));  // open: pin12, pin13
  _74574 _74574_13 (
    .pin1(_74574_13_pin1), .pin2(_74574_3_pin9), .pin3(_74574_3_pin8), .pin4(_74574_3_pin7),
    .pin5(_74574_3_pin6), .pin6(_74574_3_pin5), .pin7(_74574_3_pin4), .pin8(_74574_3_pin3),
    .pin9(_74574_3_pin2), .pin10(1'b0), .pin11(_74574_3_pin11), .pin12(_74574_13_pin12),
    .pin13(_74574_13_pin13), .pin14(_74574_13_pin14), .pin15(_74574_13_pin15), .pin16(_74574_13_pin16),
    .pin17(_74574_13_pin17), .pin18(_74574_13_pin18), .pin19(_74574_13_pin19), .pin20(1'b1));
  _74193 _74193_5 (
    .pin1(_74574_13_pin18), .pin2(_74574_3_pin8), .pin3(_74574_3_pin9), .pin4(_74193_5_pin4),
    .pin5(_74193_5_pin5), .pin6(_74574_3_pin7), .pin7(_74574_3_pin6), .pin8(1'b0), .pin9(_74574_13_pin16),
    .pin10(_74574_13_pin17), .pin11(_74193_5_pin11), .pin12(_74193_5_pin12), .pin13(_74193_5_pin13),
    .pin14(_74193_5_pin14), .pin15(_74574_13_pin19), .pin16(1'b1));
  _74193 _74193_6 (
    .pin1(_74574_13_pin14), .pin2(_74574_3_pin4), .pin3(_74574_3_pin5), .pin4(_74193_5_pin13),
    .pin5(_74193_5_pin12), .pin6(_74574_3_pin3), .pin7(_74574_3_pin2), .pin8(1'b0), .pin9(_74574_13_pin12),
    .pin10(_74574_13_pin13), .pin11(_74193_5_pin11), .pin12(_74193_6_pin12), .pin13(_74193_6_pin13),
    .pin14(_74193_5_pin14), .pin15(_74574_13_pin15), .pin16(1'b1));
  _74574 _74574_14 (
    .pin1(_74574_13_pin1), .pin2(_74574_4_pin9), .pin3(_74574_4_pin8), .pin4(_74574_4_pin7),
    .pin5(_74574_4_pin6), .pin6(_74574_4_pin5), .pin7(_74574_4_pin4), .pin8(_74574_4_pin3),
    .pin9(_74574_4_pin2), .pin10(1'b0), .pin11(_74574_3_pin11), .pin12(_74574_14_pin12),
    .pin13(_74574_14_pin13), .pin14(_74574_14_pin14), .pin15(_74574_14_pin15), .pin16(_74574_14_pin16),
    .pin17(_74574_14_pin17), .pin18(_74574_14_pin18), .pin19(_74574_14_pin19), .pin20(1'b1));
  _74193 _74193_7 (
    .pin1(_74574_14_pin18), .pin2(_74574_4_pin8), .pin3(_74574_4_pin9), .pin4(_74193_6_pin13),
    .pin5(_74193_6_pin12), .pin6(_74574_4_pin7), .pin7(_74574_4_pin6), .pin8(1'b0), .pin9(_74574_14_pin16),
    .pin10(_74574_14_pin17), .pin11(_74193_5_pin11), .pin12(_74193_7_pin12), .pin13(_74193_7_pin13),
    .pin14(_74193_5_pin14), .pin15(_74574_14_pin19), .pin16(1'b1));
  _74193 _74193_8 (
    .pin1(_74574_14_pin14), .pin2(_74574_4_pin4), .pin3(_74574_4_pin5), .pin4(_74193_7_pin13),
    .pin5(_74193_7_pin12), .pin6(_74574_4_pin3), .pin7(_74574_4_pin2), .pin8(1'b0), .pin9(_74574_14_pin12),
    .pin10(_74574_14_pin13), .pin11(_74193_5_pin11), .pin14(_74193_5_pin14), .pin15(_74574_14_pin15),
    .pin16(1'b1));  // open: pin12, pin13
  _74574 _74574_15 (
    .pin1(_74574_15_pin1), .pin2(_74574_5_pin9), .pin3(_74574_5_pin8), .pin4(_74574_5_pin7),
    .pin5(_74574_5_pin6), .pin6(_74574_5_pin5), .pin7(_74574_5_pin4), .pin8(_74574_5_pin3),
    .pin9(_74574_5_pin2), .pin10(1'b0), .pin11(_74574_5_pin11), .pin12(_74574_15_pin12),
    .pin13(_74574_15_pin13), .pin14(_74574_15_pin14), .pin15(_74574_15_pin15), .pin16(_74574_15_pin16),
    .pin17(_74574_15_pin17), .pin18(_74574_15_pin18), .pin19(_74574_15_pin19), .pin20(1'b1));
  _74193 _74193_9 (
    .pin1(_74574_15_pin18), .pin2(_74574_5_pin8), .pin3(_74574_5_pin9), .pin4(_74193_9_pin4),
    .pin5(_74193_9_pin5), .pin6(_74574_5_pin7), .pin7(_74574_5_pin6), .pin8(1'b0), .pin9(_74574_15_pin16),
    .pin10(_74574_15_pin17), .pin11(_74193_9_pin11), .pin12(_74193_9_pin12), .pin13(_74193_9_pin13),
    .pin14(_74193_9_pin14), .pin15(_74574_15_pin19), .pin16(1'b1));
  _74193 _74193_10 (
    .pin1(_74574_15_pin14), .pin2(_74574_5_pin4), .pin3(_74574_5_pin5), .pin4(_74193_9_pin13),
    .pin5(_74193_9_pin12), .pin6(_74574_5_pin3), .pin7(_74574_5_pin2), .pin8(1'b0), .pin9(_74574_15_pin12),
    .pin10(_74574_15_pin13), .pin11(_74193_9_pin11), .pin12(_74193_10_pin12), .pin13(_74193_10_pin13),
    .pin14(_74193_9_pin14), .pin15(_74574_15_pin15), .pin16(1'b1));
  _74574 _74574_16 (
    .pin1(_74574_15_pin1), .pin2(_74574_6_pin9), .pin3(_74574_6_pin8), .pin4(_74574_6_pin7),
    .pin5(_74574_6_pin6), .pin6(_74574_6_pin5), .pin7(_74574_6_pin4), .pin8(_74574_6_pin3),
    .pin9(_74574_6_pin2), .pin10(1'b0), .pin11(_74574_5_pin11), .pin12(_74574_16_pin12),
    .pin13(_74574_16_pin13), .pin14(_74574_16_pin14), .pin15(_74574_16_pin15), .pin16(_74574_16_pin16),
    .pin17(_74574_16_pin17), .pin18(_74574_16_pin18), .pin19(_74574_16_pin19), .pin20(1'b1));
  _74193 _74193_11 (
    .pin1(_74574_16_pin18), .pin2(_74574_6_pin8), .pin3(_74574_6_pin9), .pin4(_74193_10_pin13),
    .pin5(_74193_10_pin12), .pin6(_74574_6_pin7), .pin7(_74574_6_pin6), .pin8(1'b0), .pin9(_74574_16_pin16),
    .pin10(_74574_16_pin17), .pin11(_74193_9_pin11), .pin12(_74193_11_pin12), .pin13(_74193_11_pin13),
    .pin14(_74193_9_pin14), .pin15(_74574_16_pin19), .pin16(1'b1));
  _74193 _74193_12 (
    .pin1(_74574_16_pin14), .pin2(_74574_6_pin4), .pin3(_74574_6_pin5), .pin4(_74193_11_pin13),
    .pin5(_74193_11_pin12), .pin6(_74574_6_pin3), .pin7(_74574_6_pin2), .pin8(1'b0), .pin9(_74574_16_pin12),
    .pin10(_74574_16_pin13), .pin11(_74193_9_pin11), .pin14(_74193_9_pin14), .pin15(_74574_16_pin15),
    .pin16(1'b1));  // open: pin12, pin13
  _74574 _74574_17 (
    .pin1(_74574_17_pin1), .pin2(_74574_7_pin9), .pin3(_74574_7_pin8), .pin4(_74574_7_pin7),
    .pin5(_74574_7_pin6), .pin6(_74574_7_pin5), .pin7(_74574_7_pin4), .pin8(_74574_7_pin3),
    .pin9(_74574_7_pin2), .pin10(1'b0), .pin11(_74574_7_pin11), .pin12(_74574_17_pin12),
    .pin13(_74574_17_pin13), .pin14(_74574_17_pin14), .pin15(_74574_17_pin15), .pin16(_74574_17_pin16),
    .pin17(_74574_17_pin17), .pin18(_74574_17_pin18), .pin19(_74574_17_pin19), .pin20(1'b1));
  _74193 _74193_13 (
    .pin1(_74574_17_pin18), .pin2(_74574_7_pin8), .pin3(_74574_7_pin9), .pin4(_74193_13_pin4),
    .pin5(_74193_13_pin5), .pin6(_74574_7_pin7), .pin7(_74574_7_pin6), .pin8(1'b0), .pin9(_74574_17_pin16),
    .pin10(_74574_17_pin17), .pin11(_74193_13_pin11), .pin12(_74193_13_pin12), .pin13(_74193_13_pin13),
    .pin14(_74193_13_pin14), .pin15(_74574_17_pin19), .pin16(1'b1));
  _74193 _74193_14 (
    .pin1(_74574_17_pin14), .pin2(_74574_7_pin4), .pin3(_74574_7_pin5), .pin4(_74193_13_pin13),
    .pin5(_74193_13_pin12), .pin6(_74574_7_pin3), .pin7(_74574_7_pin2), .pin8(1'b0), .pin9(_74574_17_pin12),
    .pin10(_74574_17_pin13), .pin11(_74193_13_pin11), .pin12(_74193_14_pin12), .pin13(_74193_14_pin13),
    .pin14(_74193_13_pin14), .pin15(_74574_17_pin15), .pin16(1'b1));
  _74574 _74574_18 (
    .pin1(_74574_17_pin1), .pin2(_74574_8_pin9), .pin3(_74574_8_pin8), .pin4(_74574_8_pin7),
    .pin5(_74574_8_pin6), .pin6(_74574_8_pin5), .pin7(_74574_8_pin4), .pin8(_74574_8_pin3),
    .pin9(_74574_8_pin2), .pin10(1'b0), .pin11(_74574_7_pin11), .pin12(_74574_18_pin12),
    .pin13(_74574_18_pin13), .pin14(_74574_18_pin14), .pin15(_74574_18_pin15), .pin16(_74574_18_pin16),
    .pin17(_74574_18_pin17), .pin18(_74574_18_pin18), .pin19(_74574_18_pin19), .pin20(1'b1));
  _74193 _74193_15 (
    .pin1(_74574_18_pin18), .pin2(_74574_8_pin8), .pin3(_74574_8_pin9), .pin4(_74193_14_pin13),
    .pin5(_74193_14_pin12), .pin6(_74574_8_pin7), .pin7(_74574_8_pin6), .pin8(1'b0), .pin9(_74574_18_pin16),
    .pin10(_74574_18_pin17), .pin11(_74193_13_pin11), .pin12(_74193_15_pin12), .pin13(_74193_15_pin13),
    .pin14(_74193_13_pin14), .pin15(_74574_18_pin19), .pin16(1'b1));
  _74193 _74193_16 (
    .pin1(_74574_18_pin14), .pin2(_74574_8_pin4), .pin3(_74574_8_pin5), .pin4(_74193_15_pin13),
    .pin5(_74193_15_pin12), .pin6(_74574_8_pin3), .pin7(_74574_8_pin2), .pin8(1'b0), .pin9(_74574_18_pin12),
    .pin10(_74574_18_pin13), .pin11(_74193_13_pin11), .pin14(_74193_13_pin14), .pin15(_74574_18_pin15),
    .pin16(1'b1));  // open: pin12, pin13
  _74574 _74574_19 (
    .pin1(_74574_19_pin1), .pin2(_74574_9_pin9), .pin3(_74574_9_pin8), .pin4(_74574_9_pin7),
    .pin5(_74574_9_pin6), .pin6(_74574_9_pin5), .pin7(_74574_9_pin4), .pin8(_74574_9_pin3),
    .pin9(_74574_9_pin2), .pin10(1'b0), .pin11(_74574_9_pin11), .pin12(_74574_19_pin12),
    .pin13(_74574_19_pin13), .pin14(_74574_19_pin14), .pin15(_74574_19_pin15), .pin16(_74574_19_pin16),
    .pin17(_74574_19_pin17), .pin18(_74574_19_pin18), .pin19(_74574_19_pin19), .pin20(1'b1));
  _74193 _74193_17 (
    .pin1(_74574_19_pin18), .pin2(_74574_9_pin8), .pin3(_74574_9_pin9), .pin4(_74193_17_pin4),
    .pin5(_74193_17_pin5), .pin6(_74574_9_pin7), .pin7(_74574_9_pin6), .pin8(1'b0), .pin9(_74574_19_pin16),
    .pin10(_74574_19_pin17), .pin11(_74193_17_pin11), .pin12(_74193_17_pin12), .pin13(_74193_17_pin13),
    .pin14(_74193_17_pin14), .pin15(_74574_19_pin19), .pin16(1'b1));
  _74193 _74193_18 (
    .pin1(_74574_19_pin14), .pin2(_74574_9_pin4), .pin3(_74574_9_pin5), .pin4(_74193_17_pin13),
    .pin5(_74193_17_pin12), .pin6(_74574_9_pin3), .pin7(_74574_9_pin2), .pin8(1'b0), .pin9(_74574_19_pin12),
    .pin10(_74574_19_pin13), .pin11(_74193_17_pin11), .pin12(_74193_18_pin12), .pin13(_74193_18_pin13),
    .pin14(_74193_17_pin14), .pin15(_74574_19_pin15), .pin16(1'b1));
  _74574 _74574_20 (
    .pin1(_74574_19_pin1), .pin2(_74574_10_pin9), .pin3(_74574_10_pin8), .pin4(_74574_10_pin7),
    .pin5(_74574_10_pin6), .pin6(_74574_10_pin5), .pin7(_74574_10_pin4), .pin8(_74574_10_pin3),
    .pin9(_74574_10_pin2), .pin10(1'b0), .pin11(_74574_9_pin11), .pin12(_74574_20_pin12),
    .pin13(_74574_20_pin13), .pin14(_74574_20_pin14), .pin15(_74574_20_pin15), .pin16(_74574_20_pin16),
    .pin17(_74574_20_pin17), .pin18(_74574_20_pin18), .pin19(_74574_20_pin19), .pin20(1'b1));
  _74193 _74193_19 (
    .pin1(_74574_20_pin18), .pin2(_74574_10_pin8), .pin3(_74574_10_pin9), .pin4(_74193_18_pin13),
    .pin5(_74193_18_pin12), .pin6(_74574_10_pin7), .pin7(_74574_10_pin6), .pin8(1'b0),
    .pin9(_74574_20_pin16), .pin10(_74574_20_pin17), .pin11(_74193_17_pin11), .pin12(_74193_19_pin12),
    .pin13(_74193_19_pin13), .pin14(_74193_17_pin14), .pin15(_74574_20_pin19), .pin16(1'b1));
  _74193 _74193_20 (
    .pin1(_74574_20_pin14), .pin2(_74574_10_pin4), .pin3(_74574_10_pin5), .pin4(_74193_19_pin13),
    .pin5(_74193_19_pin12), .pin6(_74574_10_pin3), .pin7(_74574_10_pin2), .pin8(1'b0),
    .pin9(_74574_20_pin12), .pin10(_74574_20_pin13), .pin11(_74193_17_pin11), .pin14(_74193_17_pin14),
    .pin15(_74574_20_pin15), .pin16(1'b1));  // open: pin12, pin13
  Fuse fuse_113 (.A(_74574_12_pin12), .B(_74541_4_pin11));
  Fuse fuse_114 (.A(_74574_12_pin12), .B(_74541_4_pin11));
  Fuse fuse_115 (.A(_74574_14_pin12), .B(_74574_12_pin12));
  Fuse fuse_116 (.A(_74574_16_pin12), .B(_74574_14_pin12));
  Fuse fuse_117 (.A(_74574_18_pin12), .B(_74574_16_pin12));
  Fuse fuse_118 (.A(_74574_20_pin12), .B(_74574_18_pin12));
  Fuse fuse_119 (.A(_74574_12_pin13), .B(_74541_4_pin12));
  Fuse fuse_120 (.A(_74574_12_pin14), .B(_74541_4_pin13));
  Fuse fuse_121 (.A(_74574_12_pin15), .B(_74541_4_pin14));
  Fuse fuse_122 (.A(_74574_12_pin16), .B(_74541_4_pin15));
  Fuse fuse_123 (.A(_74574_12_pin13), .B(_74541_4_pin12));
  Fuse fuse_124 (.A(_74574_12_pin14), .B(_74541_4_pin13));
  Fuse fuse_125 (.A(_74574_12_pin15), .B(_74541_4_pin14));
  Fuse fuse_126 (.A(_74574_12_pin16), .B(_74541_4_pin15));
  Fuse fuse_127 (.A(_74574_14_pin13), .B(_74574_12_pin13));
  Fuse fuse_128 (.A(_74574_14_pin14), .B(_74574_12_pin14));
  Fuse fuse_129 (.A(_74574_14_pin15), .B(_74574_12_pin15));
  Fuse fuse_130 (.A(_74574_14_pin16), .B(_74574_12_pin16));
  Fuse fuse_131 (.A(_74574_16_pin13), .B(_74574_14_pin13));
  Fuse fuse_132 (.A(_74574_16_pin14), .B(_74574_14_pin14));
  Fuse fuse_133 (.A(_74574_16_pin15), .B(_74574_14_pin15));
  Fuse fuse_134 (.A(_74574_16_pin16), .B(_74574_14_pin16));
  Fuse fuse_135 (.A(_74574_18_pin13), .B(_74574_16_pin13));
  Fuse fuse_136 (.A(_74574_18_pin14), .B(_74574_16_pin14));
  Fuse fuse_137 (.A(_74574_18_pin15), .B(_74574_16_pin15));
  Fuse fuse_138 (.A(_74574_18_pin16), .B(_74574_16_pin16));
  Fuse fuse_139 (.A(_74574_20_pin13), .B(_74574_18_pin13));
  Fuse fuse_140 (.A(_74574_20_pin14), .B(_74574_18_pin14));
  Fuse fuse_141 (.A(_74574_20_pin15), .B(_74574_18_pin15));
  Fuse fuse_142 (.A(_74574_20_pin16), .B(_74574_18_pin16));
  Fuse fuse_143 (.A(_74574_12_pin17), .B(_74541_4_pin16));
  Fuse fuse_144 (.A(_74574_12_pin18), .B(_74541_4_pin17));
  Fuse fuse_145 (.A(_74574_12_pin19), .B(_74541_4_pin18));
  Fuse fuse_146 (.A(_74574_11_pin12), .B(_74541_3_pin11));
  Fuse fuse_147 (.A(_74574_12_pin17), .B(_74541_4_pin16));
  Fuse fuse_148 (.A(_74574_12_pin18), .B(_74541_4_pin17));
  Fuse fuse_149 (.A(_74574_12_pin19), .B(_74541_4_pin18));
  Fuse fuse_150 (.A(_74574_11_pin12), .B(_74541_3_pin11));
  Fuse fuse_151 (.A(_74574_14_pin17), .B(_74574_12_pin17));
  Fuse fuse_152 (.A(_74574_14_pin18), .B(_74574_12_pin18));
  Fuse fuse_153 (.A(_74574_14_pin19), .B(_74574_12_pin19));
  Fuse fuse_154 (.A(_74574_13_pin12), .B(_74574_11_pin12));
  Fuse fuse_155 (.A(_74574_16_pin17), .B(_74574_14_pin17));
  Fuse fuse_156 (.A(_74574_16_pin18), .B(_74574_14_pin18));
  Fuse fuse_157 (.A(_74574_16_pin19), .B(_74574_14_pin19));
  Fuse fuse_158 (.A(_74574_15_pin12), .B(_74574_13_pin12));
  Fuse fuse_159 (.A(_74574_18_pin17), .B(_74574_16_pin17));
  Fuse fuse_160 (.A(_74574_18_pin18), .B(_74574_16_pin18));
  Fuse fuse_161 (.A(_74574_18_pin19), .B(_74574_16_pin19));
  Fuse fuse_162 (.A(_74574_17_pin12), .B(_74574_15_pin12));
  Fuse fuse_163 (.A(_74574_20_pin17), .B(_74574_18_pin17));
  Fuse fuse_164 (.A(_74574_20_pin18), .B(_74574_18_pin18));
  Fuse fuse_165 (.A(_74574_20_pin19), .B(_74574_18_pin19));
  Fuse fuse_166 (.A(_74574_19_pin12), .B(_74574_17_pin12));
  Fuse fuse_167 (.A(fuse_167_a), .B(fuse_167_b));
  Fuse fuse_168 (.A(fuse_168_a), .B(fuse_168_b));
  Fuse fuse_169 (.A(fuse_169_a), .B(fuse_169_b));
  Fuse fuse_170 (.A(fuse_170_a), .B(fuse_170_b));
  Fuse fuse_171 (.A(fuse_171_a), .B(fuse_171_b));
  Fuse fuse_172 (.A(fuse_172_a), .B(fuse_172_b));
  Fuse fuse_173 (.A(fuse_173_a), .B(fuse_173_b));
  Fuse fuse_174 (.A(fuse_174_a), .B(fuse_174_b));
  Fuse fuse_175 (.A(_74574_11_pin13), .B(_74541_3_pin12));
  Fuse fuse_176 (.A(_74574_11_pin14), .B(_74541_3_pin13));
  Fuse fuse_177 (.A(_74574_11_pin15), .B(_74541_3_pin14));
  Fuse fuse_178 (.A(_74574_11_pin16), .B(_74541_3_pin15));
  Fuse fuse_179 (.A(_74574_11_pin13), .B(_74541_3_pin12));
  Fuse fuse_180 (.A(_74574_11_pin14), .B(_74541_3_pin13));
  Fuse fuse_181 (.A(_74574_11_pin15), .B(_74541_3_pin14));
  Fuse fuse_182 (.A(_74574_11_pin16), .B(_74541_3_pin15));
  Fuse fuse_183 (.A(_74574_13_pin13), .B(_74574_11_pin13));
  Fuse fuse_184 (.A(_74574_13_pin14), .B(_74574_11_pin14));
  Fuse fuse_185 (.A(_74574_13_pin15), .B(_74574_11_pin15));
  Fuse fuse_186 (.A(_74574_13_pin16), .B(_74574_11_pin16));
  Fuse fuse_187 (.A(_74574_15_pin13), .B(_74574_13_pin13));
  Fuse fuse_188 (.A(_74574_15_pin14), .B(_74574_13_pin14));
  Fuse fuse_189 (.A(_74574_15_pin15), .B(_74574_13_pin15));
  Fuse fuse_190 (.A(_74574_15_pin16), .B(_74574_13_pin16));
  Fuse fuse_191 (.A(_74574_17_pin13), .B(_74574_15_pin13));
  Fuse fuse_192 (.A(_74574_17_pin14), .B(_74574_15_pin14));
  Fuse fuse_193 (.A(_74574_17_pin15), .B(_74574_15_pin15));
  Fuse fuse_194 (.A(_74574_17_pin16), .B(_74574_15_pin16));
  Fuse fuse_195 (.A(_74574_19_pin13), .B(_74574_17_pin13));
  Fuse fuse_196 (.A(_74574_19_pin14), .B(_74574_17_pin14));
  Fuse fuse_197 (.A(_74574_19_pin15), .B(_74574_17_pin15));
  Fuse fuse_198 (.A(_74574_19_pin16), .B(_74574_17_pin16));
  _7404 _7404_1 (
    .pin1(fuse_25_a), .pin2(_7404_1_pin2), .pin3(_7404_1_pin3), .pin4(_7404_1_pin4), .pin5(_7404_1_pin5),
    .pin6(_7404_1_pin6), .pin7(1'b0), .pin8(_7404_1_pin8), .pin9(_7404_1_pin6), .pin10(_7404_1_pin5),
    .pin11(_7404_1_pin4), .pin12(_7404_1_pin12), .pin13(_7404_1_pin13), .pin14(1'b1));
  Fuse fuse_199 (.A(_74574_11_pin17), .B(_74541_3_pin16));
  Fuse fuse_200 (.A(_74574_11_pin18), .B(_74541_3_pin17));
  Fuse fuse_201 (.A(_74574_11_pin19), .B(_74541_3_pin18));
  Fuse fuse_202 (.A(_74574_11_pin17), .B(_74541_3_pin16));
  Fuse fuse_203 (.A(_74574_11_pin18), .B(_74541_3_pin17));
  Fuse fuse_204 (.A(_74574_11_pin19), .B(_74541_3_pin18));
  Fuse fuse_205 (.A(_74574_13_pin17), .B(_74574_11_pin17));
  Fuse fuse_206 (.A(_74574_13_pin18), .B(_74574_11_pin18));
  Fuse fuse_207 (.A(_74574_13_pin19), .B(_74574_11_pin19));
  Fuse fuse_208 (.A(_74574_15_pin17), .B(_74574_13_pin17));
  Fuse fuse_209 (.A(_74574_15_pin18), .B(_74574_13_pin18));
  Fuse fuse_210 (.A(_74574_15_pin19), .B(_74574_13_pin19));
  Fuse fuse_211 (.A(_74574_17_pin17), .B(_74574_15_pin17));
  Fuse fuse_212 (.A(_74574_17_pin18), .B(_74574_15_pin18));
  Fuse fuse_213 (.A(_74574_17_pin19), .B(_74574_15_pin19));
  Fuse fuse_214 (.A(_74574_19_pin17), .B(_74574_17_pin17));
  Fuse fuse_215 (.A(_74574_19_pin18), .B(_74574_17_pin18));
  Fuse fuse_216 (.A(_74574_19_pin19), .B(_74574_17_pin19));
  Fuse fuse_217 (.A(fuse_217_a), .B(_7408_1_pin2));
  Fuse fuse_218 (.A(fuse_218_a), .B(_74541_1_pin1));
  Fuse fuse_219 (.A(fuse_217_a), .B(_7408_1_pin2));
  Fuse fuse_220 (.A(fuse_218_a), .B(_74541_1_pin1));
  Fuse fuse_221 (.A(_74193_1_pin5), .B(fuse_221_b));
  Fuse fuse_222 (.A(_74193_1_pin4), .B(fuse_222_b));
  Fuse fuse_223 (.A(_74193_1_pin11), .B(fuse_223_b));
  Fuse fuse_224 (.A(_74574_1_pin11), .B(clk));
  Fuse fuse_225 (.A(_74193_1_pin14), .B(fuse_225_b));
  Fuse fuse_226 (.A(_74574_11_pin1), .B(fuse_226_b));
  Fuse fuse_227 (.A(_74574_1_pin1), .B(fuse_227_b));
  Fuse fuse_228 (.A(_74193_5_pin5), .B(fuse_228_b));
  Fuse fuse_229 (.A(_74193_5_pin4), .B(fuse_229_b));
  Fuse fuse_230 (.A(_74193_5_pin11), .B(fuse_230_b));
  Fuse fuse_231 (.A(_74574_3_pin11), .B(clk));
  Fuse fuse_232 (.A(_74193_5_pin14), .B(fuse_225_b));
  Fuse fuse_233 (.A(_74574_13_pin1), .B(fuse_233_b));
  Fuse fuse_234 (.A(_74574_3_pin1), .B(fuse_234_b));
  Fuse fuse_235 (.A(_74193_9_pin5), .B(fuse_235_b));
  Fuse fuse_236 (.A(_74193_9_pin4), .B(fuse_236_b));
  Fuse fuse_237 (.A(_74193_9_pin11), .B(fuse_237_b));
  Fuse fuse_238 (.A(_74574_5_pin11), .B(clk));
  Fuse fuse_239 (.A(_74193_9_pin14), .B(fuse_225_b));
  Fuse fuse_240 (.A(_74574_15_pin1), .B(fuse_240_b));
  Fuse fuse_241 (.A(_74574_5_pin1), .B(fuse_241_b));
  Fuse fuse_242 (.A(_74193_13_pin5), .B(fuse_242_b));
  Fuse fuse_243 (.A(_74193_13_pin4), .B(fuse_243_b));
  Fuse fuse_244 (.A(_74193_13_pin11), .B(fuse_244_b));
  Fuse fuse_245 (.A(_74574_7_pin11), .B(clk));
  Fuse fuse_246 (.A(_74193_13_pin14), .B(fuse_225_b));
  Fuse fuse_247 (.A(_74574_17_pin1), .B(fuse_247_b));
  Fuse fuse_248 (.A(_74574_7_pin1), .B(fuse_248_b));
  Fuse fuse_249 (.A(_74193_17_pin5), .B(fuse_249_b));
  Fuse fuse_250 (.A(_74193_17_pin4), .B(fuse_250_b));
  Fuse fuse_251 (.A(_74193_17_pin11), .B(fuse_251_b));
  Fuse fuse_252 (.A(_74574_9_pin11), .B(clk));
  Fuse fuse_253 (.A(_74193_17_pin14), .B(fuse_225_b));
  Fuse fuse_254 (.A(_74574_19_pin1), .B(fuse_254_b));
  Fuse fuse_255 (.A(_74574_9_pin1), .B(fuse_255_b));
  _74574 _74574_21 (
    .pin1(1'b0), .pin2(fuse_174_a), .pin3(fuse_173_a), .pin4(fuse_172_a), .pin5(fuse_171_a),
    .pin6(fuse_170_a), .pin7(fuse_169_a), .pin8(fuse_168_a), .pin9(fuse_167_a), .pin10(1'b0), .pin11(clk),
    .pin12(_74574_21_pin12), .pin13(_74574_21_pin13), .pin14(_74574_21_pin14), .pin15(_74574_21_pin15),
    .pin16(_74574_21_pin16), .pin17(_74574_21_pin17), .pin18(_74574_21_pin18), .pin19(_74574_21_pin19),
    .pin20(1'b1));
  Fuse fuse_256 (.A(fuse_256_a), .B(_74541_3_pin1));
  Fuse fuse_257 (.A(fuse_257_a), .B(fuse_257_b));
  Fuse fuse_258 (.A(fuse_258_a), .B(_7408_1_pin1));
  Fuse fuse_259 (.A(fuse_256_a), .B(_74541_3_pin1));
  Fuse fuse_260 (.A(fuse_257_a), .B(fuse_257_b));
  Fuse fuse_261 (.A(fuse_258_a), .B(_7408_1_pin1));
  Fuse fuse_262 (.A(fuse_262_a), .B(fuse_262_b));
  Fuse fuse_263 (.A(fuse_262_a), .B(fuse_262_b));
  _74138 _74138_1 (
    .pin1(_74138_1_pin1), .pin2(_74138_1_pin2), .pin3(_74138_1_pin3), .pin4(_74138_1_pin4),
    .pin5(_74138_1_pin5), .pin6(1'b1), .pin8(1'b0), .pin9(fuse_217_a), .pin10(fuse_251_b),
    .pin11(fuse_244_b), .pin12(fuse_237_b), .pin13(fuse_230_b), .pin14(fuse_223_b), .pin16(1'b1));  // open: pin7, pin15
  _74138 _74138_2 (
    .pin1(_74138_1_pin1), .pin2(_74138_1_pin2), .pin3(_74138_1_pin3), .pin4(1'b0), .pin5(_74138_1_pin5),
    .pin6(_74138_1_pin4), .pin8(1'b0), .pin10(fuse_250_b), .pin11(fuse_243_b), .pin12(fuse_236_b),
    .pin13(fuse_229_b), .pin14(fuse_222_b), .pin15(_74138_2_pin15), .pin16(1'b1));  // open: pin7, pin9
  Button Reset (.out(fuse_225_b));
  _74157 _74157_1 (
    .pin1(_7408_1_pin11), .pin2(_74157_3_pin14[2]), .pin3(_74541_3_pin16), .pin4(_74157_1_pin4),
    .pin5(_74157_3_pin14[3]), .pin6(_74541_3_pin15), .pin7(_74157_1_pin7), .pin8(1'b0), .pin9(_74157_1_pin9),
    .pin10(_74541_3_pin17), .pin11(_74157_3_pin14[1]), .pin12(_74157_1_pin12), .pin13(_74541_3_pin18),
    .pin14(_74157_3_pin14[0]), .pin15(1'b0), .pin16(1'b1));
  _74157 _74157_2 (
    .pin1(_7408_1_pin8), .pin2(_74157_3_pin14[2]), .pin3(_74541_4_pin16), .pin4(_74157_2_pin4),
    .pin5(_74157_3_pin14[3]), .pin6(_74541_4_pin15), .pin7(_74157_2_pin7), .pin8(1'b0), .pin9(_74157_2_pin9),
    .pin10(_74541_4_pin17), .pin11(_74157_3_pin14[1]), .pin12(_74157_2_pin12), .pin13(_74541_4_pin18),
    .pin14(_74157_3_pin14[0]), .pin15(1'b0), .pin16(1'b1));
  Fuse fuse_264 (.A(fuse_264_a), .B(_7408_1_pin4));
  Fuse fuse_265 (.A(fuse_264_a), .B(_7408_1_pin4));
  _74153 _74153_1 (
    .pin1(1'b0), .pin2(_74153_1_pin2), .pin3(_74574_21_pin18), .pin4(1'b0), .pin5(1'b0), .pin6(fuse_173_a),
    .pin7(_74153_1_pin7), .pin8(1'b0), .pin9(_74153_1_pin9), .pin10(fuse_174_a), .pin11(1'b0), .pin12(1'b0),
    .pin13(_74574_21_pin19), .pin14(_74153_1_pin14), .pin15(1'b0), .pin16(1'b1));
  _74153 _74153_2 (
    .pin1(1'b0), .pin2(_74153_1_pin2), .pin3(_74574_21_pin16), .pin4(1'b0), .pin5(1'b0), .pin6(fuse_171_a),
    .pin7(_74153_2_pin7), .pin8(1'b0), .pin9(_74153_2_pin9), .pin10(fuse_172_a), .pin11(1'b0), .pin12(1'b0),
    .pin13(_74574_21_pin17), .pin14(_74153_1_pin14), .pin15(1'b0), .pin16(1'b1));
  _74153 _74153_3 (
    .pin1(1'b0), .pin2(_74153_1_pin2), .pin3(_74574_21_pin14), .pin4(1'b0), .pin5(1'b0), .pin6(fuse_169_a),
    .pin7(_74153_3_pin7), .pin8(1'b0), .pin9(_74153_3_pin9), .pin10(fuse_170_a), .pin11(1'b0), .pin12(1'b0),
    .pin13(_74574_21_pin15), .pin14(_74153_1_pin14), .pin15(1'b0), .pin16(1'b1));
  _74153 _74153_4 (
    .pin1(1'b0), .pin2(_74153_1_pin2), .pin3(_74574_21_pin12), .pin4(1'b0), .pin5(1'b0), .pin6(fuse_167_a),
    .pin7(_74153_4_pin7), .pin8(1'b0), .pin9(_74153_4_pin9), .pin10(fuse_168_a), .pin11(1'b0), .pin12(1'b0),
    .pin13(_74574_21_pin13), .pin14(_74153_1_pin14), .pin15(1'b0), .pin16(1'b1));
  _74157 _74157_3 (
    .pin1(_7408_1_pin11), .pin2(_74157_3_pin14[6]), .pin3(_74541_3_pin12), .pin4(_74157_3_pin4),
    .pin5(_74157_3_pin14[7]), .pin6(_74541_3_pin11), .pin7(_74157_3_pin7), .pin8(1'b0), .pin9(_74157_3_pin9),
    .pin10(_74541_3_pin13), .pin11(_74157_3_pin14[5]), .pin12(_74157_3_pin12), .pin13(_74541_3_pin14),
    .pin14(_74157_3_pin14[4]), .pin15(1'b0), .pin16(1'b1));
  _74157 _74157_4 (
    .pin1(_7408_1_pin8), .pin2(_74157_3_pin14[6]), .pin3(_74541_4_pin12), .pin4(_74157_4_pin4),
    .pin5(_74157_3_pin14[7]), .pin6(_74541_4_pin11), .pin7(_74157_4_pin7), .pin8(1'b0), .pin9(_74157_4_pin9),
    .pin10(_74541_4_pin13), .pin11(_74157_3_pin14[5]), .pin12(_74157_4_pin12), .pin13(_74541_4_pin14),
    .pin14(_74157_3_pin14[4]), .pin15(1'b0), .pin16(1'b1));
  not not_1 (_74138_1_pin5, clk);
  _7404 _7404_2 (
    .pin1(1'b0), .pin3(_7404_2_pin3), .pin4(_7404_2_pin4), .pin5(_7404_2_pin5), .pin6(_7404_2_pin6),
    .pin7(1'b0), .pin9(1'b0), .pin10(_7404_2_pin5), .pin11(_74153_1_pin14), .pin12(_7404_2_pin3),
    .pin13(_7404_2_pin13), .pin14(1'b1));  // open: pin2, pin8
  _74139 _74139_1 (
    .pin1(_74138_1_pin5), .pin2(_74139_1_pin2), .pin3(_74139_1_pin3), .pin4(fuse_221_b), .pin5(fuse_228_b),
    .pin8(1'b0), .pin9(fuse_249_b), .pin10(fuse_242_b), .pin11(fuse_235_b), .pin13(_74139_1_pin13),
    .pin14(_74139_1_pin14), .pin15(_74138_1_pin5), .pin16(1'b1));  // open: pin6, pin7, pin12
  Fuse fuse_266 (.A(_7404_2_pin6), .B(_74139_1_pin3));
  Fuse fuse_267 (.A(_7404_2_pin4), .B(_74139_1_pin2));
  _7400 _7400_1 (
    .pin1(_74153_1_pin2), .pin2(_74153_1_pin14), .pin3(_7400_1_pin3), .pin4(1'b0), .pin5(1'b0), .pin7(1'b0),
    .pin8(1'b0), .pin9(_74153_1_pin14), .pin10(_74574_21_pin19), .pin11(1'b0), .pin12(1'b0),
    .pin13(fuse_174_a), .pin14(_74153_1_pin9));  // open: pin6
  _74138 _74138_3 (
    .pin1(_74138_3_pin1), .pin2(_74138_3_pin2), .pin3(_74138_3_pin3), .pin4(1'b0), .pin5(1'b0), .pin6(1'b1),
    .pin7(fuse_256_a), .pin8(1'b0), .pin10(fuse_254_b), .pin11(fuse_247_b), .pin12(fuse_240_b),
    .pin13(fuse_233_b), .pin14(fuse_226_b), .pin16(1'b1));  // open: pin9, pin15
  _74138 _74138_4 (
    .pin1(_74138_4_pin1), .pin2(_74138_4_pin2), .pin3(_74138_4_pin3), .pin4(1'b0), .pin5(1'b0), .pin6(1'b1),
    .pin8(1'b0), .pin9(fuse_218_a), .pin10(fuse_255_b), .pin11(fuse_248_b), .pin12(fuse_241_b),
    .pin13(fuse_234_b), .pin14(fuse_227_b), .pin16(1'b1));  // open: pin7, pin15
  _74574 _74574_22 (
    .pin1(1'b0), .pin2(_74574_22_pin2), .pin3(_74574_22_pin3), .pin4(_74574_22_pin4), .pin5(_74574_22_pin5),
    .pin6(_74574_22_pin6), .pin7(_74574_22_pin7), .pin8(_74574_22_pin8), .pin9(_74574_22_pin9), .pin10(1'b0),
    .pin11(clk), .pin12(_74574_22_pin12), .pin13(_74574_22_pin13), .pin14(_74574_22_pin14),
    .pin15(_74574_22_pin15), .pin16(_74574_22_pin16), .pin17(_74574_22_pin17), .pin18(_74574_22_pin18),
    .pin19(_74153_1_pin2), .pin20(1'b1));
  _74574 _74574_23 (
    .pin1(1'b0), .pin2(_74574_23_pin2), .pin3(_74574_23_pin3), .pin4(_74574_23_pin4), .pin5(_74574_23_pin5),
    .pin6(_74574_23_pin6), .pin7(_74574_23_pin7), .pin8(_74574_23_pin8), .pin9(_74574_23_pin9), .pin10(1'b0),
    .pin11(clk), .pin12(_74574_23_pin12), .pin13(_74574_23_pin13), .pin14(_74574_23_pin14),
    .pin15(_74574_23_pin15), .pin16(_74574_23_pin16), .pin17(_74574_23_pin17), .pin18(_74574_23_pin18),
    .pin19(_74574_23_pin19), .pin20(1'b1));
  _74574 _74574_24 (
    .pin1(1'b0), .pin2(_74157_1_pin12), .pin3(_74157_1_pin9), .pin4(_74157_1_pin4), .pin5(_74157_1_pin7),
    .pin6(_74157_3_pin12), .pin7(_74157_3_pin9), .pin8(_74157_3_pin4), .pin9(_74157_3_pin7), .pin10(1'b0),
    .pin11(_7408_1_pin3), .pin12(_74541_1_pin2), .pin13(_74541_1_pin3), .pin14(_74541_1_pin4),
    .pin15(_74541_1_pin5), .pin16(_74541_1_pin6), .pin17(_74541_1_pin7), .pin18(_74541_1_pin8),
    .pin19(_74541_1_pin9), .pin20(1'b1));
  _74574 _74574_25 (
    .pin1(1'b0), .pin2(_74157_2_pin12), .pin3(_74157_2_pin9), .pin4(_74157_2_pin4), .pin5(_74157_2_pin7),
    .pin6(_74157_4_pin12), .pin7(_74157_4_pin9), .pin8(_74157_4_pin4), .pin9(_74157_4_pin7), .pin10(1'b0),
    .pin11(_7408_1_pin6), .pin12(_74541_2_pin2), .pin13(_74541_2_pin3), .pin14(_74541_2_pin4),
    .pin15(_74541_2_pin5), .pin16(_74541_2_pin6), .pin17(_74541_2_pin7), .pin18(_74541_2_pin8),
    .pin19(_74541_2_pin9), .pin20(1'b1));
  Fuse fuse_268 (.A(_74574_23_pin19), .B(_74138_3_pin3));
  Fuse fuse_269 (.A(_74574_22_pin18), .B(_74138_3_pin2));
  Fuse fuse_270 (.A(_74574_23_pin18), .B(_74138_3_pin1));
  Fuse fuse_271 (.A(_74574_22_pin17), .B(_74138_1_pin4));
  Fuse fuse_272 (.A(_74574_23_pin17), .B(_74138_1_pin3));
  Fuse fuse_273 (.A(_74574_22_pin16), .B(_74138_1_pin2));
  Fuse fuse_274 (.A(_74574_23_pin16), .B(_74138_1_pin1));
  Fuse fuse_275 (.A(_74574_22_pin15), .B(fuse_275_b));
  _28c256_programmable _1B (
    .nCE(1'b0), .nOE(1'b0), .nWE(1'b1), .VCC(1'b1), .GND(1'b0), .I_O0(_74574_23_pin5), .I_O1(_74574_22_pin5),
    .I_O2(_74574_23_pin4), .I_O3(_74574_22_pin4), .I_O4(_74574_23_pin3), .I_O5(_74574_22_pin3),
    .I_O6(_74574_23_pin2), .I_O7(_74574_22_pin2), .A0(_74153_1_pin9), .A1(_74153_1_pin7), .A2(_74153_2_pin9),
    .A3(_74153_2_pin7), .A4(_74153_3_pin9), .A5(_74153_3_pin7), .A6(_74153_4_pin9), .A7(_74153_4_pin7),
    .A8(fuse_287_a), .A9(fuse_286_a), .A10(fuse_285_a), .A11(fuse_284_a), .A12(fuse_283_a),
    .A13(_7404_2_pin13), .A14(fuse_225_b));
  _74541 _74541_5 (
    .pin1(fuse_257_b), .pin2(_74541_1_pin9), .pin3(_74541_1_pin8), .pin4(_74541_1_pin7),
    .pin5(_74541_1_pin6), .pin6(_74541_1_pin5), .pin7(_74541_1_pin4), .pin8(_74541_1_pin3),
    .pin9(_74541_1_pin2), .pin10(1'b0), .pin11(_74157_3_pin14[7]), .pin12(_74157_3_pin14[6]),
    .pin13(_74157_3_pin14[5]), .pin14(_74157_3_pin14[4]), .pin15(_74157_3_pin14[3]),
    .pin16(_74157_3_pin14[2]), .pin17(_74157_3_pin14[1]), .pin18(_74157_3_pin14[0]), .pin19(1'b0),
    .pin20(1'b1));
  _74541 _74541_6 (
    .pin1(fuse_262_b), .pin2(_74541_2_pin9), .pin3(_74541_2_pin8), .pin4(_74541_2_pin7),
    .pin5(_74541_2_pin6), .pin6(_74541_2_pin5), .pin7(_74541_2_pin4), .pin8(_74541_2_pin3),
    .pin9(_74541_2_pin2), .pin10(1'b0), .pin11(_74157_3_pin14[7]), .pin12(_74157_3_pin14[6]),
    .pin13(_74157_3_pin14[5]), .pin14(_74157_3_pin14[4]), .pin15(_74157_3_pin14[3]),
    .pin16(_74157_3_pin14[2]), .pin17(_74157_3_pin14[1]), .pin18(_74157_3_pin14[0]), .pin19(1'b0),
    .pin20(1'b1));
  Fuse fuse_276 (.A(_74574_23_pin15), .B(fuse_276_b));
  Fuse fuse_277 (.A(_74574_22_pin14), .B(fuse_277_b));
  Fuse fuse_278 (.A(_74574_23_pin14), .B(fuse_278_b));
  Fuse fuse_279 (.A(_74574_22_pin13), .B(fuse_279_b));
  Fuse fuse_280 (.A(_74574_23_pin13), .B(fuse_280_b));
  Fuse fuse_281 (.A(_74574_22_pin12), .B(fuse_281_b));
  Fuse fuse_282 (.A(_74574_23_pin12), .B(fuse_282_b));
  _74139 _74139_2 (
    .pin1(1'b0), .pin2(fuse_282_b), .pin3(fuse_281_b), .pin4(_74139_2_pin4), .pin5(_74139_2_pin5),
    .pin6(_74139_2_pin6), .pin7(_74139_2_pin7), .pin8(1'b0), .pin9(_74139_2_pin9), .pin10(_74139_2_pin10),
    .pin11(_74139_2_pin11), .pin12(_74139_2_pin12), .pin13(fuse_279_b), .pin14(fuse_280_b), .pin15(1'b0),
    .pin16(1'b1));
  not not_2 (not_2_out, _7400_1_pin3);
  Fuse fuse_283 (.A(fuse_283_a), .B(fuse_283_b));
  _74574 _74574_26 (
    .pin1(not_2_out), .pin2(_74153_1_pin9), .pin3(_74153_1_pin7), .pin4(_74153_2_pin9), .pin5(_74153_2_pin7),
    .pin6(_74153_3_pin9), .pin7(_74153_3_pin7), .pin8(_74153_4_pin9), .pin9(_74153_4_pin7), .pin10(1'b0),
    .pin11(clk), .pin12(_74574_26_pin12), .pin13(_74574_26_pin13), .pin14(_74574_26_pin14),
    .pin15(_74574_26_pin15), .pin16(_74574_26_pin16), .pin17(_74574_26_pin17), .pin18(_74574_26_pin18),
    .pin19(_74574_26_pin19), .pin20(1'b1));
  _28c256_programmable _1A (
    .nCE(1'b0), .nOE(1'b0), .nWE(1'b1), .VCC(1'b1), .GND(1'b0), .I_O0(_74574_23_pin9), .I_O1(_74574_22_pin9),
    .I_O2(_74574_23_pin8), .I_O3(_74574_22_pin8), .I_O4(_74574_23_pin7), .I_O5(_74574_22_pin7),
    .I_O6(_74574_23_pin6), .I_O7(_74574_22_pin6), .A0(_74153_1_pin9), .A1(_74153_1_pin7), .A2(_74153_2_pin9),
    .A3(_74153_2_pin7), .A4(_74153_3_pin9), .A5(_74153_3_pin7), .A6(_74153_4_pin9), .A7(_74153_4_pin7),
    .A8(fuse_287_a), .A9(fuse_286_a), .A10(fuse_285_a), .A11(fuse_284_a), .A12(fuse_283_a),
    .A13(_7404_2_pin13), .A14(fuse_225_b));
  Fuse fuse_284 (.A(fuse_284_a), .B(fuse_284_b));
  Fuse fuse_285 (.A(fuse_285_a), .B(fuse_285_b));
  Fuse fuse_286 (.A(fuse_286_a), .B(fuse_286_b));
  Fuse fuse_287 (.A(fuse_287_a), .B(fuse_287_b));
  _74138 _74138_5 (
    .pin1(_74138_5_pin1), .pin2(_74138_5_pin2), .pin3(_74138_5_pin3), .pin4(_74138_5_pin4), .pin5(1'b0),
    .pin6(1'b1), .pin7(fuse_257_a), .pin8(1'b0), .pin9(fuse_262_a), .pin10(_74138_5_pin10),
    .pin11(_74138_5_pin11), .pin12(_74138_5_pin12), .pin13(_74138_5_pin13), .pin14(_74138_5_pin14),
    .pin16(1'b1));  // open: pin15
  _74138 _74138_6 (
    .pin1(_74138_6_pin1), .pin2(_74138_6_pin2), .pin3(_74138_6_pin3), .pin4(_74138_6_pin4),
    .pin5(_74138_1_pin5), .pin6(1'b1), .pin7(fuse_264_a), .pin8(1'b0), .pin9(fuse_258_a),
    .pin11(_74138_6_pin11), .pin12(_74138_6_pin12), .pin13(_74138_6_pin13), .pin14(_74138_6_pin14),
    .pin16(1'b1));  // open: pin10, pin15
  _74574 _74574_27 (
    .pin1(1'b0), .pin2(_74574_27_pin2), .pin3(_74574_27_pin3), .pin4(_74574_27_pin4), .pin5(_74574_27_pin5),
    .pin6(_74574_27_pin6), .pin7(_74574_27_pin7), .pin8(_74574_27_pin8), .pin9(_74574_27_pin9), .pin10(1'b0),
    .pin11(clk), .pin12(_74574_27_pin12), .pin13(_74574_27_pin13), .pin14(_74574_27_pin14),
    .pin15(_74574_27_pin15), .pin16(_74574_27_pin16), .pin17(_74574_27_pin17), .pin18(_7404_2_pin13),
    .pin20(1'b1));  // open: pin19
  _74574 _74574_28 (
    .pin1(1'b0), .pin2(_74574_28_pin2), .pin3(_74574_28_pin3), .pin4(_74574_28_pin4), .pin5(_74574_28_pin5),
    .pin6(_74574_28_pin6), .pin7(_74574_28_pin7), .pin8(_74574_28_pin8), .pin9(_74574_28_pin9), .pin10(1'b0),
    .pin11(clk), .pin12(_74574_28_pin12), .pin13(_74574_28_pin13), .pin14(_74574_28_pin14),
    .pin15(_74574_28_pin15), .pin16(_74574_28_pin16), .pin17(_74574_28_pin17), .pin18(_74574_28_pin18),
    .pin19(_74153_1_pin14), .pin20(1'b1));
  Fuse fuse_288 (.A(_74574_28_pin18), .B(_74138_4_pin3));
  Fuse fuse_289 (.A(_74574_27_pin17), .B(_74138_4_pin2));
  Fuse fuse_290 (.A(_74574_28_pin17), .B(_74138_4_pin1));
  Fuse fuse_291 (.A(_74574_27_pin16), .B(_74139_1_pin13));
  Fuse fuse_292 (.A(_74574_28_pin16), .B(_74139_1_pin14));
  _28c256_programmable _2B (
    .nCE(1'b0), .nOE(1'b0), .nWE(1'b1), .VCC(1'b1), .GND(1'b0), .I_O0(_74574_28_pin5), .I_O1(_74574_27_pin5),
    .I_O2(_74574_28_pin4), .I_O3(_74574_27_pin4), .I_O4(_74574_28_pin3), .I_O5(_74574_27_pin3),
    .I_O6(_74574_28_pin2), .I_O7(_74574_27_pin2), .A0(_74574_26_pin19), .A1(_74574_26_pin18),
    .A2(_74574_26_pin17), .A3(_74574_26_pin16), .A4(_74574_26_pin15), .A5(_74574_26_pin14),
    .A6(_74574_26_pin13), .A7(_74574_26_pin12), .A8(fuse_287_a), .A9(fuse_286_a), .A10(fuse_285_a),
    .A11(fuse_284_a), .A12(fuse_283_a), .A13(_7404_2_pin13), .A14(fuse_225_b));
  _74138 _74138_7 (
    .pin1(_74138_5_pin1), .pin2(_74138_5_pin2), .pin3(_74138_5_pin3), .pin4(1'b0), .pin5(1'b0),
    .pin6(_74138_5_pin4), .pin7(_74138_7_pin7), .pin8(1'b0), .pin10(_74138_7_pin10), .pin11(_74138_7_pin11),
    .pin12(_74138_7_pin12), .pin13(_74138_7_pin13), .pin14(_74138_7_pin14), .pin15(_74138_7_pin15),
    .pin16(1'b1));  // open: pin9
  _74138 _74138_8 (
    .pin1(_74138_6_pin1), .pin2(_74138_6_pin2), .pin3(_74138_6_pin3), .pin4(1'b0), .pin5(_74138_1_pin5),
    .pin6(_74138_6_pin4), .pin7(_7404_1_pin3), .pin8(1'b0), .pin10(_74138_8_pin10), .pin11(_74138_8_pin11),
    .pin12(_74138_8_pin12), .pin13(_74138_8_pin13), .pin14(_74138_8_pin14), .pin16(1'b1));  // open: pin9, pin15
  Fuse fuse_293 (.A(_74574_27_pin15), .B(_74138_6_pin4));
  Fuse fuse_294 (.A(_74574_28_pin15), .B(_74138_6_pin3));
  Fuse fuse_295 (.A(_74574_27_pin14), .B(_74138_6_pin2));
  Fuse fuse_296 (.A(_74574_28_pin14), .B(_74138_6_pin1));
  Fuse fuse_297 (.A(_74574_27_pin13), .B(_74138_5_pin4));
  Fuse fuse_298 (.A(_74574_28_pin13), .B(_74138_5_pin3));
  Fuse fuse_299 (.A(_74574_27_pin12), .B(_74138_5_pin2));
  Fuse fuse_300 (.A(_74574_28_pin12), .B(_74138_5_pin1));
  _7420 _7420_1 (
    .pin1(_74138_6_pin4), .pin2(_74138_6_pin3), .pin4(_74138_6_pin2), .pin5(_74138_6_pin1),
    .pin6(_7404_1_pin13), .pin7(1'b0), .pin9(1'b0), .pin10(1'b0), .pin12(1'b0), .pin13(1'b0), .pin14(1'b1));  // open: pin3, pin8, pin11
  Terminal terminal_1 (.Data(_74157_3_pin14), .Clock(clk), .Load(_74138_8_pin14));
  _28c256_programmable _2A (
    .nCE(1'b0), .nOE(1'b0), .nWE(1'b1), .VCC(1'b1), .GND(1'b0), .I_O0(_74574_28_pin9), .I_O1(_74574_27_pin9),
    .I_O2(_74574_28_pin8), .I_O3(_74574_27_pin8), .I_O4(_74574_28_pin7), .I_O5(_74574_27_pin7),
    .I_O6(_74574_28_pin6), .I_O7(_74574_27_pin6), .A0(_74574_26_pin19), .A1(_74574_26_pin18),
    .A2(_74574_26_pin17), .A3(_74574_26_pin16), .A4(_74574_26_pin15), .A5(_74574_26_pin14),
    .A6(_74574_26_pin13), .A7(_74574_26_pin12), .A8(fuse_287_a), .A9(fuse_286_a), .A10(fuse_285_a),
    .A11(fuse_284_a), .A12(fuse_283_a), .A13(_7404_2_pin13), .A14(fuse_225_b));
  Fuse fuse_301 (.A(_74139_2_pin4), .B(fuse_301_b));
  Fuse fuse_302 (.A(_74139_2_pin12), .B(fuse_302_b));
  Fuse fuse_303 (.A(_74138_6_pin14), .B(fuse_303_b));
  Fuse fuse_304 (.A(_74138_5_pin14), .B(fuse_304_b));
  Fuse fuse_305 (.A(_74139_2_pin5), .B(fuse_305_b));
  Fuse fuse_306 (.A(_74139_2_pin11), .B(fuse_306_b));
  Fuse fuse_307 (.A(_74138_6_pin13), .B(fuse_307_b));
  Fuse fuse_308 (.A(_74138_5_pin13), .B(fuse_308_b));
  Fuse fuse_309 (.A(_74139_2_pin6), .B(fuse_309_b));
  Fuse fuse_310 (.A(_74139_2_pin10), .B(fuse_310_b));
  Fuse fuse_311 (.A(_74138_6_pin12), .B(fuse_311_b));
  Fuse fuse_312 (.A(_74138_5_pin12), .B(fuse_312_b));
  Fuse fuse_313 (.A(_74139_2_pin7), .B(fuse_313_b));
  Fuse fuse_314 (.A(_74139_2_pin9), .B(fuse_314_b));
  Fuse fuse_315 (.A(_74138_6_pin11), .B(fuse_315_b));
  Fuse fuse_316 (.A(_74138_5_pin11), .B(fuse_316_b));
  Fuse fuse_317 (.A(fuse_278_b), .B(fuse_317_b));
  Fuse fuse_318 (.A(fuse_277_b), .B(fuse_318_b));
  Fuse fuse_319 (.A(fuse_276_b), .B(fuse_319_b));
  Fuse fuse_320 (.A(fuse_275_b), .B(fuse_320_b));
  Fuse fuse_321 (.A(fuse_283_b), .B(fuse_321_b));
  Fuse fuse_322 (.A(fuse_284_b), .B(fuse_322_b));
  Fuse fuse_323 (.A(fuse_285_b), .B(fuse_323_b));
  Fuse fuse_324 (.A(fuse_286_b), .B(fuse_324_b));
  Fuse fuse_325 (.A(fuse_287_b), .B(fuse_325_b));
  Fuse fuse_326 (.A(_74138_7_pin15), .B(fuse_326_b));
  Fuse fuse_327 (.A(_74138_2_pin15), .B(fuse_327_b));
  Fuse fuse_328 (.A(_74138_5_pin10), .B(fuse_328_b));
  Fuse fuse_329 (.A(_74138_7_pin7), .B(fuse_329_b));
  Fuse fuse_330 (.A(_7404_1_pin13), .B(fuse_330_b));
  Fuse fuse_331 (.A(fuse_331_a), .B(fuse_167_a));
  Fuse fuse_332 (.A(fuse_332_a), .B(fuse_168_a));
  Fuse fuse_333 (.A(fuse_333_a), .B(fuse_169_a));
  Fuse fuse_334 (.A(fuse_334_a), .B(fuse_170_a));
  Fuse fuse_335 (.A(fuse_335_a), .B(fuse_171_a));
  Fuse fuse_336 (.A(fuse_336_a), .B(fuse_172_a));
  Fuse fuse_337 (.A(fuse_337_a), .B(fuse_173_a));
  Fuse fuse_338 (.A(fuse_338_a), .B(fuse_174_a));
  Fuse fuse_339 (.A(fuse_339_a), .B(_74157_3_pin14[7]));
  Fuse fuse_340 (.A(fuse_340_a), .B(_74157_3_pin14[6]));
  Fuse fuse_341 (.A(fuse_341_a), .B(_74157_3_pin14[5]));
  Fuse fuse_342 (.A(fuse_342_a), .B(_74157_3_pin14[4]));
  Fuse fuse_343 (.A(fuse_343_a), .B(fuse_339_a));
  Fuse fuse_344 (.A(fuse_344_a), .B(fuse_340_a));
  Fuse fuse_345 (.A(fuse_345_a), .B(fuse_341_a));
  Fuse fuse_346 (.A(fuse_346_a), .B(fuse_342_a));
  Fuse fuse_347 (.A(fuse_347_a), .B(fuse_343_a));
  Fuse fuse_348 (.A(fuse_348_a), .B(fuse_344_a));
  Fuse fuse_349 (.A(fuse_349_a), .B(fuse_345_a));
  Fuse fuse_350 (.A(fuse_350_a), .B(fuse_346_a));
  Fuse fuse_351 (.A(fuse_351_a), .B(fuse_347_a));
  Fuse fuse_352 (.A(fuse_352_a), .B(fuse_348_a));
  Fuse fuse_353 (.A(fuse_353_a), .B(fuse_349_a));
  Fuse fuse_354 (.A(fuse_354_a), .B(fuse_350_a));
  Fuse fuse_355 (.A(fuse_355_a), .B(fuse_351_a));
  Fuse fuse_356 (.A(fuse_356_a), .B(fuse_352_a));
  Fuse fuse_357 (.A(fuse_357_a), .B(fuse_353_a));
  Fuse fuse_358 (.A(fuse_358_a), .B(fuse_354_a));
  Fuse fuse_359 (.A(fuse_359_a), .B(fuse_355_a));
  Fuse fuse_360 (.A(fuse_360_a), .B(fuse_356_a));
  Fuse fuse_361 (.A(fuse_361_a), .B(fuse_357_a));
  Fuse fuse_362 (.A(fuse_362_a), .B(fuse_358_a));
  Fuse fuse_363 (.A(fuse_363_a), .B(_74157_3_pin14[3]));
  Fuse fuse_364 (.A(fuse_364_a), .B(_74157_3_pin14[2]));
  Fuse fuse_365 (.A(fuse_365_a), .B(_74157_3_pin14[1]));
  Fuse fuse_366 (.A(fuse_366_a), .B(_74157_3_pin14[0]));
  Fuse fuse_367 (.A(fuse_367_a), .B(fuse_363_a));
  Fuse fuse_368 (.A(fuse_368_a), .B(fuse_364_a));
  Fuse fuse_369 (.A(fuse_369_a), .B(fuse_365_a));
  Fuse fuse_370 (.A(fuse_370_a), .B(fuse_366_a));
  Fuse fuse_371 (.A(fuse_371_a), .B(fuse_367_a));
  Fuse fuse_372 (.A(fuse_372_a), .B(fuse_368_a));
  Fuse fuse_373 (.A(fuse_373_a), .B(fuse_369_a));
  Fuse fuse_374 (.A(fuse_374_a), .B(fuse_370_a));
  Fuse fuse_375 (.A(fuse_375_a), .B(fuse_371_a));
  Fuse fuse_376 (.A(fuse_376_a), .B(fuse_372_a));
  Fuse fuse_377 (.A(fuse_377_a), .B(fuse_373_a));
  Fuse fuse_378 (.A(fuse_378_a), .B(fuse_374_a));
  Fuse fuse_379 (.A(fuse_379_a), .B(fuse_375_a));
  Fuse fuse_380 (.A(fuse_380_a), .B(fuse_376_a));
  Fuse fuse_381 (.A(fuse_381_a), .B(fuse_377_a));
  Fuse fuse_382 (.A(fuse_382_a), .B(fuse_378_a));
  Fuse fuse_383 (.A(fuse_383_a), .B(fuse_379_a));
  Fuse fuse_384 (.A(fuse_384_a), .B(fuse_380_a));
  Fuse fuse_385 (.A(fuse_385_a), .B(fuse_381_a));
  Fuse fuse_386 (.A(fuse_386_a), .B(fuse_382_a));
  _74574 _74574_29 (
    .pin1(1'b0), .pin2(fuse_366_a), .pin3(fuse_365_a), .pin4(fuse_364_a), .pin5(fuse_363_a),
    .pin6(fuse_342_a), .pin7(fuse_341_a), .pin8(fuse_340_a), .pin9(fuse_339_a), .pin10(1'b0),
    .pin11(fuse_303_b), .pin12(_74574_29_pin12), .pin13(_74574_29_pin13), .pin14(_74574_29_pin14),
    .pin15(_74574_29_pin15), .pin16(_74574_29_pin16), .pin17(_74574_29_pin17), .pin18(_74574_29_pin18),
    .pin19(_74574_29_pin19), .pin20(1'b1));
  _74574 _74574_30 (
    .pin1(1'b0), .pin2(fuse_370_a), .pin3(fuse_369_a), .pin4(fuse_368_a), .pin5(fuse_367_a),
    .pin6(fuse_346_a), .pin7(fuse_345_a), .pin8(fuse_344_a), .pin9(fuse_343_a), .pin10(1'b0),
    .pin11(fuse_307_b), .pin12(_74574_30_pin12), .pin13(_74574_30_pin13), .pin14(_74574_30_pin14),
    .pin15(_74574_30_pin15), .pin16(_74574_30_pin16), .pin17(_74574_30_pin17), .pin18(_74574_30_pin18),
    .pin19(_74574_30_pin19), .pin20(1'b1));
  _74574 _74574_31 (
    .pin1(1'b0), .pin2(fuse_374_a), .pin3(fuse_373_a), .pin4(fuse_372_a), .pin5(fuse_371_a),
    .pin6(fuse_350_a), .pin7(fuse_349_a), .pin8(fuse_348_a), .pin9(fuse_347_a), .pin10(1'b0),
    .pin11(fuse_311_b), .pin12(_74574_31_pin12), .pin13(_74574_31_pin13), .pin14(_74574_31_pin14),
    .pin15(_74574_31_pin15), .pin16(_74574_31_pin16), .pin17(_74574_31_pin17), .pin18(_74574_31_pin18),
    .pin19(_74574_31_pin19), .pin20(1'b1));
  _74574 _74574_32 (
    .pin1(1'b0), .pin2(fuse_378_a), .pin3(fuse_377_a), .pin4(fuse_376_a), .pin5(fuse_375_a),
    .pin6(fuse_354_a), .pin7(fuse_353_a), .pin8(fuse_352_a), .pin9(fuse_351_a), .pin10(1'b0),
    .pin11(fuse_315_b), .pin12(_74574_32_pin12), .pin13(_74574_32_pin13), .pin14(_74574_32_pin14),
    .pin15(_74574_32_pin15), .pin16(_74574_32_pin16), .pin17(_74574_32_pin17), .pin18(_74574_32_pin18),
    .pin19(_74574_32_pin19), .pin20(1'b1));
  _7402 _7402_1 (
    .pin1(_7402_1_pin1), .pin2(_7402_1_pin2), .pin3(_7402_1_pin2), .pin4(_7402_1_pin2), .pin5(clk),
    .pin6(_7402_1_pin6), .pin7(1'b0), .pin8(fuse_320_b), .pin9(fuse_319_b), .pin10(_7402_1_pin10),
    .pin11(fuse_317_b), .pin12(fuse_318_b), .pin13(_7402_1_pin13), .pin14(1'b1));
  _7408 _7408_2 (
    .pin1(_7402_1_pin10), .pin2(_7402_1_pin13), .pin3(_7402_1_pin6), .pin4(_7408_2_pin4),
    .pin5(_7408_2_pin5), .pin6(fuse_324_b), .pin7(1'b0), .pin8(fuse_325_b), .pin9(_7408_2_pin9),
    .pin10(_7408_2_pin10), .pin12(1'b0), .pin13(1'b0), .pin14(1'b1));  // open: pin11
  _7486 _7486_1 (
    .pin1(1'b0), .pin2(1'b0), .pin4(1'b0), .pin5(1'b0), .pin7(1'b0), .pin8(_7408_2_pin4), .pin9(fuse_323_b),
    .pin10(_7486_1_pin10), .pin11(_7408_2_pin5), .pin12(fuse_323_b), .pin13(_7486_1_pin13), .pin14(1'b1));  // open: pin3, pin6
  _74541 _74541_7 (
    .pin1(fuse_326_b), .pin2(fuse_382_a), .pin3(fuse_381_a), .pin4(fuse_380_a), .pin5(fuse_379_a),
    .pin6(fuse_358_a), .pin7(fuse_357_a), .pin8(fuse_356_a), .pin9(fuse_355_a), .pin10(1'b0),
    .pin11(_74541_7_pin11), .pin12(_74541_7_pin12), .pin13(_74541_7_pin13), .pin14(_74541_7_pin14),
    .pin15(_74541_7_pin15), .pin16(_74541_7_pin16), .pin17(_74541_7_pin17), .pin18(fuse_323_b), .pin19(1'b0),
    .pin20(1'b1));
  _74541 _74541_8 (
    .pin1(fuse_329_b), .pin2(fuse_359_a), .pin3(fuse_360_a), .pin4(fuse_361_a), .pin5(fuse_362_a),
    .pin6(fuse_383_a), .pin7(fuse_384_a), .pin8(fuse_385_a), .pin9(fuse_386_a), .pin10(1'b0),
    .pin11(fuse_338_a), .pin12(fuse_337_a), .pin13(fuse_336_a), .pin14(fuse_335_a), .pin15(fuse_334_a),
    .pin16(fuse_333_a), .pin17(fuse_332_a), .pin18(fuse_331_a), .pin19(1'b0), .pin20(1'b1));
  _7425 _7425_1 (
    .pin1(_74541_7_pin16), .pin2(_74541_7_pin17), .pin3(_74541_7_pin14), .pin4(fuse_323_b),
    .pin5(_74541_7_pin15), .pin6(_7408_2_pin10), .pin7(1'b0), .pin8(_7408_2_pin9), .pin9(_74541_7_pin11),
    .pin10(_74541_7_pin14), .pin12(_74541_7_pin12), .pin13(_74541_7_pin13), .pin14(1'b1));  // open: pin11
  _74574 _74574_33 (
    .pin1(fuse_328_b), .pin2(fuse_338_a), .pin3(fuse_337_a), .pin4(fuse_336_a), .pin5(fuse_335_a),
    .pin6(fuse_334_a), .pin7(fuse_333_a), .pin8(fuse_332_a), .pin9(fuse_331_a), .pin10(1'b0),
    .pin11(fuse_327_b), .pin12(fuse_359_a), .pin13(fuse_360_a), .pin14(fuse_361_a), .pin15(fuse_362_a),
    .pin16(fuse_383_a), .pin17(fuse_384_a), .pin18(fuse_385_a), .pin19(fuse_386_a), .pin20(1'b1));
  _74541 _74541_9 (
    .pin1(fuse_304_b), .pin2(_74574_29_pin12), .pin3(_74574_29_pin13), .pin4(_74574_29_pin14),
    .pin5(_74574_29_pin15), .pin6(_74574_29_pin16), .pin7(_74574_29_pin17), .pin8(_74574_29_pin18),
    .pin9(_74574_29_pin19), .pin10(1'b0), .pin11(fuse_366_a), .pin12(fuse_365_a), .pin13(fuse_364_a),
    .pin14(fuse_363_a), .pin15(fuse_342_a), .pin16(fuse_341_a), .pin17(fuse_340_a), .pin18(fuse_339_a),
    .pin19(1'b0), .pin20(1'b1));
  _74541 _74541_10 (
    .pin1(fuse_308_b), .pin2(_74574_30_pin12), .pin3(_74574_30_pin13), .pin4(_74574_30_pin14),
    .pin5(_74574_30_pin15), .pin6(_74574_30_pin16), .pin7(_74574_30_pin17), .pin8(_74574_30_pin18),
    .pin9(_74574_30_pin19), .pin10(1'b0), .pin11(fuse_370_a), .pin12(fuse_369_a), .pin13(fuse_368_a),
    .pin14(fuse_367_a), .pin15(fuse_346_a), .pin16(fuse_345_a), .pin17(fuse_344_a), .pin18(fuse_343_a),
    .pin19(1'b0), .pin20(1'b1));
  _74541 _74541_11 (
    .pin1(fuse_312_b), .pin2(_74574_31_pin12), .pin3(_74574_31_pin13), .pin4(_74574_31_pin14),
    .pin5(_74574_31_pin15), .pin6(_74574_31_pin16), .pin7(_74574_31_pin17), .pin8(_74574_31_pin18),
    .pin9(_74574_31_pin19), .pin10(1'b0), .pin11(fuse_374_a), .pin12(fuse_373_a), .pin13(fuse_372_a),
    .pin14(fuse_371_a), .pin15(fuse_350_a), .pin16(fuse_349_a), .pin17(fuse_348_a), .pin18(fuse_347_a),
    .pin19(1'b0), .pin20(1'b1));
  _74541 _74541_12 (
    .pin1(fuse_316_b), .pin2(_74574_32_pin12), .pin3(_74574_32_pin13), .pin4(_74574_32_pin14),
    .pin5(_74574_32_pin15), .pin6(_74574_32_pin16), .pin7(_74574_32_pin17), .pin8(_74574_32_pin18),
    .pin9(_74574_32_pin19), .pin10(1'b0), .pin11(fuse_378_a), .pin12(fuse_377_a), .pin13(fuse_376_a),
    .pin14(fuse_375_a), .pin15(fuse_354_a), .pin16(fuse_353_a), .pin17(fuse_352_a), .pin18(fuse_351_a),
    .pin19(1'b0), .pin20(1'b1));
  _74574 _74574_34 (
    .pin1(1'b0), .pin2(_74253_1_pin14[7]), .pin3(_74253_1_pin14[6]), .pin4(1'b0), .pin5(fuse_321_b),
    .pin6(_74574_34_pin6), .pin7(1'b0), .pin8(1'b0), .pin9(1'b0), .pin10(1'b0), .pin13(1'b0),
    .pin14(_74574_34_pin14), .pin15(1'b0), .pin16(_74574_34_pin16), .pin17(1'b1), .pin18(1'b0),
    .pin19(_74574_34_pin19), .pin20(1'b0));  // open: pin11, pin12
  _74253 _74253_1 (
    .pin1(1'b0), .pin2(_74253_1_pin14[1]), .pin3(1'b0), .pin4(_74253_1_pin4), .pin5(_74253_1_pin5),
    .pin6(fuse_322_b), .pin7(_74574_34_pin6), .pin8(1'b0), .pin10(1'b0), .pin11(1'b0), .pin12(1'b0),
    .pin13(1'b0), .pin14(_74253_1_pin14[0]), .pin15(1'b1), .pin16(1'b1));  // open: pin9
  _74253 _74253_2 (
    .pin1(1'b0), .pin2(_74253_1_pin14[1]), .pin3(1'b0), .pin4(_74253_2_pin4), .pin5(_74253_1_pin4),
    .pin6(_74253_2_pin6), .pin7(_74253_2_pin7), .pin8(1'b0), .pin9(_74253_2_pin9), .pin10(_74253_1_pin4),
    .pin11(fuse_322_b), .pin12(_74253_2_pin6), .pin13(1'b0), .pin14(_74253_1_pin14[0]), .pin15(1'b0),
    .pin16(1'b1));
  _74253 _74253_3 (
    .pin1(1'b0), .pin2(_74253_1_pin14[1]), .pin3(1'b0), .pin4(_74253_3_pin4), .pin5(_74253_2_pin4),
    .pin6(_74253_3_pin6), .pin7(_74253_3_pin7), .pin8(1'b0), .pin9(_74253_3_pin9), .pin10(_74253_2_pin4),
    .pin11(_74253_2_pin6), .pin12(_74253_3_pin6), .pin13(1'b0), .pin14(_74253_1_pin14[0]), .pin15(1'b0),
    .pin16(1'b1));
  _74253 _74253_4 (
    .pin1(1'b0), .pin2(_74253_1_pin14[1]), .pin3(1'b0), .pin4(_74253_4_pin4), .pin5(_74253_3_pin4),
    .pin6(_74253_4_pin6), .pin7(_74253_4_pin7), .pin8(1'b0), .pin9(1'b0), .pin10(_74253_3_pin7),
    .pin11(_74253_3_pin6), .pin12(_74253_2_pin4), .pin13(_74253_3_pin4), .pin14(1'b0),
    .pin15(_74253_1_pin14[1]), .pin16(1'b0));
  _74253 _74253_5 (
    .pin1(1'b0), .pin2(_74253_1_pin14[1]), .pin3(1'b0), .pin4(fuse_322_b), .pin5(_74253_4_pin4),
    .pin6(_74253_1_pin5), .pin7(_7486_1_pin10), .pin8(1'b0), .pin9(_74253_5_pin9), .pin10(_74253_4_pin4),
    .pin11(_74253_4_pin6), .pin12(_74253_1_pin5), .pin13(1'b0), .pin14(_74253_1_pin14[0]), .pin15(1'b0),
    .pin16(1'b1));
  _74541 _74541_13 (
    .pin1(fuse_330_b), .pin2(fuse_338_a), .pin3(fuse_337_a), .pin4(fuse_336_a), .pin5(fuse_335_a),
    .pin6(fuse_334_a), .pin7(fuse_333_a), .pin8(fuse_332_a), .pin9(fuse_331_a), .pin10(1'b0),
    .pin11(fuse_359_a), .pin12(fuse_360_a), .pin13(fuse_361_a), .pin14(fuse_362_a), .pin15(fuse_383_a),
    .pin16(fuse_384_a), .pin17(fuse_385_a), .pin18(fuse_386_a), .pin19(1'b0), .pin20(1'b1));
  _74541 _74541_14 (
    .pin1(fuse_302_b), .pin2(_74574_29_pin19), .pin3(_74574_29_pin18), .pin4(_74574_29_pin17),
    .pin5(_74574_29_pin16), .pin6(_74574_29_pin15), .pin7(_74574_29_pin14), .pin8(_74574_29_pin13),
    .pin9(_74574_29_pin12), .pin10(1'b0), .pin11(_74541_14_pin11), .pin12(_74541_14_pin12),
    .pin13(_74541_14_pin13), .pin14(_74541_14_pin14), .pin15(_74541_14_pin15), .pin16(_74541_14_pin16),
    .pin17(_74541_14_pin17), .pin18(_74541_14_pin18), .pin19(1'b0), .pin20(1'b1));
  _74541 _74541_15 (
    .pin1(fuse_306_b), .pin2(_74574_30_pin19), .pin3(_74574_30_pin18), .pin4(_74574_30_pin17),
    .pin5(_74574_30_pin16), .pin6(_74574_30_pin15), .pin7(_74574_30_pin14), .pin8(_74574_30_pin13),
    .pin9(_74574_30_pin12), .pin10(1'b0), .pin11(_74541_15_pin11), .pin12(_74541_15_pin12),
    .pin13(_74541_15_pin13), .pin14(_74541_15_pin14), .pin15(_74541_15_pin15), .pin16(_74541_15_pin16),
    .pin17(_74541_15_pin17), .pin18(_74541_15_pin18), .pin19(1'b0), .pin20(1'b1));
  _74541 _74541_16 (
    .pin1(fuse_310_b), .pin2(_74574_31_pin19), .pin3(_74574_31_pin18), .pin4(_74574_31_pin17),
    .pin5(_74574_31_pin16), .pin6(_74574_31_pin15), .pin7(_74574_31_pin14), .pin8(_74574_31_pin13),
    .pin9(_74574_31_pin12), .pin10(1'b0), .pin11(_74541_16_pin11), .pin12(_74541_16_pin12),
    .pin13(_74541_16_pin13), .pin14(_74541_16_pin14), .pin15(_74541_16_pin15), .pin16(_74541_16_pin16),
    .pin17(_74541_16_pin17), .pin18(_74541_16_pin18), .pin19(1'b0), .pin20(1'b1));
  _74541 _74541_17 (
    .pin1(fuse_314_b), .pin2(_74574_32_pin19), .pin3(_74574_32_pin18), .pin4(_74574_32_pin17),
    .pin5(_74574_32_pin16), .pin6(_74574_32_pin15), .pin7(_74574_32_pin14), .pin8(_74574_32_pin13),
    .pin9(_74574_32_pin12), .pin10(1'b0), .pin11(_74541_17_pin11), .pin12(_74541_17_pin12),
    .pin13(_74541_17_pin13), .pin14(_74541_17_pin14), .pin15(_74541_17_pin15), .pin16(_74541_17_pin16),
    .pin17(_74541_17_pin17), .pin18(_74541_17_pin18), .pin19(1'b0), .pin20(1'b1));
  LookUpTable #(.Bits(8)) ALU_Control (
    .in0(fuse_317_b), .in1(fuse_318_b), .in2(fuse_319_b), .in3(fuse_320_b), .out(_74253_1_pin14));
  _74541 _74541_18 (
    .pin1(fuse_301_b), .pin2(_74574_29_pin19), .pin3(_74574_29_pin18), .pin4(_74574_29_pin17),
    .pin5(_74574_29_pin16), .pin6(_74574_29_pin15), .pin7(_74574_29_pin14), .pin8(_74574_29_pin13),
    .pin9(_74574_29_pin12), .pin10(1'b0), .pin11(_74541_18_pin11), .pin12(_74541_18_pin12),
    .pin13(_74541_18_pin13), .pin14(_74541_18_pin14), .pin15(_74541_18_pin15), .pin16(_74541_18_pin16),
    .pin17(_74541_18_pin17), .pin18(_74541_18_pin18), .pin19(1'b0), .pin20(1'b1));
  _74541 _74541_19 (
    .pin1(fuse_305_b), .pin2(_74574_30_pin19), .pin3(_74574_30_pin18), .pin4(_74574_30_pin17),
    .pin5(_74574_30_pin16), .pin6(_74574_30_pin15), .pin7(_74574_30_pin14), .pin8(_74574_30_pin13),
    .pin9(_74574_30_pin12), .pin10(1'b0), .pin11(_74541_19_pin11), .pin12(_74541_19_pin12),
    .pin13(_74541_19_pin13), .pin14(_74541_19_pin14), .pin15(_74541_19_pin15), .pin16(_74541_19_pin16),
    .pin17(_74541_19_pin17), .pin18(_74541_19_pin18), .pin19(1'b0), .pin20(1'b1));
  _74541 _74541_20 (
    .pin1(fuse_309_b), .pin2(_74574_31_pin19), .pin3(_74574_31_pin18), .pin4(_74574_31_pin17),
    .pin5(_74574_31_pin16), .pin6(_74574_31_pin15), .pin7(_74574_31_pin14), .pin8(_74574_31_pin13),
    .pin9(_74574_31_pin12), .pin10(1'b0), .pin11(_74541_20_pin11), .pin12(_74541_20_pin12),
    .pin13(_74541_20_pin13), .pin14(_74541_20_pin14), .pin15(_74541_20_pin15), .pin16(_74541_20_pin16),
    .pin17(_74541_20_pin17), .pin18(_74541_20_pin18), .pin19(1'b0), .pin20(1'b1));
  _74541 _74541_21 (
    .pin1(fuse_313_b), .pin2(_74574_32_pin19), .pin3(_74574_32_pin18), .pin4(_74574_32_pin17),
    .pin5(_74574_32_pin16), .pin6(_74574_32_pin15), .pin7(_74574_32_pin14), .pin8(_74574_32_pin13),
    .pin9(_74574_32_pin12), .pin10(1'b0), .pin11(_74541_21_pin11), .pin12(_74541_21_pin12),
    .pin13(_74541_21_pin13), .pin14(_74541_21_pin14), .pin15(_74541_21_pin15), .pin16(_74541_21_pin16),
    .pin17(_74541_21_pin17), .pin18(_74541_21_pin18), .pin19(1'b0), .pin20(1'b1));
  _74253 _74253_6 (
    .pin1(1'b0), .pin2(_74574_34_pin19), .pin3(1'b0), .pin4(1'b1), .pin5(_74574_34_pin16), .pin6(1'b0),
    .pin7(_74574_34_pin14), .pin8(1'b0), .pin10(1'b0), .pin11(1'b0), .pin12(1'b0), .pin13(1'b0),
    .pin14(_74253_6_pin14), .pin15(1'b1), .pin16(1'b1));  // open: pin9
  Fuse fuse_387 (.A(_74541_15_pin11), .B(_74541_14_pin11));
  Fuse fuse_388 (.A(_74541_16_pin11), .B(_74541_15_pin11));
  Fuse fuse_389 (.A(_74541_17_pin11), .B(_74541_16_pin11));
  Fuse fuse_390 (.A(_74253_1_pin4), .B(_74541_17_pin11));
  _74283 _74283_1 (
    .pin1(_74541_7_pin17), .pin2(_74283_1_pin2), .pin3(_74283_1_pin3), .pin4(fuse_323_b),
    .pin5(_74283_1_pin5), .pin6(_74283_1_pin6), .pin7(_74574_34_pin14), .pin8(1'b0), .pin9(_74283_1_pin9),
    .pin10(_74541_7_pin15), .pin11(_74283_1_pin11), .pin12(_74283_1_pin12), .pin13(_74541_7_pin16),
    .pin14(_74283_1_pin14), .pin15(_74283_1_pin15), .pin16(1'b1));
  _74283 _74283_2 (
    .pin1(_74541_7_pin13), .pin2(_74283_2_pin2), .pin3(_74283_2_pin3), .pin4(_74541_7_pin14),
    .pin5(_74283_2_pin5), .pin6(_74283_2_pin6), .pin7(_74283_1_pin9), .pin8(1'b0), .pin9(fuse_321_b),
    .pin10(_74541_7_pin11), .pin11(_74283_2_pin11), .pin12(_74283_2_pin12), .pin13(_74541_7_pin12),
    .pin14(_74283_2_pin14), .pin15(_74283_2_pin15), .pin16(1'b1));
  Fuse fuse_391 (.A(_74541_15_pin12), .B(_74541_14_pin12));
  Fuse fuse_392 (.A(_74541_15_pin13), .B(_74541_14_pin13));
  Fuse fuse_393 (.A(_74541_15_pin14), .B(_74541_14_pin14));
  Fuse fuse_394 (.A(_74541_15_pin15), .B(_74541_14_pin15));
  Fuse fuse_395 (.A(_74541_16_pin12), .B(_74541_15_pin12));
  Fuse fuse_396 (.A(_74541_16_pin13), .B(_74541_15_pin13));
  Fuse fuse_397 (.A(_74541_16_pin14), .B(_74541_15_pin14));
  Fuse fuse_398 (.A(_74541_16_pin15), .B(_74541_15_pin15));
  Fuse fuse_399 (.A(_74541_17_pin12), .B(_74541_16_pin12));
  Fuse fuse_400 (.A(_74541_17_pin13), .B(_74541_16_pin13));
  Fuse fuse_401 (.A(_74541_17_pin14), .B(_74541_16_pin14));
  Fuse fuse_402 (.A(_74541_17_pin15), .B(_74541_16_pin15));
  Fuse fuse_403 (.A(_74253_2_pin6), .B(_74541_17_pin12));
  Fuse fuse_404 (.A(_74253_2_pin4), .B(_74541_17_pin13));
  Fuse fuse_405 (.A(_74253_3_pin6), .B(_74541_17_pin14));
  Fuse fuse_406 (.A(_74253_3_pin4), .B(_74541_17_pin15));
  Fuse fuse_407 (.A(_74541_15_pin16), .B(_74541_14_pin16));
  Fuse fuse_408 (.A(_74541_15_pin17), .B(_74541_14_pin17));
  Fuse fuse_409 (.A(_74541_15_pin18), .B(_74541_14_pin18));
  Fuse fuse_410 (.A(_74541_16_pin16), .B(_74541_15_pin16));
  Fuse fuse_411 (.A(_74541_16_pin17), .B(_74541_15_pin17));
  Fuse fuse_412 (.A(_74541_16_pin18), .B(_74541_15_pin18));
  Fuse fuse_413 (.A(_74541_17_pin16), .B(_74541_16_pin16));
  Fuse fuse_414 (.A(_74541_17_pin17), .B(_74541_16_pin17));
  Fuse fuse_415 (.A(_74541_17_pin18), .B(_74541_16_pin18));
  Fuse fuse_416 (.A(_74253_4_pin6), .B(_74541_17_pin16));
  Fuse fuse_417 (.A(_74253_4_pin4), .B(_74541_17_pin17));
  Fuse fuse_418 (.A(_74253_1_pin5), .B(_74541_17_pin18));
  _74574 _74574_35 (
    .pin1(1'b0), .pin2(_74253_2_pin9), .pin3(_74253_2_pin7), .pin4(_74253_3_pin9), .pin5(_74253_3_pin7),
    .pin6(1'b0), .pin7(_74253_4_pin7), .pin8(_74253_5_pin9), .pin9(_7486_1_pin10), .pin10(1'b0),
    .pin11(_7402_1_pin1), .pin12(_74283_1_pin5), .pin13(_74283_1_pin3), .pin14(_74283_1_pin14),
    .pin15(_74283_1_pin12), .pin16(_74283_2_pin5), .pin17(_74283_2_pin3), .pin18(_74283_2_pin14),
    .pin19(_74283_2_pin12), .pin20(1'b1));
  Fuse fuse_419 (.A(_74541_19_pin11), .B(_74541_18_pin11));
  Fuse fuse_420 (.A(_74541_19_pin12), .B(_74541_18_pin12));
  Fuse fuse_421 (.A(_74541_19_pin13), .B(_74541_18_pin13));
  Fuse fuse_422 (.A(_74541_19_pin14), .B(_74541_18_pin14));
  Fuse fuse_423 (.A(_74541_20_pin11), .B(_74541_19_pin11));
  Fuse fuse_424 (.A(_74541_20_pin12), .B(_74541_19_pin12));
  Fuse fuse_425 (.A(_74541_20_pin13), .B(_74541_19_pin13));
  Fuse fuse_426 (.A(_74541_20_pin14), .B(_74541_19_pin14));
  Fuse fuse_427 (.A(_74541_21_pin11), .B(_74541_20_pin11));
  Fuse fuse_428 (.A(_74541_21_pin12), .B(_74541_20_pin12));
  Fuse fuse_429 (.A(_74541_21_pin13), .B(_74541_20_pin13));
  Fuse fuse_430 (.A(_74541_21_pin14), .B(_74541_20_pin14));
  Fuse fuse_431 (.A(fuse_431_a), .B(_74541_21_pin11));
  Fuse fuse_432 (.A(fuse_432_a), .B(_74541_21_pin12));
  Fuse fuse_433 (.A(fuse_433_a), .B(_74541_21_pin13));
  Fuse fuse_434 (.A(fuse_434_a), .B(_74541_21_pin14));
  Fuse fuse_435 (.A(_74541_19_pin15), .B(_74541_18_pin15));
  Fuse fuse_436 (.A(_74541_19_pin16), .B(_74541_18_pin16));
  Fuse fuse_437 (.A(_74541_19_pin17), .B(_74541_18_pin17));
  Fuse fuse_438 (.A(_74541_19_pin18), .B(_74541_18_pin18));
  Fuse fuse_439 (.A(_74541_20_pin15), .B(_74541_19_pin15));
  Fuse fuse_440 (.A(_74541_20_pin16), .B(_74541_19_pin16));
  Fuse fuse_441 (.A(_74541_20_pin17), .B(_74541_19_pin17));
  Fuse fuse_442 (.A(_74541_20_pin18), .B(_74541_19_pin18));
  Fuse fuse_443 (.A(_74541_21_pin15), .B(_74541_20_pin15));
  Fuse fuse_444 (.A(_74541_21_pin16), .B(_74541_20_pin16));
  Fuse fuse_445 (.A(_74541_21_pin17), .B(_74541_20_pin17));
  Fuse fuse_446 (.A(_74541_21_pin18), .B(_74541_20_pin18));
  Fuse fuse_447 (.A(fuse_447_a), .B(_74541_21_pin15));
  Fuse fuse_448 (.A(fuse_448_a), .B(_74541_21_pin16));
  Fuse fuse_449 (.A(fuse_449_a), .B(_74541_21_pin17));
  Fuse fuse_450 (.A(fuse_450_a), .B(_74541_21_pin18));
  _74574 _74574_36 (
    .pin1(1'b0), .pin2(_74574_36_pin2), .pin3(_74574_36_pin3), .pin4(_74574_36_pin4), .pin5(_74574_36_pin5),
    .pin6(_74574_36_pin6), .pin7(_74574_36_pin7), .pin8(_74574_36_pin8), .pin9(_7486_1_pin13), .pin10(1'b0),
    .pin11(_7402_1_pin1), .pin12(_74283_1_pin6), .pin13(_74283_1_pin2), .pin14(_74283_1_pin15),
    .pin15(_74283_1_pin11), .pin16(_74283_2_pin6), .pin17(_74283_2_pin2), .pin18(_74283_2_pin15),
    .pin19(_74283_2_pin11), .pin20(1'b1));
  _74253 _74253_7 (
    .pin1(1'b0), .pin2(fuse_431_a), .pin3(_74253_1_pin14[5]), .pin4(_74253_1_pin14[4]),
    .pin5(_74253_1_pin14[3]), .pin6(_74253_1_pin14[2]), .pin7(_74574_36_pin2), .pin8(1'b0), .pin9(1'b0),
    .pin10(_74574_36_pin3), .pin11(_74253_1_pin14[2]), .pin12(_74253_1_pin14[3]), .pin13(_74253_1_pin14[4]),
    .pin14(_74253_1_pin14[5]), .pin15(fuse_432_a), .pin16(1'b0));
  _74253 _74253_8 (
    .pin1(1'b0), .pin2(fuse_432_a), .pin3(_74253_1_pin14[5]), .pin4(_74253_1_pin14[4]),
    .pin5(_74253_1_pin14[3]), .pin6(_74253_1_pin14[2]), .pin7(_74574_36_pin3), .pin8(1'b0), .pin9(1'b0),
    .pin10(_74574_36_pin4), .pin11(_74253_1_pin14[2]), .pin12(_74253_1_pin14[3]), .pin13(_74253_1_pin14[4]),
    .pin14(_74253_1_pin14[5]), .pin15(fuse_433_a), .pin16(1'b0));
  _74253 _74253_9 (
    .pin1(1'b0), .pin2(fuse_433_a), .pin3(_74253_1_pin14[5]), .pin4(_74253_1_pin14[4]),
    .pin5(_74253_1_pin14[3]), .pin6(_74253_1_pin14[2]), .pin7(_74574_36_pin4), .pin8(1'b0), .pin9(1'b0),
    .pin10(1'b0), .pin11(1'b0), .pin12(1'b0), .pin13(1'b0), .pin14(_74253_2_pin4), .pin15(1'b0), .pin16(1'b1));
  _74253 _74253_10 (
    .pin1(1'b0), .pin2(fuse_434_a), .pin3(_74253_1_pin14[5]), .pin4(_74253_1_pin14[4]),
    .pin5(_74253_1_pin14[3]), .pin6(_74253_1_pin14[2]), .pin7(_74574_36_pin5), .pin8(1'b0), .pin9(1'b0),
    .pin10(1'b0), .pin11(1'b0), .pin12(1'b0), .pin13(1'b0), .pin14(_74253_3_pin6), .pin15(1'b0), .pin16(1'b1));
  _74253 _74253_11 (
    .pin1(1'b0), .pin2(fuse_447_a), .pin3(_74253_1_pin14[5]), .pin4(_74253_1_pin14[4]),
    .pin5(_74253_1_pin14[3]), .pin6(_74253_1_pin14[2]), .pin7(_74574_36_pin6), .pin8(1'b0), .pin9(1'b0),
    .pin10(_74574_36_pin7), .pin11(_74253_1_pin14[2]), .pin12(_74253_1_pin14[3]), .pin13(_74253_1_pin14[4]),
    .pin14(_74253_1_pin14[5]), .pin15(fuse_448_a), .pin16(1'b0));
  _74253 _74253_12 (
    .pin1(1'b0), .pin2(fuse_448_a), .pin3(_74253_1_pin14[5]), .pin4(_74253_1_pin14[4]),
    .pin5(_74253_1_pin14[3]), .pin6(_74253_1_pin14[2]), .pin7(_74574_36_pin7), .pin8(1'b0), .pin9(1'b0),
    .pin10(_74574_36_pin8), .pin11(_74253_1_pin14[2]), .pin12(_74253_1_pin14[3]), .pin13(_74253_1_pin14[4]),
    .pin14(_74253_1_pin14[5]), .pin15(fuse_449_a), .pin16(1'b0));
  _74253 _74253_13 (
    .pin1(1'b0), .pin2(fuse_449_a), .pin3(_74253_1_pin14[5]), .pin4(_74253_1_pin14[4]),
    .pin5(_74253_1_pin14[3]), .pin6(_74253_1_pin14[2]), .pin7(_74574_36_pin8), .pin8(1'b0), .pin9(1'b0),
    .pin10(_7486_1_pin13), .pin11(_74253_1_pin14[2]), .pin12(_74253_1_pin14[3]), .pin13(_74253_1_pin14[4]),
    .pin14(_74253_1_pin14[5]), .pin15(fuse_450_a), .pin16(1'b0));
  _74253 _74253_14 (
    .pin1(1'b0), .pin2(fuse_450_a), .pin3(_74253_1_pin14[5]), .pin4(_74253_1_pin14[4]),
    .pin5(_74253_1_pin14[3]), .pin6(_74253_1_pin14[2]), .pin7(_7486_1_pin13), .pin8(1'b0), .pin10(1'b0),
    .pin11(1'b0), .pin12(1'b0), .pin13(1'b0), .pin14(_74253_1_pin5), .pin15(1'b0), .pin16(1'b1));  // open: pin9

  // Notes on the sheet:
  //   clk: Hz: 10
  //   XFER
  //   AR/C
  //   MEM
  //   Pipeline
  //   Bus control
  //   load xfer
  //   dec reg
  //   inc reg
  //   RegTX
  //   assert xfer
  //   assert addr
  //   assert lhs/rhs
  //   ALU op
  //   ALU falgs
  //   assert main
  //   load main
  //   RegTl/TH
  //   main
  //   dev assert
  //   dev load
  //   MEM BRIDGE/CONST
  //   contents of ALU_Control (hex, n*v repeats v):
  //   0,10,20,c,4c,80,40,3,43,f,38,3e,36,33,30
  //   GPR
  //   ALU
  //   contents of 1A (hex, n*v repeats v):
  //   0,0,0,0,0,0,0,0,0,0,0,0,0,0,0,0,0,0,0,0,0,0,0,0,0,0,0,0,0,0,0,0,0,0,0,0,0,0,0,0,0, 0,0,0,0,
  //   0,0,0,0,0,0,0,0,0,0,0,0,0,0,0,0,0,0,0,0,0,0,0,0,0,0,0,0,0,0,0,0,0,0,0,0,0, 0,0,0,0,0,0,0,0,
  //   0,0,0,0,0,0,0,0,0,0,0,0,0,0,0,0,0,0,0,0,0,0,0,0,0,0,0,0,0,0,0,0,0, 0,0,0,0,e0,10,15,1a,1f,20,
  //   25,2a,2f,34,38,3c,31,39,3d,32,36,3e,33,37,3b,44,48,4c,41, 49,4d,42,46,4e,43,47,4b,50,55,5a,
  //   5f,60,65,6a,6f,74,78,7c,71,79,7d,72,76,7e,73,77, 7b,84,88,8c,81,89,8d,82,86,8e,83,87,8b,90,
  //   95,9a,9f,a4,a8,ac,a1,a9,ad,a2,a6,ae,a3, a7,ab,b4,b8,bc,b1,b9,bd,b2,b6,be,b3,b7,bb,c4,c8,cc,
  //   c1,c9,cd,c2,c6,ce,c3,c7,cb,c0, c5,ca,cf,d0,d5,da,df,74,78,7c,71,79,7d,72,76,7e,73,77,7b,a0,
  //   a5,aa,af,0,0,0,0,0,0, 0,0,0,0,0,0,0,0,0,0,0,0,0,0,0,0,0,0,0,0,0,0,0,0,0,0,0,0,0,0,0,0,0,0,0,
  //   0,0,0,0,0,0, 0,0,0,0,0,0,0,0,0,0,0,0,0,0,0,0,0,0,0,0,0,0,0,0,0,0,0,0,0,0,0,0,0,0,0,0,0,0,0,
  //   0,0, 0,0,0,0,0,0,0,0,0,0,0,0,0,0,0,0,0,0,0,0,0,0,0,0,0,0,0,0,0,0,0,0,0,0,0,0,0,0,0,e0, 10,15,
  //   1a,1f,20,25,2a,2f,34,38,3c,31,39,3d,32,36,3e,33,37,3b,44,48,4c,41,49,4d,42, 46,4e,43,47,4b,
  //   50,55,5a,5f,60,65,6a,6f,74,78,7c,71,79,7d,72,76,7e,73,77,7b,84,88, 8c,81,89,8d,82,86,8e,83,
  //   87,8b,90,95,9a,9f,a4,a8,ac,a1,a9,ad,a2,a6,ae,a3,a7,ab,b4, b8,bc,b1,b9,bd,b2,b6,be,b3,b7,bb,
  //   c4,c8,cc,c1,c9,cd,c2,c6,ce,c3,c7,cb,c0,c5,ca,cf, d0,d5,da,df,74,78,7c,71,79,7d,72,76,7e,73,
  //   77,7b,a0,a5,aa,af,0,0,0,0,0,0,0,0,0,0,0, 0,0,0,0,0,0,0,0,0,0,0,0,0,0,0,0,0,0,0,0,0,0,0,0,0,
  //   0,0,0,0,0,0,0,0,0,0,0,0,0,0,0,0, 0,0,0,0,0,0,0,0,0,0,0,0,0,0,0,0,0,0,0,0,0,0,0,0,0,0,0,0,0,
  //   0,0,0,0,0,0,0,0,0,0,0,0, 0,0,0,0,0,0,0,0,0,0,0,0,0,0,0,0,0,0,0,0,0,0,0,0,0,0,0,0,0,0,0,0,0,
  //   0,e0,10,15,1a,1f, 20,25,2a,2f,34,38,3c,31,39,3d,32,36,3e,33,37,3b,44,48,4c,41,49,4d,42,46,4e,
  //   43,47, 4b,50,55,5a,5f,60,65,6a,6f,74,78,7c,71,79,7d,72,76,7e,73,77,7b,84,88,8c,81,89,8d, 82,
  //   86,8e,83,87,8b,90,95,9a,9f,a4,a8,ac,a1,a9,ad,a2,a6,ae,a3,a7,ab,b4,b8,bc,b1,b9, bd,b2,b6,be,
  //   b3,b7,bb,c4,c8,cc,c1,c9,cd,c2,c6,ce,c3,c7,cb,c0,c5,ca,cf,d0,d5,da,df, 74,78,7c,71,79,7d,72,
  //   76,7e,73,77,7b,a0,a5,aa,af,0,0,0,0,0,0,0,0,0,0,0,0,0,0,0,0,0, 0,0,0,0,0,0,0,0,0,0,0,0,0,0,0,
  //   0,0,0,0,0,0,0,0,0,0,0,0,0,0,0,0,0,0,0,0,0,0,0,0,0,0, 0,0,0,0,0,0,0,0,0,0,0,0,0,0,0,0,0,0,0,
  //   0,0,0,0,0,0,0,0,0,0,0,0,0,0,0,0,0,0,0,0,0,0, 0,0,0,0,0,0,0,0,0,0,0,0,0,0,0,0,0,0,0,0,0,0,0,
  //   0,0,0,0,0,e0,10,15,1a,1f,20,25,2a,2f, 34,38,3c,31,39,3d,32,36,3e,33,37,3b,44,48,4c,41,49,4d,
  //   42,46,4e,43,47,4b,50,55,5a, 5f,60,65,6a,6f,74,78,7c,71,79,7d,72,76,7e,73,77,7b,84,88,8c,81,
  //   89,8d,82,86,8e,83, 87,8b,90,95,9a,9f,a4,a8,ac,a1,a9,ad,a2,a6,ae,a3,a7,ab,b4,b8,bc,b1,b9,bd,
  //   b2,b6,be, b3,b7,bb,c4,c8,cc,c1,c9,cd,c2,c6,ce,c3,c7,cb,c0,c5,ca,cf,d0,d5,da,df,74,78,7c,71,
  //    79,7d,72,76,7e,73,77,7b,a0,a5,aa,af,0,0,0,0,0,0,0,0,0,0,0,0,0,0,0,0,0,0,0,0,0,0,0, 0,0,0,0,
  //   0,0,0,0,0,0,0,0,0,0,0,0,0,0,0,0,0,0,0,0,0,0,0,0,0,0,0,0,0,0,0,0,0,0,0,0,0, 0,0,0,0,0,0,0,0,
  //   0,0,0,0,0,0,0,0,0,0,0,0,0,0,0,0,0,0,0,0,0,0,0,0,0,0,0,0,0,0,0,0,0, 0,0,0,0,0,0,0,0,0,0,0,0,
  //   0,0,0,0,0,0,0,0,0,0,e0,10,15,1a,1f,20,25,2a,2f,34,38,3c,31, 39,3d,32,36,3e,33,37,3b,44,48,4c,
  //   41,49,4d,42,46,4e,43,47,4b,50,55,5a,5f,60,65,6a, 6f,74,78,7c,71,79,7d,72,76,7e,73,77,7b,84,
  //   88,8c,81,89,8d,82,86,8e,83,87,8b,90,95, 9a,9f,a4,a8,ac,a1,a9,ad,a2,a6,ae,a3,a7,ab,b4,b8,bc,
  //   b1,b9,bd,b2,b6,be,b3,b7,bb,c4, c8,cc,c1,c9,cd,c2,c6,ce,c3,c7,cb,c0,c5,ca,cf,d0,d5,da,df,74,
  //   78,7c,71,79,7d,72,76, 7e,73,77,7b,a0,a5,aa,af,0,0,0,0,0,0,0,0,0,0,0,0,0,0,0,0,0,0,0,0,0,0,0,
  //   0,0,0,0,0,0, 0,0,0,0,0,0,0,0,0,0,0,0,0,0,0,0,0,0,0,0,0,0,0,0,0,0,0,0,0,0,0,0,0,0,0,0,0,0,0,
  //   0,0, 0,0,0,0,0,0,0,0,0,0,0,0,0,0,0,0,0,0,0,0,0,0,0,0,0,0,0,0,0,0,0,0,0,0,0,0,0,0,0,0,0, 0,0,
  //   0,0,0,0,0,0,0,0,0,0,0,0,0,0,e0,10,15,1a,1f,20,25,2a,2f,34,38,3c,31,39,3d,32,36, 3e,33,37,3b,
  //   44,48,4c,41,49,4d,42,46,4e,43,47,4b,50,55,5a,5f,60,65,6a,6f,74,78,7c, 71,79,7d,72,76,7e,73,
  //   77,7b,84,88,8c,81,89,8d,82,86,8e,83,87,8b,90,95,9a,9f,a4,a8, ac,a1,a9,ad,a2,a6,ae,a3,a7,ab,
  //   b4,b8,bc,b1,b9,bd,b2,b6,be,b3,b7,bb,c4,c8,cc,c1,c9, cd,c2,c6,ce,c3,c7,cb,c0,c5,ca,cf,d0,d5,
  //   da,df,74,78,7c,71,79,7d,72,76,7e,73,77,7b, a0,a5,aa,af,0,0,0,0,0,0,0,0,0,0,0,0,0,0,0,0,0,0,
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  //   contents of 2B (hex, n*v repeats v):
  //   4,4,4,4,4,4,4,4,4,4,4,4,4,4,4,4,4,4,4,4,4,4,4,4,4,4,4,4,4,4,4,4,4,4,4,4,4,4,4,4,4, 4,4,4,4,
  //   4,4,4,4,4,4,4,5,6,7,4,4,4,4,4,4,4,4,4,30,30,30,30,34,34,34,34,38,38,38,38, 30,30,30,30,34,34,
  //   34,34,38,38,38,38,4,4,4,32,48,48,48,24,4,4,4,4,4,4,4,4,4,4,4,4, 4,4,4,4,4,4,2c,2c,2c,2c,2c,
  //   2c,2d,2d,2d,2d,2d,2d,4,4,4,4,4,4,4,4,4,4,4,4,4,4,4,4,4, 4,4,4,4,4,4,4,4,4,4,4,4,4,4,4,4,4,4,
  //   4,4,4,4,4,4,4,4,4,4,4,4,4,4,4,4,4,4,4,4,4,4,4, 4,4,4,4,4,4,4,4,4,4,4,4,4,4,4,4,4,4,4,4,4,4,
  //   4,4,4,4,4,4,4,4,4,4,4,4,4,4,4,4,4,4,4, 4,4,4,4,4,4,4,4,4,4,4,4,4,4,4,4,4,4,4,4,4,4,4,4,4,4,
  //   4,4,4,4,4,4,4,4,4,4,4,4,4,4,4, 4,4,4,4,4,4,4,4,4,4,4,4,4,4,4,4,4,4,4,4,4,4,4,4,4,4,4,4,4,4,
  //   4,4,4,4,4,4,4,4,4,4,4, 4,5,6,7,4,4,4,4,4,4,4,4,4,30,30,30,30,34,34,34,34,38,38,38,38,30,30,
  //   30,30,34,34,34, 34,38,38,38,38,4,4,4,32,48,48,48,24,4,4,4,4,4,4,4,4,4,4,4,4,4,4,4,4,4,4,2c,
  //   2c,2c, 2c,2c,2c,2d,2d,2d,2d,2d,2d,4,4,4,4,4,4,4,4,4,4,4,4,4,4,4,4,4,4,4,4,4,4,4,4,4,4,4, 4,
  //   4,4,4,4,4,4,4,4,4,4,4,4,4,4,4,4,4,4,4,4,4,4,4,4,4,4,4,4,4,4,4,4,4,4,4,4,4,4,4,4, 4,4,4,4,4,
  //   4,4,4,4,4,4,4,4,4,4,4,4,4,4,4,4,4,4,4,4,4,4,4,4,4,4,4,4,4,4,4,4,4,4,4,4, 4,4,4,4,4,4,4,4,4,
  //   4,4,4,4,4,4,4,4,4,4,4,4,4,4,4,4,4,4,4,4,4,4,4,4,4,4,4,4,4,4,4,4, 4,4,4,4,4,4,4,4,4,4,4,4,4,
  //   4,4,4,4,4,4,4,4,4,4,4,4,4,4,4,4,4,4,4,5,6,7,4,4,4,4,4,4, 4,4,4,30,30,30,30,34,34,34,34,38,38,
  //   38,38,30,30,30,30,34,34,34,34,38,38,38,38,4,4, 4,32,48,48,48,24,4,4,4,4,4,4,4,4,4,4,4,4,4,4,
  //   4,4,4,4,2c,2c,2c,2c,2c,2c,2d,2d,2d,2d, 2d,2d,4,4,4,4,4,4,4,4,4,4,4,4,4,4,4,4,4,4,4,4,4,4,4,
  //   4,4,4,4,4,4,4,4,4,4,4,4,4,4,4, 4,4,4,4,4,4,4,4,4,4,4,4,4,4,4,4,4,4,4,4,4,4,4,4,4,4,4,4,4,4,
  //   4,4,4,4,4,4,4,4,4,4,4, 4,4,4,4,4,4,4,4,4,4,4,4,4,4,4,4,4,4,4,4,4,4,4,4,4,4,4,4,4,4,4,4,4,4,
  //   4,4,4,4,4,4,4, 4,4,4,4,4,4,4,4,4,4,4,4,4,4,4,4,4,4,4,4,4,4,4,4,4,4,4,4,4,4,4,4,4,4,4,4,4,4,
  //   4,4,4, 4,4,4,4,4,4,4,4,4,4,4,4,4,4,4,4,4,4,4,4,4,5,6,7,4,4,4,4,4,4,4,4,4,30,30,30,30,34, 34,
  //   34,34,38,38,38,38,30,30,30,30,34,34,34,34,38,38,38,38,4,4,4,32,48,48,48,24,4,4, 4,4,4,4,4,4,
  //   4,4,4,4,4,4,4,4,4,4,2c,2c,2c,2c,2c,2c,2d,2d,2d,2d,2d,2d,4,4,4,4,4,4,4, 4,4,4,4,4,4,4,4,4,4,
  //   4,4,4,4,4,4,4,4,4,4,4,4,4,4,4,4,4,4,4,4,4,4,4,4,4,4,4,4,4,4,4, 4,4,4,4,4,4,4,4,4,4,4,4,4,4,
  //   4,4,4,4,4,4,4,4,4,4,4,4,4,4,4,4,4,4,4,4,4,4,4,4,4,4,4, 4,4,4,4,4,4,4,4,4,4,4,4,4,4,4,4,4,4,
  //   4,4,4,4,4,4,4,4,4,4,4,4,4,4,4,4,4,4,4,4,4,4,4, 4,4,4,4,4,4,4,4,4,4,4,4,4,4,4,4,4,4,4,4,4,4,
  //   4,4,4,4,4,4,4,4,4,4,4,4,4,4,4,4,4,4,4, 4,4,4,4,4,4,4,4,4,4,4,5,6,7,4,4,4,4,4,4,4,4,4,30,30,
  //   30,30,34,34,34,34,38,38,38,38, 30,30,30,30,34,34,34,34,38,38,38,38,4,4,4,32,48,48,48,24,4,4,
  //   4,4,4,4,4,4,4,4,4,4, 4,4,4,4,4,4,2c,2c,2c,2c,2c,2c,2d,2d,2d,2d,2d,2d,4,4,4,4,4,4,4,4,4,4,4,
  //   4,4,4,4,4,4, 4,4,4,4,4,4,4,4,4,4,4,4,4,4,4,4,4,4,4,4,4,4,4,4,4,4,4,4,4,4,4,4,4,4,4,4,4,4,4,
  //   4,4, 4,4,4,4,4,4,4,4,4,4,4,4,4,4,4,4,4,4,4,4,4,4,4,4,4,4,4,4,4,4,4,4,4,4,4,4,4,4,4,4,4, 4,4,
  //   4,4,4,4,4,4,4,4,4,4,4,4,4,4,4,4,4,4,4,4,4,4,4,4,4,4,4,4,4,4,4,4,4,4,4,4,4,4,4, 4,4,4,4,4,4,
  //   4,4,4,4,4,4,4,4,4,4,4,4,4,4,4,4,4,4,4,4,4,4,4,4,4,4,4,4,4,4,4,4,4,4,4, 4,5,6,7,4,4,4,4,4,4,
  //   4,4,4,30,30,30,30,34,34,34,34,38,38,38,38,30,30,30,30,34,34,34, 34,38,38,38,38,4,4,4,32,48,
  //   48,48,24,4,4,4,4,4,4,4,4,4,4,4,4,4,4,4,4,4,4,2c,2c,2c, 2c,2c,2c,2d,2d,2d,2d,2d,2d,4,4,4,4,4,
  //   4,4,4,4,4,4,4,4,4,4,4,4,4,4,4,4,4,4,4,4,4,4, 4,4,4,4,4,4,4,4,4,4,4,4,4,4,4,4,4,4,4,4,4,4,4,
  //   4,4,4,4,4,4,4,4,4,4,4,4,4,4,4,4,4,4, 4,4,4,4,4,4,4,4,4,4,4,4,4,4,4,4,4,4,4,4,4,4,4,4,4,4,4,
  //   4,4,4,4,4,4,4,4,4,4,4,4,4,4, 4,4,4,4,4,4,4,4,4,4,4,4,4,4,4,4,4,4,4,4,4,4,4,4,4,4,4,4,4,4,4,
  //   4,4,4,4,4,4,4,4,4,4, 4,4,4,4,4,4,4,4,4,4,4,4,4,4,4,4,4,4,4,4,4,4,4,4,4,4,4,4,4,4,4,4,5,6,7,
  //   4,4,4,4,4,4, 4,4,4,30,30,30,30,34,34,34,34,38,38,38,38,30,30,30,30,34,34,34,34,38,38,38,38,
  //   4,4, 4,32,48,48,48,24,4,4,4,4,4,4,4,4,4,4,4,4,4,4,4,4,4,4,2c,2c,2c,2c,2c,2c,2d,2d,2d,2d, 2d,
  //   2d,4,4,4,4,4,4,4,4,4,4,4,4,4,4,4,4,4,4,4,4,4,4,4,4,4,4,4,4,4,4,4,4,4,4,4,4,4,4, 4,4,4,4,4,4,
  //   4,4,4,4,4,4,4,4,4,4,4,4,4,4,4,4,4,4,4,4,4,4,4,4,4,4,4,4,4,4,4,4,4,4,4, 4,4,4,4,4,4,4,4,4,4,
  //   4,4,4,4,4,4,4,4,4,4,4,4,4,4,4,4,4,4,4,4,4,4,4,4,4,4,4,4,4,4,4, 4,4,4,4,4,4,4,4,4,4,4,4,4,4,
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  //   contents of 1B (hex, n*v repeats v):
  //   0,88,88,88,88,88,88,0,0,0,0,0,0,0,0,0,0,0,0,0,0,0,0,0,0,0,0,0,0,0,0,0,0,0,0,62,26, 63,36,64,
  //   46,65,56,45,54,34,35,0,a,b,c,d,0,0,0,0,0,0,0,0,0,0,0,0,0,0,0,0,0,0,0,0,0, 0,0,0,0,0,0,0,0,0,
  //   0,0,0,0,0,0,0,0,0,0,62,52,0,0,61,0,61,0,61,0,61,0,61,0,61,0,61, 0,61,0,61,51,b,b,b,b,b,b,0,
  //   0,0,0,0,0,0,0,0,0,0,0,0,0,0,0,0,0,0,0,0,0,0,0,0,0,0,0, 0,0,0,0,0,0,0,0,0,0,0,0,0,0,0,0,0,0,
  //   0,0,0,0,0,0,0,0,0,0,0,0,0,0,0,0,0,0,0,0,0,0,0, 0,0,0,0,0,0,0,0,0,0,0,0,0,0,0,0,0,0,0,0,0,0,
  //   0,0,0,0,0,0,0,0,0,0,0,0,0,0,0,0,0,0,0, 0,0,0,0,0,0,0,0,0,0,0,0,0,0,0,0,0,0,0,0,0,0,0,0,0,0,
  //   0,88,88,88,88,88,88,0,0,0,0,0, 0,0,0,0,0,0,0,0,0,0,0,0,0,0,0,0,0,0,0,0,0,0,0,62,26,63,36,64,
  //   46,65,56,45,54,34,35, 0,a,b,c,d,0,0,0,0,0,0,0,0,0,0,0,0,0,0,0,0,0,0,0,0,0,0,0,0,0,0,0,0,0,0,
  //   0,0,0,0,0,0, 0,0,0,0,62,52,0,0,61,61,0,0,61,0,61,0,61,0,61,61,0,61,61,0,61,51,b,b,b,b,b,b,0,
  //   0, 0,0,0,0,0,0,0,0,0,0,0,0,0,0,0,0,0,0,0,0,0,0,0,0,0,0,0,0,0,0,0,0,0,0,0,0,0,0,0,0,0, 0,0,0,
  //   0,0,0,0,0,0,0,0,0,0,0,0,0,0,0,0,0,0,0,0,0,0,0,0,0,0,0,0,0,0,0,0,0,0,0,0,0,0, 0,0,0,0,0,0,0,
  //   0,0,0,0,0,0,0,0,0,0,0,0,0,0,0,0,0,0,0,0,0,0,0,0,0,0,0,0,0,0,0,0,0,0, 0,0,0,0,0,0,0,0,0,0,0,
  //   0,88,88,88,88,88,88,0,0,0,0,0,0,0,0,0,0,0,0,0,0,0,0,0,0,0,0, 0,0,0,0,0,0,0,0,62,26,63,36,64,
  //   46,65,56,45,54,34,35,0,a,b,c,d,0,0,0,0,0,0,0,0,0,0, 0,0,0,0,0,0,0,0,0,0,0,0,0,0,0,0,0,0,0,0,
  //   0,0,0,0,0,0,0,0,0,0,62,52,0,0,61,0,61,61, 0,0,61,0,61,0,61,61,0,61,0,0,61,51,b,b,b,b,b,b,0,
  //   0,0,0,0,0,0,0,0,0,0,0,0,0,0,0,0, 0,0,0,0,0,0,0,0,0,0,0,0,0,0,0,0,0,0,0,0,0,0,0,0,0,0,0,0,0,
  //   0,0,0,0,0,0,0,0,0,0,0,0, 0,0,0,0,0,0,0,0,0,0,0,0,0,0,0,0,0,0,0,0,0,0,0,0,0,0,0,0,0,0,0,0,0,
  //   0,0,0,0,0,0,0,0, 0,0,0,0,0,0,0,0,0,0,0,0,0,0,0,0,0,0,0,0,0,0,0,0,0,0,0,0,0,0,0,0,0,0,0,0,0,
  //   0,88,88, 88,88,88,88,0,0,0,0,0,0,0,0,0,0,0,0,0,0,0,0,0,0,0,0,0,0,0,0,0,0,0,0,62,26,63,36,64,
  //    46,65,56,45,54,34,35,0,a,b,c,d,0,0,0,0,0,0,0,0,0,0,0,0,0,0,0,0,0,0,0,0,0,0,0,0,0, 0,0,0,0,
  //   0,0,0,0,0,0,0,0,0,0,0,62,52,0,0,61,61,0,61,0,0,61,0,61,0,61,0,61,0,0,0,61, 51,b,b,b,b,b,b,0,
  //   0,0,0,0,0,0,0,0,0,0,0,0,0,0,0,0,0,0,0,0,0,0,0,0,0,0,0,0,0,0,0,0, 0,0,0,0,0,0,0,0,0,0,0,0,0,
  //   0,0,0,0,0,0,0,0,0,0,0,0,0,0,0,0,0,0,0,0,0,0,0,0,0,0,0,0, 0,0,0,0,0,0,0,0,0,0,0,0,0,0,0,0,0,
  //   0,0,0,0,0,0,0,0,0,0,0,0,0,0,0,0,0,0,0,0,0,0,0,0, 0,0,0,0,0,0,0,0,0,0,0,0,0,0,0,0,0,0,0,0,0,
  //   0,88,88,88,88,88,88,0,0,0,0,0,0,0,0,0,0, 0,0,0,0,0,0,0,0,0,0,0,0,0,0,0,0,0,0,62,26,63,36,64,
  //   46,65,56,45,54,34,35,0,a,b,c,d, 0,0,0,0,0,0,0,0,0,0,0,0,0,0,0,0,0,0,0,0,0,0,0,0,0,0,0,0,0,0,
  //   0,0,0,0,0,0,0,0,0,0,62, 52,0,0,61,0,61,0,61,61,0,0,61,61,0,0,61,61,0,0,61,51,b,b,b,b,b,b,0,
  //   0,0,0,0,0,0,0, 0,0,0,0,0,0,0,0,0,0,0,0,0,0,0,0,0,0,0,0,0,0,0,0,0,0,0,0,0,0,0,0,0,0,0,0,0,0,
  //   0,0,0, 0,0,0,0,0,0,0,0,0,0,0,0,0,0,0,0,0,0,0,0,0,0,0,0,0,0,0,0,0,0,0,0,0,0,0,0,0,0,0,0,0, 0,
  //   0,0,0,0,0,0,0,0,0,0,0,0,0,0,0,0,0,0,0,0,0,0,0,0,0,0,0,0,0,0,0,0,0,0,0,0,0,0,0,0, 0,0,0,0,0,
  //   0,88,88,88,88,88,88,0,0,0,0,0,0,0,0,0,0,0,0,0,0,0,0,0,0,0,0,0,0,0,0,0,0, 0,0,62,26,63,36,64,
  //   46,65,56,45,54,34,35,0,a,b,c,d,0,0,0,0,0,0,0,0,0,0,0,0,0,0,0,0, 0,0,0,0,0,0,0,0,0,0,0,0,0,0,
  //   0,0,0,0,0,0,0,0,0,0,62,52,0,0,61,61,0,0,61,61,0,0,61, 61,0,61,0,61,0,0,61,51,b,b,b,b,b,b,0,
  //   0,0,0,0,0,0,0,0,0,0,0,0,0,0,0,0,0,0,0,0,0,0, 0,0,0,0,0,0,0,0,0,0,0,0,0,0,0,0,0,0,0,0,0,0,0,
  //   0,0,0,0,0,0,0,0,0,0,0,0,0,0,0,0,0,0, 0,0,0,0,0,0,0,0,0,0,0,0,0,0,0,0,0,0,0,0,0,0,0,0,0,0,0,
  //   0,0,0,0,0,0,0,0,0,0,0,0,0,0, 0,0,0,0,0,0,0,0,0,0,0,0,0,0,0,0,0,0,0,0,0,0,0,0,0,0,0,0,0,0,0,
  //   0,88,88,88,88,88,88, 0,0,0,0,0,0,0,0,0,0,0,0,0,0,0,0,0,0,0,0,0,0,0,0,0,0,0,0,62,26,63,36,64,
  //   46,65,56,45, 54,34,35,0,a,b,c,d,0,0,0,0,0,0,0,0,0,0,0,0,0,0,0,0,0,0,0,0,0,0,0,0,0,0,0,0,0,0,
  //   0, 0,0,0,0,0,0,0,0,0,62,52,0,0,61,0,61,61,0,61,0,0,61,61,0,61,0,61,0,0,61,51,b,b,b,b, b,b,0,
  //   0,0,0,0,0,0,0,0,0,0,0,0,0,0,0,0,0,0,0,0,0,0,0,0,0,0,0,0,0,0,0,0,0,0,0,0,0,0, 0,0,0,0,0,0,0,
  //   0,0,0,0,0,0,0,0,0,0,0,0,0,0,0,0,0,0,0,0,0,0,0,0,0,0,0,0,0,0,0,0,0,0, 0,0,0,0,0,0,0,0,0,0,0,
  //   0,0,0,0,0,0,0,0,0,0,0,0,0,0,0,0,0,0,0,0,0,0,0,0,0,0,0,0,0,0, 0,0,0,0,0,0,0,0,0,0,0,0,0,0,0,
  //   0,88,88,88,88,88,88,0,0,0,0,0,0,0,0,0,0,0,0,0,0,0,0, 0,0,0,0,0,0,0,0,0,0,0,0,62,26,63,36,64,
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  //   contents of ROM (hex, n*v repeats v):
  //   0,5,2f,6,0,27,5,14,6,0,5c,0,0,0,5,1,6,0,5f,60,2a,72,76,77,0,5,22,6,0,29,5,29,6,0, 5b,fc,5f,
  //   65,39,5f,71,7d,7c,78,29,5e,0,48,65,6c,6c,6f,20,57,6f,72,6c,64,21,a
  //   contents of 2A (hex, n*v repeats v):
  //   0,15,25,35,45,65,75,12,13,14,21,23,24,31,32,34,41,42,43,61,62,63,64,71,72,73,74,16, 26,36,46,
  //   17,27,37,47,0,0,0,0,0,0,0,0,0,0,0,0,0,0,0,0,0,0,0,0,e1,d1,91,0,0,0,0,0,0, 1f,2f,3f,4f,1f,2f,
  //   3f,4f,1f,2f,3f,4f,f1,f2,f3,f4,f1,f2,f3,f4,f1,f2,f3,f4,0,0,0,1f, 0,0,0,0,0,0,0,0,0,0,0,0,0,0,
  //   0,0,0,0,0,0,0,0,f1,f2,f3,f4,f6,f7,1f,2f,3f,4f,6f,7f,0, 0,18,28,38,48,18,28,38,48,18,18,18,28,
  //   28,28,38,38,38,48,48,48,18,18,18,28,28,28,38, 38,38,48,48,48,18,28,38,48,18,28,38,48,18,18,
  //   18,28,28,28,38,38,38,48,48,48,18,18, 18,28,28,28,38,38,38,48,48,48,18,28,38,48,18,18,18,28,
  //   28,28,38,38,38,48,48,48,18, 18,18,28,28,28,38,38,38,48,48,48,18,18,18,28,28,28,38,38,38,48,
  //   48,48,18,28,38,48, 18,28,38,48,0,0,0,0,0,0,0,0,0,0,0,0,0,0,0,0,0,15,25,35,45,65,75,12,13,14,
  //   21,23,24, 31,32,34,41,42,43,61,62,63,64,71,72,73,74,16,26,36,46,17,27,37,47,0,0,0,0,0,0,0,0,
  //    0,0,0,0,0,0,0,0,0,0,0,0,e1,d1,91,0,0,0,0,0,0,1f,2f,3f,4f,1f,2f,3f,4f,1f,2f,3f,4f, f1,f2,f3,
  //   f4,f1,f2,f3,f4,f1,f2,f3,f4,0,0,0,1f,0,0,0,0,0,0,0,0,0,0,0,0,0,0,0,0,0,0, 0,0,0,0,f1,f2,f3,f4,
  //   f6,f7,1f,2f,3f,4f,6f,7f,0,0,18,28,38,48,18,28,38,48,18,18,18, 28,28,28,38,38,38,48,48,48,18,
  //   18,18,28,28,28,38,38,38,48,48,48,18,28,38,48,18,28, 38,48,18,18,18,28,28,28,38,38,38,48,48,
  //   48,18,18,18,28,28,28,38,38,38,48,48,48,18, 28,38,48,18,18,18,28,28,28,38,38,38,48,48,48,18,
  //   18,18,28,28,28,38,38,38,48,48,48, 18,18,18,28,28,28,38,38,38,48,48,48,18,28,38,48,18,28,38,
  //   48,0,0,0,0,0,0,0,0,0,0,0, 0,0,0,0,0,0,15,25,35,45,65,75,12,13,14,21,23,24,31,32,34,41,42,43,
  //   61,62,63,64,71, 72,73,74,16,26,36,46,17,27,37,47,0,0,0,0,0,0,0,0,0,0,0,0,0,0,0,0,0,0,0,0,e1,
  //   d1,91, 0,0,0,0,0,0,1f,2f,3f,4f,1f,2f,3f,4f,1f,2f,3f,4f,f1,f2,f3,f4,f1,f2,f3,f4,f1,f2,f3, f4,
  //   0,0,0,1f,0,0,0,0,0,0,0,0,0,0,0,0,0,0,0,0,0,0,0,0,0,0,f1,f2,f3,f4,f6,f7,1f,2f,3f, 4f,6f,7f,0,
  //   0,18,28,38,48,18,28,38,48,18,18,18,28,28,28,38,38,38,48,48,48,18,18,18, 28,28,28,38,38,38,48,
  //   48,48,18,28,38,48,18,28,38,48,18,18,18,28,28,28,38,38,38,48, 48,48,18,18,18,28,28,28,38,38,
  //   38,48,48,48,18,28,38,48,18,18,18,28,28,28,38,38,38, 48,48,48,18,18,18,28,28,28,38,38,38,48,
  //   48,48,18,18,18,28,28,28,38,38,38,48,48,48, 18,28,38,48,18,28,38,48,0,0,0,0,0,0,0,0,0,0,0,0,
  //   0,0,0,0,0,15,25,35,45,65,75,12,13, 14,21,23,24,31,32,34,41,42,43,61,62,63,64,71,72,73,74,16,
  //   26,36,46,17,27,37,47,0,0, 0,0,0,0,0,0,0,0,0,0,0,0,0,0,0,0,0,0,e1,d1,91,0,0,0,0,0,0,1f,2f,3f,
  //   4f,1f,2f,3f,4f, 1f,2f,3f,4f,f1,f2,f3,f4,f1,f2,f3,f4,f1,f2,f3,f4,0,0,0,1f,0,0,0,0,0,0,0,0,0,
  //   0,0,0, 0,0,0,0,0,0,0,0,0,0,f1,f2,f3,f4,f6,f7,1f,2f,3f,4f,6f,7f,0,0,18,28,38,48,18,28,38, 48,
  //   18,18,18,28,28,28,38,38,38,48,48,48,18,18,18,28,28,28,38,38,38,48,48,48,18,28, 38,48,18,28,
  //   38,48,18,18,18,28,28,28,38,38,38,48,48,48,18,18,18,28,28,28,38,38,38, 48,48,48,18,28,38,48,
  //   18,18,18,28,28,28,38,38,38,48,48,48,18,18,18,28,28,28,38,38, 38,48,48,48,18,18,18,28,28,28,
  //   38,38,38,48,48,48,18,28,38,48,18,28,38,48,0,0,0,0,0, 0,0,0,0,0,0,0,0,0,0,0,0,15,25,35,45,65,
  //   75,12,13,14,21,23,24,31,32,34,41,42,43,61, 62,63,64,71,72,73,74,16,26,36,46,17,27,37,47,0,0,
  //   0,0,0,0,0,0,0,0,0,0,0,0,0,0,0,0, 0,0,e1,d1,91,0,0,0,0,0,0,1f,2f,3f,4f,1f,2f,3f,4f,1f,2f,3f,
  //   4f,f1,f2,f3,f4,f1,f2,f3, f4,f1,f2,f3,f4,0,0,0,1f,0,0,0,0,0,0,0,0,0,0,0,0,0,0,0,0,0,0,0,0,0,
  //   0,f1,f2,f3,f4,f6, f7,1f,2f,3f,4f,6f,7f,0,0,18,28,38,48,18,28,38,48,18,18,18,28,28,28,38,38,
  //   38,48,48, 48,18,18,18,28,28,28,38,38,38,48,48,48,18,28,38,48,18,28,38,48,18,18,18,28,28,28,
  //    38,38,38,48,48,48,18,18,18,28,28,28,38,38,38,48,48,48,18,28,38,48,18,18,18,28,28, 28,38,38,
  //   38,48,48,48,18,18,18,28,28,28,38,38,38,48,48,48,18,18,18,28,28,28,38,38, 38,48,48,48,18,28,
  //   38,48,18,28,38,48,0,0,0,0,0,0,0,0,0,0,0,0,0,0,0,0,0,15,25,35,45, 65,75,12,13,14,21,23,24,31,
  //   32,34,41,42,43,61,62,63,64,71,72,73,74,16,26,36,46,17, 27,37,47,0,0,0,0,0,0,0,0,0,0,0,0,0,0,
  //   0,0,0,0,0,0,e1,d1,91,0,0,0,0,0,0,1f,2f,3f,4f, 1f,2f,3f,4f,1f,2f,3f,4f,f1,f2,f3,f4,f1,f2,f3,
  //   f4,f1,f2,f3,f4,0,0,0,1f,0,0,0,0,0,0, 0,0,0,0,0,0,0,0,0,0,0,0,0,0,0,0,f1,f2,f3,f4,f6,f7,1f,2f,
  //   3f,4f,6f,7f,0,0,18,28,38, 48,18,28,38,48,18,18,18,28,28,28,38,38,38,48,48,48,18,18,18,28,28,
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endmodule
