// Digital circuit Memory Bridge.dig as structural Verilog
module Memory_Bridge (
  input  [3:0] Control,
  output [7:0] MAIN,
  output [7:0] MEM
);

  _74541 _74541_1 (
    .pin1(Control[1]), .pin2(MEM[0]), .pin3(MEM[1]), .pin4(MEM[2]), .pin5(MEM[3]), .pin6(MEM[4]),
    .pin7(MEM[5]), .pin8(MEM[6]), .pin9(MEM[7]), .pin10(1'b0), .pin11(MAIN[7]), .pin12(MAIN[6]),
    .pin13(MAIN[5]), .pin14(MAIN[4]), .pin15(MAIN[3]), .pin16(MAIN[2]), .pin17(MAIN[1]), .pin18(MAIN[0]),
    .pin19(1'b0), .pin20(1'b1));
  _74541 _74541_2 (
    .pin1(Control[2]), .pin2(MAIN[0]), .pin3(MAIN[1]), .pin4(MAIN[2]), .pin5(MAIN[3]), .pin6(MAIN[4]),
    .pin7(MAIN[5]), .pin8(MAIN[6]), .pin9(MAIN[7]), .pin10(1'b0), .pin11(MEM[7]), .pin12(MEM[6]),
    .pin13(MEM[5]), .pin14(MEM[4]), .pin15(MEM[3]), .pin16(MEM[2]), .pin17(MEM[1]), .pin18(MEM[0]),
    .pin19(1'b0), .pin20(1'b1));

  // Other names for the same wires on the sheet: MainBus[7:0] = MAIN; MemData[7:0] = MEM;
  //   MemBridge_Assert = Control[1]; MemBridge_Dir = Control[2]

  // Notes on the sheet:
  //   Control: 0: Assert
  //   1: Load
  //   2: Dir
  //   3: Ack, default 1
endmodule
