// Digital circuit Memory.dig as structural Verilog
module Memory (
  input  [15:0] ADDR,
  input  [3:0] Control,
  output [7:0] MEM
);

  wire _7404_1_pin4, _7404_1_pin5, _7404_1_pin6, OutputEnabled, RamCE, RamWE, RomCE;

  LY62256 RAM (
    .nCE(RamCE), .nOE(OutputEnabled), .nWE(RamWE), .VCC(1'b1), .GND(1'b0), .I_O0(MEM[0]), .I_O1(MEM[1]),
    .I_O2(MEM[2]), .I_O3(MEM[3]), .I_O4(MEM[4]), .I_O5(MEM[5]), .I_O6(MEM[6]), .I_O7(MEM[7]), .A0(ADDR[0]),
    .A1(ADDR[1]), .A2(ADDR[2]), .A3(ADDR[3]), .A4(ADDR[4]), .A5(ADDR[5]), .A6(ADDR[6]), .A7(ADDR[7]),
    .A8(ADDR[8]), .A9(ADDR[9]), .A10(ADDR[10]), .A11(ADDR[11]), .A12(ADDR[12]), .A13(ADDR[13]), .A14(ADDR[14]));
  _28c256_programmable ROM (
    .nCE(RomCE), .nOE(OutputEnabled), .nWE(1'b1), .VCC(1'b1), .GND(1'b0), .I_O0(MEM[0]), .I_O1(MEM[1]),
    .I_O2(MEM[2]), .I_O3(MEM[3]), .I_O4(MEM[4]), .I_O5(MEM[5]), .I_O6(MEM[6]), .I_O7(MEM[7]), .A0(ADDR[0]),
    .A1(ADDR[1]), .A2(ADDR[2]), .A3(ADDR[3]), .A4(ADDR[4]), .A5(ADDR[5]), .A6(ADDR[6]), .A7(ADDR[7]),
    .A8(ADDR[8]), .A9(ADDR[9]), .A10(ADDR[10]), .A11(ADDR[11]), .A12(ADDR[12]), .A13(ADDR[13]), .A14(ADDR[14]));
  _74138 _74138_1 (
    .pin1(ADDR[15]), .pin2(1'b0), .pin3(1'b0), .pin4(1'b0), .pin5(1'b0), .pin6(1'b1), .pin8(1'b0),
    .pin14(RamCE), .pin15(RomCE), .pin16(1'b1));  // open: pin7, pin9, pin10, pin11, pin12, pin13
  _7404 _7404_1 (
    .pin1(Control[2]), .pin2(OutputEnabled), .pin3(Control[1]), .pin4(_7404_1_pin4), .pin5(_7404_1_pin5),
    .pin6(_7404_1_pin6), .pin7(1'b0), .pin8(RamWE), .pin9(_7404_1_pin6), .pin10(_7404_1_pin5),
    .pin11(_7404_1_pin4), .pin13(1'b1), .pin14(1'b1));  // open: pin12

  // Other names for the same wires on the sheet: MemData[7:0] = MEM; Addr_t[14:0] = ADDR[14:0];
  //   MemBridge_Load = Control[1]; MemBridge_Dir = Control[2]

  // Notes on the sheet:
  //   Control: 0: Assert
  //   1: Load
  //   2: Dir
  //   3: Ack, default 1
  //   contents of ROM (hex, n*v repeats v):
  //   1,2,3,4,5,6,7
endmodule
