// Digital circuit Fetch.dig as structural Verilog
module Fetch (
  input  [7:0] MEM,
  input  [1:0] Control,
  input  [6:0] Flags,
  input  Clock,
  input  [1:0] PCRA,
  output [7:0] PipeOut
);

  wire _7404_1_pin2, _74574_1_pin12, _74574_1_pin13, _74574_1_pin14, _74574_1_pin15, _74574_1_pin16,
       _74574_1_pin17, _74574_1_pin18, _74574_1_pin19;

  _74574 _74574_1 (
    .pin1(1'b0), .pin2(MEM[0]), .pin3(MEM[1]), .pin4(MEM[2]), .pin5(MEM[3]), .pin6(MEM[4]), .pin7(MEM[5]),
    .pin8(MEM[6]), .pin9(MEM[7]), .pin10(1'b0), .pin11(Clock), .pin12(_74574_1_pin12),
    .pin13(_74574_1_pin13), .pin14(_74574_1_pin14), .pin15(_74574_1_pin15), .pin16(_74574_1_pin16),
    .pin17(_74574_1_pin17), .pin18(_74574_1_pin18), .pin19(_74574_1_pin19), .pin20(1'b1));
  _74153 _74153_1 (
    .pin1(1'b0), .pin2(Control[1]), .pin3(_74574_1_pin18), .pin4(1'b0), .pin5(1'b0), .pin6(MEM[1]),
    .pin7(PipeOut[1]), .pin8(1'b0), .pin9(PipeOut[0]), .pin10(MEM[0]), .pin11(1'b0), .pin12(1'b0),
    .pin13(_74574_1_pin19), .pin14(Control[0]), .pin15(1'b0), .pin16(1'b1));
  _74153 _74153_2 (
    .pin1(1'b0), .pin2(Control[1]), .pin3(_74574_1_pin16), .pin4(1'b0), .pin5(1'b0), .pin6(MEM[3]),
    .pin7(PipeOut[3]), .pin8(1'b0), .pin9(PipeOut[2]), .pin10(MEM[2]), .pin11(1'b0), .pin12(1'b0),
    .pin13(_74574_1_pin17), .pin14(Control[0]), .pin15(1'b0), .pin16(1'b1));
  _74153 _74153_3 (
    .pin1(1'b0), .pin2(Control[1]), .pin3(_74574_1_pin14), .pin4(1'b0), .pin5(1'b0), .pin6(MEM[5]),
    .pin7(PipeOut[5]), .pin8(1'b0), .pin9(PipeOut[4]), .pin10(MEM[4]), .pin11(1'b0), .pin12(1'b0),
    .pin13(_74574_1_pin15), .pin14(Control[0]), .pin15(1'b0), .pin16(1'b1));
  _74153 _74153_4 (
    .pin1(1'b0), .pin2(Control[1]), .pin3(_74574_1_pin12), .pin4(1'b0), .pin5(1'b0), .pin6(MEM[7]),
    .pin7(PipeOut[7]), .pin8(1'b0), .pin9(PipeOut[6]), .pin10(MEM[6]), .pin11(1'b0), .pin12(1'b0),
    .pin13(_74574_1_pin13), .pin14(Control[0]), .pin15(1'b0), .pin16(1'b1));
  _7404 _7404_1 (
    .pin1(Flags[5]), .pin2(_7404_1_pin2), .pin3(_7404_1_pin2), .pin4(PCRA[0]), .pin5(1'b0), .pin7(1'b0),
    .pin8(1'b0), .pin9(PipeOut[7]), .pin10(MEM[7]), .pin11(1'b0), .pin12(1'b0), .pin13(_74574_1_pin12),
    .pin14(Control[1]));  // open: pin6

  // Other names for the same wires on the sheet: ControlOut[1:0] = PCRA; ControlIn[1:0] = Control; PipeIn[7:0] = MEM

  // Notes on the sheet:
  //   Control: 0: FetchSurpress
  //   1: BusRequest
  //   Flags: 0: Overflow
  //   1: Sign
  //   2: Zero
  //   3: CarryA
  //   4: CarryL
  //   5: PCRA Flip
  //   6: Reset
  //   PCRA: 0,1: Inc PCRAI0,1
endmodule
