// Digital circuit Stage 2.dig as structural Verilog
module Stage_2 (
  input  [6:0] Flags,
  input  Clock,
  input  [7:0] PipeIn,
  output Bus_Request,
  output PCRA_Flip,
  output Break,
  output [7:0] Main,
  output [1:0] SPSIDI,
  output [2:0] Addr
);

  wire [7:0] _74574_1_pin19, _74574_2_pin2, _74574_3_pin2;

  _74574 _74574_1 (
    .pin1(1'b0), .pin2(PipeIn[0]), .pin3(PipeIn[1]), .pin4(PipeIn[2]), .pin5(PipeIn[3]), .pin6(PipeIn[4]),
    .pin7(PipeIn[5]), .pin8(PipeIn[6]), .pin9(PipeIn[7]), .pin10(1'b0), .pin11(Clock),
    .pin12(_74574_1_pin19[7]), .pin13(_74574_1_pin19[6]), .pin14(_74574_1_pin19[5]),
    .pin15(_74574_1_pin19[4]), .pin16(_74574_1_pin19[3]), .pin17(_74574_1_pin19[2]),
    .pin18(_74574_1_pin19[1]), .pin19(_74574_1_pin19[0]), .pin20(1'b1));
  _28c256_programmable A (
    .nCE(1'b0), .nOE(1'b0), .nWE(1'b1), .VCC(1'b1), .GND(1'b0), .I_O0(_74574_2_pin2[0]),
    .I_O1(_74574_2_pin2[1]), .I_O2(_74574_2_pin2[2]), .I_O3(_74574_2_pin2[3]), .I_O4(_74574_2_pin2[4]),
    .I_O5(_74574_2_pin2[5]), .I_O6(_74574_2_pin2[6]), .I_O7(_74574_2_pin2[7]), .A0(_74574_1_pin19[0]),
    .A1(_74574_1_pin19[1]), .A2(_74574_1_pin19[2]), .A3(_74574_1_pin19[3]), .A4(_74574_1_pin19[4]),
    .A5(_74574_1_pin19[5]), .A6(_74574_1_pin19[6]), .A7(_74574_1_pin19[7]), .A8(Flags[0]), .A9(Flags[1]),
    .A10(Flags[2]), .A11(Flags[3]), .A12(Flags[4]), .A13(Flags[5]), .A14(Flags[6]));
  _74574 _74574_2 (
    .pin1(1'b0), .pin2(_74574_2_pin2[0]), .pin3(_74574_2_pin2[1]), .pin4(_74574_2_pin2[2]),
    .pin5(_74574_2_pin2[3]), .pin6(_74574_2_pin2[4]), .pin7(_74574_2_pin2[5]), .pin8(_74574_2_pin2[6]),
    .pin9(_74574_2_pin2[7]), .pin10(1'b0), .pin11(Clock), .pin12(Main[7]), .pin13(Main[6]), .pin14(Main[5]),
    .pin15(Main[4]), .pin16(Main[3]), .pin17(Main[2]), .pin18(Main[1]), .pin19(Main[0]), .pin20(1'b1));
  _28c256_programmable B (
    .nCE(1'b0), .nOE(1'b0), .nWE(1'b1), .VCC(1'b1), .GND(1'b0), .I_O0(_74574_3_pin2[0]),
    .I_O1(_74574_3_pin2[1]), .I_O2(_74574_3_pin2[2]), .I_O3(_74574_3_pin2[3]), .I_O4(_74574_3_pin2[4]),
    .I_O5(_74574_3_pin2[5]), .I_O6(_74574_3_pin2[6]), .I_O7(_74574_3_pin2[7]), .A0(_74574_1_pin19[0]),
    .A1(_74574_1_pin19[1]), .A2(_74574_1_pin19[2]), .A3(_74574_1_pin19[3]), .A4(_74574_1_pin19[4]),
    .A5(_74574_1_pin19[5]), .A6(_74574_1_pin19[6]), .A7(_74574_1_pin19[7]), .A8(Flags[0]), .A9(Flags[1]),
    .A10(Flags[2]), .A11(Flags[3]), .A12(Flags[4]), .A13(Flags[5]), .A14(Flags[6]));
  _74574 _74574_3 (
    .pin1(1'b0), .pin2(_74574_3_pin2[0]), .pin3(_74574_3_pin2[1]), .pin4(_74574_3_pin2[2]),
    .pin5(_74574_3_pin2[3]), .pin6(_74574_3_pin2[4]), .pin7(_74574_3_pin2[5]), .pin8(_74574_3_pin2[6]),
    .pin9(_74574_3_pin2[7]), .pin10(1'b0), .pin11(Clock), .pin12(Break), .pin13(PCRA_Flip),
    .pin14(Bus_Request), .pin15(Addr[2]), .pin16(Addr[1]), .pin17(Addr[0]), .pin18(SPSIDI[1]),
    .pin19(SPSIDI[0]), .pin20(1'b1));

  // Other names for the same wires on the sheet: ControlOut[15:0] = {Break, PCRA_Flip, Bus_Request, Addr, SPSIDI, Main}

  // Notes on the sheet:
  //   Flags: 0: Overflow
  //   1: Sign
  //   2: Zero
  //   3: CarryA
  //   4: CarryL
  //   5: PCRA Flip
  //   6: Reset
  //   Bus_Request: 1: PCRA Flip
  //   2: Break
  //   Main: 0-3: Assert A-D
  //   4-7: Load A-D
  //   SPSIDI: 0,1: Inc SPSIDI0,1
  //   Addr: 000 Memory Ack
  //   001 PCRA0
  //   010 PCRA1
  //   011 SP
  //   100 SI
  //   101 DI
  //   111 TX
  //   contents of B (hex, n*v repeats v):
  //   4,4,4,4,4,4,4,4,4,4,4
endmodule
