// Digital circuit System.dig as structural Verilog
module System (
  input  Clock,
  input  BTN0,
  input  BTN3,
  input  BTN1,
  input  BTN2,
  input  SW0,
  input  SW1,
  input  SW2,
  input  SW3,
  output JA1,
  output JA2,
  output JA3,
  output JA4,
  output JA7,
  output JA8,
  output JA9,
  output JA10
);

  wire and_1_out, core_1_r_nw, decoder_1_out_1;
  wire [1:0] core_1_addr_2;
  wire [7:0] core_1_d_out, multiplexer_1_out, multiplexer_2_out, P_mod_JA_d_out, pincontrol_1_p1,
       pincontrol_1_p2, pincontrol_1_p4, RAM_d, ROM_d;
  wire [13:0] core_1_addr;

  Core core_1 (
    .R_nW(core_1_r_nw), .Addr({core_1_addr_2, core_1_addr}), .D_OUT(core_1_d_out), .D_IN(multiplexer_1_out),
    .Clock(Clock), .nReset(BTN0));
  Decoder #(.Selector_Bits(4)) decoder_1 (
    .sel(core_1_addr[3:0]), .out_1(decoder_1_out_1));  // open: out_0, out_2, out_3, out_4, out_5, out_6, out_7, out_8, out_9, out_10, out_11, out_12, out_13, out_14, out_15
  and and_1 (and_1_out, core_1_addr_2[1], core_1_r_nw);
  BlockRAMDualPort #(.AddrBits(15), .Bits(8)) RAM (
    .A({core_1_addr_2[0], core_1_addr}), .Din(core_1_d_out), .str(and_1_out), .C(Clock), .D(RAM_d));
  ROM #(.AddrBits(14), .Bits(8)) ROM (.A(core_1_addr), .sel(1'b1), .D(ROM_d));
  Multiplexer #(.Selector_Bits(2), .Bits(8)) multiplexer_1 (
    .sel(core_1_addr_2), .in_0(ROM_d), .in_1(multiplexer_2_out), .in_2(RAM_d), .in_3(RAM_d),
    .out(multiplexer_1_out));
  // PinControl #(.Bits(8), .generic("this.Bits=int(args.bitWidth);")) pincontrol_1: pin names not known; wires that end beside it: pincontrol_1_p1, pincontrol_1_p2, {JA10, JA9, JA8, JA7, JA4, JA3, JA2, JA1}, pincontrol_1_p4
  IOBuffer #(.generic("bitWidth := 8;")) P_mod_JA (
    .Out_en(pincontrol_1_p4), .D_w(pincontrol_1_p2), .D_r(pincontrol_1_p1), .D_out(P_mod_JA_d_out),
    .Sel(decoder_1_out_1), .R_nW(core_1_r_nw), .D_IN(core_1_d_out), .Clock(Clock));
  Multiplexer #(.Selector_Bits(4), .Bits(8)) multiplexer_2 (
    .sel(core_1_addr[3:0]), .in_0({8{1'b0}}), .in_1(P_mod_JA_d_out), .in_2({8{1'b0}}), .in_3({8{1'b0}}),
    .in_4({8{1'b0}}), .in_5({8{1'b0}}), .in_6({8{1'b0}}), .in_7({8{1'b0}}), .in_8({8{1'b0}}),
    .in_9({8{1'b0}}), .in_10({8{1'b0}}), .in_11({8{1'b0}}), .in_12({8{1'b0}}), .in_13({8{1'b0}}),
    .in_14({8{1'b0}}), .in_15({8{1'b0}}), .out(multiplexer_2_out));

  // Other names for the same wires on the sheet: Reset = BTN0

  // Notes on the sheet:
  //   Clock: pin E3, Hz: 500
  //   BTN0: pin D9
  //   BTN3: pin B8
  //   BTN1: pin C9
  //   BTN2: pin B9
  //   SW0: pin A8
  //   SW1: pin C11
  //   SW2: pin C10
  //   SW3: pin A10
  //   JA1: pin G13
  //   JA2: pin B11
  //   JA3: pin A11
  //   JA4: pin D12
  //   JA7: pin D13
  //   JA8: pin B18
  //   JA9: pin A18
  //   JA10: pin K18
  //   Switches
  //   Buttons
  //   contents of ROM (hex, n*v repeats v):
  //   0,5,3e,6,0,27,5,14,6,0,5c,0,0,0,5,0,6,0,5f,60,2a,72,76,77,0,5,22,6,0,29,5,38,6,0,
  //   5b,0,0,fc,0,0,5,38,6,0,5f,65,5,1,6,40,54,5f,71,0,0,0,7d,7c,78,29,5e,0,48,65,6c,6c,
  //   6f,20,57,6f,72,6c,64,21,a
endmodule
