// Digital circuit Terminal.dig as structural Verilog
module Terminal (
  input  [7:0] Data,
  input  Clock,
  input  Load,
  input  Sel
);

  wire and_1_out, not_1_out;

  and and_1 (and_1_out, Load, Sel);
  not not_1 (not_1_out, Clock);
  Terminal terminal_1 (.D(Data), .C(not_1_out), .en(and_1_out));
endmodule
