// Digital circuit Tranfer Register.dig as structural Verilog
module Tranfer_Register (
  input  RegTL_L,
  input  RegTL_A,
  input  RegTH_L,
  input  RegTH_A,
  input  RegTX_L,
  input  RegTX_A_Addr,
  input  RegTX_A_Xfer,
  input  RegTX_A_Mode,
  output [7:0] MAIN,
  output [15:0] ADDR,
  output [15:0] XFER
);

  wire Load_H, Load_L, Select_H, Select_L;
  wire [7:0] Data_H, Data_L, Reg_H, Reg_L;

  _74541 _74541_1 (
    .pin1(RegTL_A), .pin2(Reg_L[0]), .pin3(Reg_L[1]), .pin4(Reg_L[2]), .pin5(Reg_L[3]), .pin6(Reg_L[4]),
    .pin7(Reg_L[5]), .pin8(Reg_L[6]), .pin9(Reg_L[7]), .pin10(1'b0), .pin11(MAIN[7]), .pin12(MAIN[6]),
    .pin13(MAIN[5]), .pin14(MAIN[4]), .pin15(MAIN[3]), .pin16(MAIN[2]), .pin17(MAIN[1]), .pin18(MAIN[0]),
    .pin19(1'b0), .pin20(1'b1));
  _74541 _74541_2 (
    .pin1(RegTH_A), .pin2(Reg_H[0]), .pin3(Reg_H[1]), .pin4(Reg_H[2]), .pin5(Reg_H[3]), .pin6(Reg_H[4]),
    .pin7(Reg_H[5]), .pin8(Reg_H[6]), .pin9(Reg_H[7]), .pin10(1'b0), .pin11(MAIN[7]), .pin12(MAIN[6]),
    .pin13(MAIN[5]), .pin14(MAIN[4]), .pin15(MAIN[3]), .pin16(MAIN[2]), .pin17(MAIN[1]), .pin18(MAIN[0]),
    .pin19(1'b0), .pin20(1'b1));
  _74157 _74157_1 (
    .pin1(Select_L), .pin2(MAIN[0]), .pin3(XFER[8]), .pin4(Data_L[4]), .pin5(MAIN[1]), .pin6(XFER[9]),
    .pin7(Data_L[5]), .pin8(1'b0), .pin9(Data_L[6]), .pin10(XFER[10]), .pin11(MAIN[2]), .pin12(Data_L[7]),
    .pin13(XFER[11]), .pin14(MAIN[3]), .pin15(1'b0), .pin16(1'b1));
  _74541 _74541_3 (
    .pin1(RegTX_A_Xfer), .pin2(Reg_L[0]), .pin3(Reg_L[1]), .pin4(Reg_L[2]), .pin5(Reg_L[3]), .pin6(Reg_L[4]),
    .pin7(Reg_L[5]), .pin8(Reg_L[6]), .pin9(Reg_L[7]), .pin10(1'b0), .pin11(XFER[15]), .pin12(XFER[14]),
    .pin13(XFER[13]), .pin14(XFER[12]), .pin15(XFER[11]), .pin16(XFER[10]), .pin17(XFER[9]), .pin18(XFER[8]),
    .pin19(1'b0), .pin20(1'b1));
  _74541 _74541_4 (
    .pin1(RegTX_A_Xfer), .pin2(Reg_H[0]), .pin3(Reg_H[1]), .pin4(Reg_H[2]), .pin5(Reg_H[3]), .pin6(Reg_H[4]),
    .pin7(Reg_H[5]), .pin8(Reg_H[6]), .pin9(Reg_H[7]), .pin10(1'b0), .pin11(XFER[7]), .pin12(XFER[6]),
    .pin13(XFER[5]), .pin14(XFER[4]), .pin15(XFER[3]), .pin16(XFER[2]), .pin17(XFER[1]), .pin18(XFER[0]),
    .pin19(1'b0), .pin20(1'b1));
  _74157 _74157_2 (
    .pin1(Select_L), .pin2(MAIN[4]), .pin3(XFER[12]), .pin4(Data_L[0]), .pin5(MAIN[5]), .pin6(XFER[13]),
    .pin7(Data_L[1]), .pin8(1'b0), .pin9(Data_L[2]), .pin10(XFER[14]), .pin11(MAIN[6]), .pin12(Data_L[3]),
    .pin13(XFER[15]), .pin14(MAIN[7]), .pin15(1'b0), .pin16(1'b1));
  _74157 _74157_3 (
    .pin1(Select_H), .pin2(MAIN[0]), .pin3(XFER[0]), .pin4(Data_H[4]), .pin5(MAIN[1]), .pin6(XFER[1]),
    .pin7(Data_H[5]), .pin8(1'b0), .pin9(Data_H[6]), .pin10(XFER[2]), .pin11(MAIN[2]), .pin12(Data_H[7]),
    .pin13(XFER[3]), .pin14(MAIN[3]), .pin15(1'b0), .pin16(1'b1));
  _74541 _74541_5 (
    .pin1(RegTX_A_Addr), .pin2(Reg_L[0]), .pin3(Reg_L[1]), .pin4(Reg_L[2]), .pin5(Reg_L[3]), .pin6(Reg_L[4]),
    .pin7(Reg_L[5]), .pin8(Reg_L[6]), .pin9(Reg_L[7]), .pin10(1'b0), .pin11(ADDR[15]), .pin12(ADDR[14]),
    .pin13(ADDR[13]), .pin14(ADDR[12]), .pin15(ADDR[11]), .pin16(ADDR[10]), .pin17(ADDR[9]), .pin18(ADDR[8]),
    .pin19(1'b0), .pin20(1'b1));
  _74541 _74541_6 (
    .pin1(RegTX_A_Addr), .pin2(Reg_H[0]), .pin3(Reg_H[1]), .pin4(Reg_H[2]), .pin5(Reg_H[3]), .pin6(Reg_H[4]),
    .pin7(Reg_H[5]), .pin8(Reg_H[6]), .pin9(Reg_H[7]), .pin10(1'b0), .pin11(ADDR[7]), .pin12(ADDR[6]),
    .pin13(ADDR[5]), .pin14(ADDR[4]), .pin15(ADDR[3]), .pin16(ADDR[2]), .pin17(ADDR[1]), .pin18(ADDR[0]),
    .pin19(1'b0), .pin20(1'b1));
  _7408 _7408_1 (
    .pin1(RegTL_L), .pin2(RegTX_L), .pin3(Load_L), .pin4(RegTH_L), .pin5(RegTX_L), .pin6(Load_H),
    .pin7(1'b0), .pin8(Select_H), .pin9(RegTH_L), .pin10(RegTH_L), .pin11(Select_L), .pin12(RegTL_L),
    .pin13(RegTL_L), .pin14(1'b1));
  _74157 _74157_4 (
    .pin1(Select_H), .pin2(MAIN[4]), .pin3(XFER[4]), .pin4(Data_H[0]), .pin5(MAIN[5]), .pin6(XFER[5]),
    .pin7(Data_H[1]), .pin8(1'b0), .pin9(Data_H[2]), .pin10(XFER[6]), .pin11(MAIN[6]), .pin12(Data_H[3]),
    .pin13(XFER[7]), .pin14(MAIN[7]), .pin15(1'b0), .pin16(1'b1));
  _74574 _74574_1 (
    .pin1(1'b0), .pin2(Data_L[0]), .pin3(Data_L[1]), .pin4(Data_L[2]), .pin5(Data_L[3]), .pin6(Data_L[4]),
    .pin7(Data_L[5]), .pin8(Data_L[6]), .pin9(Data_L[7]), .pin10(1'b0), .pin11(Load_L), .pin12(Reg_L[7]),
    .pin13(Reg_L[6]), .pin14(Reg_L[5]), .pin15(Reg_L[4]), .pin16(Reg_L[3]), .pin17(Reg_L[2]),
    .pin18(Reg_L[1]), .pin19(Reg_L[0]), .pin20(1'b1));
  _74574 _74574_2 (
    .pin1(1'b0), .pin2(Data_H[0]), .pin3(Data_H[1]), .pin4(Data_H[2]), .pin5(Data_H[3]), .pin6(Data_H[4]),
    .pin7(Data_H[5]), .pin8(Data_H[6]), .pin9(Data_H[7]), .pin10(1'b0), .pin11(Load_H), .pin12(Reg_H[7]),
    .pin13(Reg_H[6]), .pin14(Reg_H[5]), .pin15(Reg_H[4]), .pin16(Reg_H[3]), .pin17(Reg_H[2]),
    .pin18(Reg_H[1]), .pin19(Reg_H[0]), .pin20(1'b1));

  // Other names for the same wires on the sheet: MainBus[7:0] = MAIN; Xfer_L[7:0] = XFER[15:8];
  //   Xfer_H[7:0] = XFER[7:0]; Addr_L[7:0] = ADDR[15:8]; Addr_H[7:0] = ADDR[7:0]

  // Notes on the sheet:
  //   ADDR: Addr Bus
  //   XFER: Xfer Bus
  //   RegTL_L: default 1
  //   RegTL_A: default 1
  //   RegTH_L: default 1
  //   RegTH_A: default 1
  //   RegTX_L: default 1
  //   RegTX_A_Addr: default 1
  //   RegTX_A_Xfer: default 1
  //   RegTX_A_Mode: default 1
endmodule
