// Digital circuit Transfer Register.dig as structural Verilog
module Transfer_Register (
  input  [7:0] C,
  output [7:0] MAIN,
  output [15:0] ADDR,
  output [15:0] XFER,
  output [15:0] I
);

  wire Load_H, Load_L, Select_H, Select_L;
  wire [7:0] Data_H, Data_L;

  _74541 _74541_1 (
    .pin1(C[5]), .pin2(I[0]), .pin3(I[1]), .pin4(I[2]), .pin5(I[3]), .pin6(I[4]), .pin7(I[5]), .pin8(I[6]),
    .pin9(I[7]), .pin10(1'b0), .pin11(MAIN[7]), .pin12(MAIN[6]), .pin13(MAIN[5]), .pin14(MAIN[4]),
    .pin15(MAIN[3]), .pin16(MAIN[2]), .pin17(MAIN[1]), .pin18(MAIN[0]), .pin19(1'b0), .pin20(1'b1));
  _74541 _74541_2 (
    .pin1(C[7]), .pin2(I[8]), .pin3(I[9]), .pin4(I[10]), .pin5(I[11]), .pin6(I[12]), .pin7(I[13]),
    .pin8(I[14]), .pin9(I[15]), .pin10(1'b0), .pin11(MAIN[7]), .pin12(MAIN[6]), .pin13(MAIN[5]),
    .pin14(MAIN[4]), .pin15(MAIN[3]), .pin16(MAIN[2]), .pin17(MAIN[1]), .pin18(MAIN[0]), .pin19(1'b0),
    .pin20(1'b1));
  _74157 _74157_1 (
    .pin1(Select_L), .pin2(MAIN[0]), .pin3(XFER[8]), .pin4(Data_L[4]), .pin5(MAIN[1]), .pin6(XFER[9]),
    .pin7(Data_L[5]), .pin8(1'b0), .pin9(Data_L[6]), .pin10(XFER[10]), .pin11(MAIN[2]), .pin12(Data_L[7]),
    .pin13(XFER[11]), .pin14(MAIN[3]), .pin15(1'b0), .pin16(1'b1));
  _74541 _74541_3 (
    .pin1(C[2]), .pin2(I[0]), .pin3(I[1]), .pin4(I[2]), .pin5(I[3]), .pin6(I[4]), .pin7(I[5]), .pin8(I[6]),
    .pin9(I[7]), .pin10(1'b0), .pin11(XFER[15]), .pin12(XFER[14]), .pin13(XFER[13]), .pin14(XFER[12]),
    .pin15(XFER[11]), .pin16(XFER[10]), .pin17(XFER[9]), .pin18(XFER[8]), .pin19(1'b0), .pin20(1'b1));
  _74541 _74541_4 (
    .pin1(C[2]), .pin2(I[8]), .pin3(I[9]), .pin4(I[10]), .pin5(I[11]), .pin6(I[12]), .pin7(I[13]),
    .pin8(I[14]), .pin9(I[15]), .pin10(1'b0), .pin11(XFER[7]), .pin12(XFER[6]), .pin13(XFER[5]),
    .pin14(XFER[4]), .pin15(XFER[3]), .pin16(XFER[2]), .pin17(XFER[1]), .pin18(XFER[0]), .pin19(1'b0),
    .pin20(1'b1));
  _74157 _74157_2 (
    .pin1(Select_L), .pin2(MAIN[4]), .pin3(XFER[12]), .pin4(Data_L[0]), .pin5(MAIN[5]), .pin6(XFER[13]),
    .pin7(Data_L[1]), .pin8(1'b0), .pin9(Data_L[2]), .pin10(XFER[14]), .pin11(MAIN[6]), .pin12(Data_L[3]),
    .pin13(XFER[15]), .pin14(MAIN[7]), .pin15(1'b0), .pin16(1'b1));
  _74157 _74157_3 (
    .pin1(Select_H), .pin2(MAIN[0]), .pin3(XFER[0]), .pin4(Data_H[4]), .pin5(MAIN[1]), .pin6(XFER[1]),
    .pin7(Data_H[5]), .pin8(1'b0), .pin9(Data_H[6]), .pin10(XFER[2]), .pin11(MAIN[2]), .pin12(Data_H[7]),
    .pin13(XFER[3]), .pin14(MAIN[3]), .pin15(1'b0), .pin16(1'b1));
  _74541 _74541_5 (
    .pin1(C[1]), .pin2(I[0]), .pin3(I[1]), .pin4(I[2]), .pin5(I[3]), .pin6(I[4]), .pin7(I[5]), .pin8(I[6]),
    .pin9(I[7]), .pin10(1'b0), .pin11(ADDR[15]), .pin12(ADDR[14]), .pin13(ADDR[13]), .pin14(ADDR[12]),
    .pin15(ADDR[11]), .pin16(ADDR[10]), .pin17(ADDR[9]), .pin18(ADDR[8]), .pin19(1'b0), .pin20(1'b1));
  _74541 _74541_6 (
    .pin1(C[1]), .pin2(I[8]), .pin3(I[9]), .pin4(I[10]), .pin5(I[11]), .pin6(I[12]), .pin7(I[13]),
    .pin8(I[14]), .pin9(I[15]), .pin10(1'b0), .pin11(ADDR[7]), .pin12(ADDR[6]), .pin13(ADDR[5]),
    .pin14(ADDR[4]), .pin15(ADDR[3]), .pin16(ADDR[2]), .pin17(ADDR[1]), .pin18(ADDR[0]), .pin19(1'b0),
    .pin20(1'b1));
  _7408 _7408_1 (
    .pin1(C[4]), .pin2(C[0]), .pin3(Load_L), .pin4(C[6]), .pin5(C[0]), .pin6(Load_H), .pin7(1'b0),
    .pin8(Select_H), .pin9(C[6]), .pin10(C[6]), .pin11(Select_L), .pin12(C[4]), .pin13(C[4]), .pin14(1'b1));
  _74157 _74157_4 (
    .pin1(Select_H), .pin2(MAIN[4]), .pin3(XFER[4]), .pin4(Data_H[0]), .pin5(MAIN[5]), .pin6(XFER[5]),
    .pin7(Data_H[1]), .pin8(1'b0), .pin9(Data_H[2]), .pin10(XFER[6]), .pin11(MAIN[6]), .pin12(Data_H[3]),
    .pin13(XFER[7]), .pin14(MAIN[7]), .pin15(1'b0), .pin16(1'b1));
  _74574 _74574_1 (
    .pin1(1'b0), .pin2(Data_L[0]), .pin3(Data_L[1]), .pin4(Data_L[2]), .pin5(Data_L[3]), .pin6(Data_L[4]),
    .pin7(Data_L[5]), .pin8(Data_L[6]), .pin9(Data_L[7]), .pin10(1'b0), .pin11(Load_L), .pin12(I[7]),
    .pin13(I[6]), .pin14(I[5]), .pin15(I[4]), .pin16(I[3]), .pin17(I[2]), .pin18(I[1]), .pin19(I[0]),
    .pin20(1'b1));
  _74574 _74574_2 (
    .pin1(1'b0), .pin2(Data_H[0]), .pin3(Data_H[1]), .pin4(Data_H[2]), .pin5(Data_H[3]), .pin6(Data_H[4]),
    .pin7(Data_H[5]), .pin8(Data_H[6]), .pin9(Data_H[7]), .pin10(1'b0), .pin11(Load_H), .pin12(I[15]),
    .pin13(I[14]), .pin14(I[13]), .pin15(I[12]), .pin16(I[11]), .pin17(I[10]), .pin18(I[9]), .pin19(I[8]),
    .pin20(1'b1));
  // Pins of 8 and 16 bits meet at I

  // Other names for the same wires on the sheet: MainBus[7:0] = MAIN; Xfer_L[7:0] = XFER[15:8];
  //   Xfer_H[7:0] = XFER[7:0]; Addr_L[7:0] = ADDR[15:8]; Addr_H[7:0] = ADDR[7:0]; Reg_L[7:0] = I[7:0];
  //   Reg_H[7:0] = I[15:8]; RegTX_L = C[0]; RegTX_A_Addr = C[1]; RegTX_A_Xfer = C[2]; RegTL_L = C[4]; RegTL_A = C[5];
  //   RegTH_L = C[6]; RegTH_A = C[7]

  // Notes on the sheet:
  //   ADDR: Addr Bus
  //   XFER: Xfer Bus
  //   C: 0: RegTX Load
  //   1: RegTX Assert Addr
  //   2: RegTX Assert Xfer
  //   3: RegTX Assert Mode
  //   4: RegTL Load
  //   5: RegTL Assert
  //   6: RegTH Load
  //   7: RegTH Assert, default 1
endmodule
