// Digital circuit TransferRegister.dig as structural Verilog
module TransferRegister (
  input  L_TL,
  input  L_TH,
  input  L_TX,
  input  [7:0] D_IN,
  input  [15:0] X_IN,
  input  C,
  output [7:0] D_TH,
  output [7:0] D_TL,
  output [15:0] D_TX
);

  wire or_1_out, or_2_out;
  wire [7:0] multiplexer_1_out, multiplexer_2_out;

  or or_1 (or_1_out, L_TL, L_TX);
  or or_2 (or_2_out, L_TX, L_TH);
  Multiplexer #(.Bits(8)) multiplexer_1 (.sel(L_TX), .in_0(D_IN), .in_1(X_IN[7:0]), .out(multiplexer_1_out));
  Multiplexer #(.Bits(8)) multiplexer_2 (.sel(L_TX), .in_0(D_IN), .in_1(X_IN[15:8]), .out(multiplexer_2_out));
  Register #(.Bits(8)) TL (.D(multiplexer_1_out), .C(C), .en(or_1_out), .Q(D_TL));
  Register #(.Bits(8)) TH (.D(multiplexer_2_out), .C(C), .en(or_2_out), .Q(D_TH));

  assign D_TX = {D_TH, D_TL};

  // Other names for the same wires on the sheet: Clock = C; LoadTH = L_TH; LoadTL = L_TL; LoadTX = L_TX;
  //   Main[7:0] = D_IN; Xfer[15:0] = X_IN
endmodule
