// Digital circuit mem-io.dig as structural Verilog
module mem_io (
  input  [7:0] D_IN,
  input  [15:0] Addr,
  input  R_nW,
  input  Clock,
  output [7:0] D_OUT
);

  wire and_1_out;
  wire [7:0] blockramdualport_1_d, multiplexer_2_out, rom_1_d;

  and and_1 (and_1_out, ~Addr[15], Addr[14]);  // And
  BlockRAMDualPort #(.AddrBits(15), .Bits(8)) blockramdualport_1 (
    .A(Addr[14:0]), .Din(D_IN), .str(R_nW), .C(Clock), .D(blockramdualport_1_d));
  ROM #(.AddrBits(14), .Bits(8)) rom_1 (.A(Addr[13:0]), .sel(1'b1), .D(rom_1_d));
  Multiplexer #(.Bits(8)) multiplexer_1 (
    .sel(Addr[15]), .in_0(multiplexer_2_out), .in_1(blockramdualport_1_d), .out(D_OUT));
  Multiplexer #(.Bits(8)) multiplexer_2 (.sel(Addr[14]), .in_0(rom_1_d), .in_1({8{1'b0}}), .out(multiplexer_2_out));
  Terminal terminal_1 (.D(D_IN), .C(Clock), .Load(and_1_out));

  // Notes on the sheet:
  //   contents of rom_1 (hex, n*v repeats v):
  //   0,5,3e,6,0,27,5,14,6,0,5c,0,0,0,5,0,6,0,5f,60,2a,72,76,77,0,5,22,6,0,29,5,38,6,0,
  //   5b,0,0,fc,0,0,5,38,6,0,5f,65,5,0,6,40,54,5f,71,0,0,0,7d,7c,78,29,5e,0,48,65,6c,6c,
  //   6f,20,57,6f,72,6c,64,21,a
endmodule
